// Logisim project teamwork.circ as structural Verilog: 42 circuits, main circuit ◇单周期+单级中断
// 单周期硬布线控制器
module \单周期硬布线控制器  (
  input  [4:0] OP,
  input  [4:0] Funct,
  input  in_3,
  output [3:0] ALU_OP,
  output uret,
  output MemToReg,
  output ecall,
  output MemWrite,
  output ALU_SRC,
  output RegWrite,
  output S_type,
  output Beq,
  output Bne,
  output Jalr,
  output JAL,
  output BLTU,
  output CSR,
  output LH,
  output LUI
);

  wire \控制信号自动生成_1_ecall ;

  \运算控制器自动生成  \u_运算控制器自动生成_1  (
    .OP2(OP[0]), .OP3(OP[1]), .OP4(OP[2]), .OP5(OP[3]), .OP6(OP[4]), .F12(Funct[0]), .F13(Funct[1]),
    .F14(Funct[2]), .F25(Funct[3]), .F30(Funct[4]), .S0(ALU_OP[0]), .S1(ALU_OP[1]), .S2(ALU_OP[2]),
    .S3(ALU_OP[3]));
  \控制信号自动生成  \u_控制信号自动生成_1  (
    .OP2(OP[0]), .OP3(OP[1]), .OP4(OP[2]), .OP5(OP[3]), .MemToReg(MemToReg), .OP6(OP[4]), .F12(Funct[0]),
    .F13(Funct[1]), .F14(Funct[2]), .F25(Funct[3]), .F30(Funct[4]), .MemWrite(MemWrite), .ALU_SRC(ALU_SRC),
    .RegWrite(RegWrite), .ecall(\控制信号自动生成_1_ecall ), .S_Type(S_type), .BEQ(Beq), .BNE(Bne), .JALR(Jalr),
    .JAL(JAL), .BLTU(BLTU), .CSR(CSR), .LH(LH), .LUI(LUI));
  and and_1 (uret, in_3, \控制信号自动生成_1_ecall );
  and and_2 (ecall, ~in_3, \控制信号自动生成_1_ecall );  // AND_Gate

  // Other names for the same wires on the sheet: IR21 = in_3; OP_CODE[4:0] = OP

  // Notes on the sheet:
  //   运算器控制器，根据指令生成运算器功能选择信号
  //   控制信号生成，产生数据通路需要的其他控制信号
endmodule

module \单周期RISC_V  (
  input  IR1,
  input  IR2,
  input  IR3,
  output RegWrite,
  output MemWrite,
  output [31:0] PC,
  output [31:0] IR,
  output [31:0] RDin,
  output [31:0] MDin,
  output [31:0] LedData
);

  wire AluSrcB, Beq, BLTU, Bne, CLK, clock_1_out, comparator_2_eq, comparator_2_lt, CSR, d_ff_1_q, ecall,
       ecall_e, Equal, GE, Go, halt, IR1_t, IR2_t, IR3_t, IRA, IRB, IRC, JAL, JALR, LH, LUI, MemToReg,
       nand_1_out, not_1_out, not_2_out, not_3_out, not_4_out, riscv_probe_1_p1, riscv_probe_1_p3,
       riscv_probe_1_p5, RST, s_type, URET, W1, W2, W3;
  wire [3:0] \单周期硬布线控制器_1_alu_op ;
  wire [4:0] multiplexer_1_out, multiplexer_2_out;
  wire [12:0] CNT_num;
  wire [15:0] \总周期数 ;
  wire [31:0] alu_bin_1_alu_bin, ALU_Res, bit_extender_1_out, CSR_out, DM_Dout, multiplexer_4_out,
       pc_in_1_pc_2, reg_din_1_rdin, regifile_1_r1, shifter_1_out;

  Button \u_继续运行  (.out(Go));
  Button _1 (.out(IRA));
  Button _2 (.out(IRB));
  Button _3 (.out(IRC));
  LED #(.active("true")) led_1 (.in(W1));
  LED #(.active("true")) led_2 (.in(W2));
  LED #(.active("true")) led_3 (.in(W3));
  not not_1 (not_1_out, halt);
  Hex_Digit_Display hex_digit_display_1 (.value(LedData[31:28]));  // open: dp
  Register #(.width(32), .trigger("rising"), .Select("low")) register_1 (
    .D(MDin), .en(ecall_e), .Q(LedData), .clk(CLK), .clr(RST));
  Register #(.width(32), .trigger("rising"), .Select("low")) register_2 (
    .D(ALU_Res), .en(CSR), .Q(CSR_out), .clk(CLK), .clr(RST));
  Counter #(.width(16), .max('hffff), .ongoal("wrap"), .trigger("rising"), .behavior("new")) counter_1 (
    .count(not_1_out), .Q(\总周期数 ), .clk(CLK), .clr(RST));  // open: load, D, carry, preset, down
  Hex_Digit_Display hex_digit_display_2 (.value(LedData[23:20]));  // open: dp
  Hex_Digit_Display hex_digit_display_3 (.value(LedData[27:24]));  // open: dp
  Hex_Digit_Display hex_digit_display_4 (.value(LedData[15:12]));  // open: dp
  Hex_Digit_Display hex_digit_display_5 (.value(LedData[19:16]));  // open: dp
  Hex_Digit_Display hex_digit_display_6 (.value(LedData[7:4]));  // open: dp
  Hex_Digit_Display hex_digit_display_7 (.value(LedData[11:8]));  // open: dp
  // Probe on \总周期数 
  Hex_Digit_Display hex_digit_display_8 (.value(LedData[3:0]));  // open: dp
  PC_in pc_in_1 (
    .PC(PC), .immb({IR[31], IR[7], IR[30:25], IR[11:8]}), .immuj({IR[31], IR[19:12], IR[20], IR[30:21]}),
    .ALU_Res(ALU_Res), .GE(GE), .BLTU(BLTU), .URET(URET), .JALR(JALR), .JAL(JAL), .Beq(Beq), .Bne(Bne),
    .Equal(Equal), .\中断触发 (1'b0), .PC_2(pc_in_1_pc_2));  // open: 中断编号, EPC
  Register #(.width(32), .trigger("rising"), .Select("low")) u_PC (
    .D(pc_in_1_pc_2), .en(not_2_out), .Q(PC), .clk(CLK), .clr(RST));
  not not_2 (not_2_out, halt);
  or or_1 (IR1_t, IR1, IRA);
  or or_2 (IR2_t, IR2, IRB);
  // RiscV_Probe riscv_probe_1: pin names not known; wires that end beside it: riscv_probe_1_p1, riscv_probe_1_p1, riscv_probe_1_p3, riscv_probe_1_p3, riscv_probe_1_p5, riscv_probe_1_p5, IR
  ROM #(.addrWidth(10), .dataWidth(32), .Select("high")) rom_1 (.addr(PC[11:2]), .data(IR));
  or or_3 (IR3_t, IR3, IRC);
  \单周期硬布线控制器  \u_单周期硬布线控制器_1  (
    .Funct({IR[30], IR[25], IR[14:12]}), .OP(IR[6:2]), .ALU_OP(\单周期硬布线控制器_1_alu_op ), .MemToReg(MemToReg),
    .MemWrite(MemWrite), .ALU_SRC(AluSrcB), .RegWrite(RegWrite), .ecall(ecall), .S_type(s_type), .Jalr(JALR),
    .Beq(Beq), .JAL(JAL), .Bne(Bne), .in_3(IR[21]), .uret(URET), .BLTU(BLTU), .CSR(CSR), .LH(LH), .LUI(LUI));
  Multiplexer #(.select(1), .width(5), .disabled("Z"), .enable("false")) multiplexer_1 (
    .in0(IR[19:15]), .in1(5'b10001), .out(multiplexer_1_out), .sel(ecall));
  Multiplexer #(.select(1), .width(5), .disabled("Z"), .enable("false")) multiplexer_2 (
    .in0(IR[24:20]), .in1(5'b01010), .out(multiplexer_2_out), .sel(ecall));
  Multiplexer #(.select(1), .width(32), .disabled("Z"), .enable("false")) multiplexer_3 (
    .in0(reg_din_1_rdin), .in1(shifter_1_out), .out(RDin), .sel(LUI));
  Reg_Din reg_din_1 (
    .DM_Dout(DM_Dout), .PC(PC), .CSR_out(CSR_out), .ALU_Res(ALU_Res), .LH(LH), .MemToReg(MemToReg),
    .CSR(CSR), .JAL(JAL), .JALR(JALR), .RDin(reg_din_1_rdin));
  Regifile regifile_1 (
    .Din(RDin), .Clk(CLK), .R1(regifile_1_r1), .R2(MDin), .WE(RegWrite), .W_num(IR[11:7]),
    .R1_num(multiplexer_1_out), .R2_num(multiplexer_2_out));
  Multiplexer #(.select(1), .width(32), .disabled("Z"), .enable("false")) multiplexer_4 (
    .in0(regifile_1_r1), .in1(CSR_out), .out(multiplexer_4_out), .sel(CSR));
  assign bit_extender_1_out = {{12{IR[31]}}, IR[31:12]};  // Bit_Extender bit_extender_1
  not not_3 (not_3_out, ecall_e);
  Comparator #(.width(32), .mode("twosComplement")) comparator_1 (
    .a(32'h22), .b(regifile_1_r1), .eq(ecall_e));  // open: gt, lt
  ALU_Bin alu_bin_1 (
    .Reg_R2(MDin), .immb(IR[31:20]), .rs1(IR[19:15]), .imms({IR[31:25], IR[11:7]}), .CSR(CSR),
    .S_type(s_type), .AluSrcB(AluSrcB), .ALU_Bin(alu_bin_1_alu_bin));
  Register #(.width(1), .trigger("rising"), .Select("low")) register_3 (
    .D(not_3_out), .en(ecall), .Q(halt), .clk(CLK), .clr(Go));
  ALU alu_1 (
    .X(multiplexer_4_out), .Y(alu_bin_1_alu_bin), .AluOP(\单周期硬布线控制器_1_alu_op ), .Equal(Equal),
    .Result(ALU_Res), .out_4(GE));  // open: Result_2, out_6
  Shifter #(.width(32), .shift("ll")) shifter_1 (.in(bit_extender_1_out), .\dist (5'b01100), .out(shifter_1_out));
  D_Flip_Flop #(.trigger("high"), .Pre_Clr_Positions("LEGACY"), .NegatePresetClear("false"), .enable("true"), .NewFFLayout("false")) d_ff_1 (.Q(d_ff_1_q));  // open: clk, D, Qn, preset, en, reset
  // Probe on 13'h609
  Comparator #(.width(13), .mode("twosComplement")) comparator_2 (
    .a(CNT_num), .b(13'h609), .eq(comparator_2_eq), .lt(comparator_2_lt));  // open: gt
  Clock #(.highDuration(1), .lowDuration(1)) clock_1 (.out(clock_1_out));
  not not_4 (not_4_out, MemWrite);
  Counter #(.width(13), .max('h1fff), .ongoal("stay"), .trigger("rising"), .behavior("old")) counter_2 (
    .count(comparator_2_lt), .Q(CNT_num), .clk(clock_1_out));  // open: load, D, carry, clr, preset
  RAM #(.addrWidth(10), .dataWidth(32), .bus("separate"), .Select("high")) ram_1 (
    .addr(ALU_Res[11:2]), .din(MDin), .data(DM_Dout), .str(MemWrite), .clk(CLK), .ld(not_4_out), .clr(RST));  // open: sel
  nand nand_1 (nand_1_out, d_ff_1_q, comparator_2_eq);
  assign CLK = nand_1_out ? clock_1_out : 1'bz;  // Controlled_Buffer controlled_buffer_1
  Pull_Resistor #(.pull(1)) pull_resistor_1 (.node(CLK));

  // Other names for the same wires on the sheet: immb[11:0] = {IR[31], IR[7], IR[30:25], IR[11:8]};
  //   imms[11:0] = {IR[31:25], IR[11:7]}; rd[4:0] = IR[11:7]; imm12[11:0] = IR[31:20]; imm20[19:0] = IR[31:12];
  //   immuj[19:0] = {IR[31], IR[19:12], IR[20], IR[30:21]}; rs2[4:0] = IR[24:20]; rs1[4:0] = IR[19:15];
  //   Reg_R2[31:0] = MDin

  // Notes on the sheet:
  //   中断源
  //   中断等待指示
  //   数码管输出应该用寄存器锁存，否则显示数据只能一闪而过
  //   数码管输出
  //   指令探针
  //   指令存储器
  //   contents of rom_1 (hex, n*v repeats v):
  //   100493 100006f 100493 200913 300993 100006f 100493 200913 300993 100006f 100493 200913 300993
  //   100006f 100493 200913 300993 29c000ef 100413 100493 1f49493 900533 2200893 73 24d493 48463 fedff06f
  //   900533 2200893 73 100493 249493 900533 2200893 73 48463 fedff06f 100493 1f49493 900533 2200893 73
  //   4034d493 900533 2200893 73 4044d493 900533 2200893 73 4044d493 900533 2200893 73 4044d493 900533
  //   2200893 73 4044d493 900533 2200893 73 4044d493 900533 2200893 73 4044d493 900533 2200893 73 4044d493
  //   900533 2200893 73 100413 1f41993 41f9d993 433 c00913 300b13 140413 f47413 800293 100313 499993
  //   89e9b3 1300533 2200893 73 406282b3 fe0294e3 140413 f00f93 1f47433 1c41413 800293 100313 49d993
  //   89e9b3 1300533 2200893 73 406282b3 fe0294e3 1c45413 406b0b33 b0463 f95ff06f 2b3 fff2c293 829293
  //   ff2e293 500533 2200893 73 fff00413 493 84a023 140413 448493 84a023 140413 448493 84a023 140413
  //   448493 84a023 140413 448493 84a023 140413 448493 84a023 140413 448493 84a023 140413 448493 84a023
  //   140413 448493 84a023 140413 448493 84a023 140413 448493 84a023 140413 448493 84a023 140413 448493
  //   84a023 140413 448493 84a023 140413 448493 84a023 140413 448493 84a023 140413 448493 140413 433
  //   3c00493 42983 4aa03 149a2b3 28663 134a023 1442023 ffc48493 fe9412e3 800533 2200893 73 440413 3c00493
  //   fc9416e3 a00893 73 413 140413 800533 2200893 73 240413 800533 2200893 73 340413 800533 2200893 73
  //   440413 800533 2200893 73 540413 800533 2200893 73 640413 800533 2200893 73 740413 800533 2200893 73
  //   840413 800533 2200893 2200893 73 8067
  //   指令字
  //   JAL
  //   JALR
  //   URET
  //   Beq
  //   Bne
  //   MemToReg
  //   MemWrite
  //   AluOP
  //   AluSrcB
  //   RegWrite
  //   为方便自动评测，需要输出PC，IR，寄存器堆写如数据RDin
  //   RAM写使能MemWrite、RAM写入数据MDin等信号
  //   控制位
  //   暂停节拍，不能为0
  //   戳工具置1进入计数暂停模式，ctrl+k时钟自动运行到对应节拍暂停
  //   ctrl+k关闭时钟连续运行，将控制位置零，进入单步调试模式调试
  //   用这个时钟源需要去掉电路中的其他时钟源
  //   数据存储器
  //   可计数暂停的时钟源
endmodule

// 运算器控制器
module \运算控制器自动生成  (
  input  OP2,
  input  OP3,
  input  OP4,
  input  OP5,
  input  OP6,
  input  F12,
  input  F13,
  input  F14,
  input  F25,
  input  F30,
  output S0,
  output S1,
  output S2,
  output S3
);

  wire and_1_out, and_2_out, and_3_out, and_4_out, and_5_out, and_6_out, and_7_out, and_8_out, and_9_out,
       and_10_out, and_11_out, and_12_out, and_13_out, and_14_out, and_15_out, and_16_out, and_17_out,
       and_18_out, and_19_out, and_20_out, and_21_out, and_22_out, and_23_out, and_24_out, and_25_out,
       and_26_out, and_27_out, and_28_out, and_29_out, and_30_out, and_31_out, and_32_out, and_33_out,
       and_34_out, and_35_out, and_36_out, and_37_out, and_38_out, and_39_out, and_40_out, and_41_out,
       and_42_out, and_43_out, and_44_out, and_45_out, and_46_out, and_47_out, and_48_out, and_49_out,
       and_50_out, not_1_out, not_2_out, not_3_out, not_4_out, not_5_out, not_6_out, not_7_out, not_8_out,
       not_9_out, not_10_out, not_11_out, not_12_out, not_13_out, not_14_out, not_15_out, not_16_out,
       not_17_out, not_18_out, not_19_out, not_20_out, not_21_out, not_22_out, not_23_out, not_24_out,
       not_25_out, not_26_out, not_27_out, not_28_out, not_29_out, not_30_out, not_31_out, not_32_out,
       not_33_out, not_34_out, not_35_out, not_36_out, not_37_out, not_38_out, not_39_out, not_40_out,
       not_41_out, not_42_out, not_43_out, not_44_out, not_45_out, not_46_out, not_47_out, not_48_out,
       not_49_out, not_50_out, not_51_out, not_52_out, not_53_out, not_54_out, not_55_out, not_56_out,
       not_57_out, not_58_out, not_59_out, not_60_out, not_61_out, not_62_out, not_63_out, not_64_out,
       not_65_out, not_66_out, not_67_out, not_68_out, not_69_out, not_70_out, not_71_out, not_72_out,
       not_73_out, not_74_out, not_75_out, not_76_out, not_77_out, not_78_out, not_79_out, not_80_out,
       not_81_out, not_82_out, not_83_out, not_84_out, not_85_out, not_86_out, not_87_out, not_88_out,
       not_89_out, not_90_out, not_91_out, not_92_out, not_93_out, not_94_out, not_95_out, not_96_out,
       not_97_out, not_98_out, not_99_out, not_100_out, not_101_out, not_102_out, not_103_out, not_104_out,
       not_105_out, not_106_out, not_107_out, not_108_out, not_109_out, not_110_out, not_111_out,
       not_112_out, not_113_out, not_114_out, not_115_out, not_116_out, not_117_out, not_118_out,
       not_119_out, not_120_out, not_121_out, not_122_out, not_123_out, not_124_out, not_125_out,
       not_126_out, not_127_out, not_128_out, not_129_out, not_130_out, not_131_out, not_132_out,
       not_133_out, not_134_out, not_135_out, not_136_out, not_137_out, not_138_out, not_139_out,
       not_140_out, not_141_out, not_142_out, not_143_out, not_144_out, not_145_out, not_146_out,
       not_147_out, not_148_out, not_149_out, not_150_out, not_151_out, not_152_out, not_153_out,
       not_154_out, not_155_out, not_156_out, not_157_out, not_158_out, not_159_out, not_160_out,
       not_161_out, not_162_out, not_163_out, not_164_out, not_165_out, not_166_out, not_167_out,
       not_168_out, not_169_out, not_170_out, not_171_out, not_172_out, not_173_out, not_174_out,
       not_175_out, not_176_out, not_177_out, not_178_out, not_179_out, not_180_out, not_181_out,
       not_182_out, not_183_out, not_184_out, not_185_out, not_186_out, not_187_out, not_188_out,
       not_189_out, not_190_out, not_191_out, not_192_out, not_193_out, not_194_out, not_195_out,
       not_196_out, not_197_out, not_198_out, not_199_out, not_200_out, not_201_out, not_202_out,
       not_203_out, not_204_out, not_205_out, not_206_out, not_207_out, not_208_out, not_209_out,
       not_210_out, not_211_out, not_212_out, not_213_out, not_214_out, not_215_out, not_216_out,
       not_217_out, not_218_out, not_219_out, not_220_out, not_221_out, not_222_out, not_223_out,
       not_224_out, not_225_out, not_226_out, not_227_out, not_228_out, not_229_out, not_230_out,
       not_231_out, not_232_out, not_233_out, not_234_out, not_235_out, not_236_out, not_237_out,
       not_238_out, not_239_out, not_240_out, not_241_out, not_242_out, not_243_out, not_244_out,
       not_245_out, not_246_out, not_247_out, not_248_out, not_249_out, not_250_out, not_251_out,
       not_252_out, not_253_out, not_254_out, not_255_out, not_256_out, not_257_out, not_258_out,
       not_259_out, not_260_out, not_261_out, not_262_out, not_263_out, not_264_out, not_265_out,
       not_266_out, not_267_out, not_268_out, not_269_out, not_270_out, not_271_out, not_272_out,
       not_273_out, not_274_out;

  not not_1 (not_1_out, F30);
  not not_2 (not_2_out, F25);
  not not_3 (not_3_out, F14);
  not not_4 (not_4_out, F13);
  not not_5 (not_5_out, F12);
  not not_6 (not_6_out, OP6);
  not not_7 (not_7_out, OP3);
  not not_8 (not_8_out, OP2);
  not not_9 (not_9_out, F30);
  not not_10 (not_10_out, F25);
  not not_11 (not_11_out, OP6);
  not not_12 (not_12_out, OP3);
  not not_13 (not_13_out, OP2);
  not not_14 (not_14_out, F30);
  not not_15 (not_15_out, F25);
  not not_16 (not_16_out, F14);
  not not_17 (not_17_out, F12);
  not not_18 (not_18_out, OP6);
  not not_19 (not_19_out, OP3);
  not not_20 (not_20_out, OP2);
  not not_21 (not_21_out, F14);
  not not_22 (not_22_out, F13);
  not not_23 (not_23_out, F12);
  not not_24 (not_24_out, OP6);
  not not_25 (not_25_out, OP5);
  not not_26 (not_26_out, OP3);
  not not_27 (not_27_out, OP2);
  not not_28 (not_28_out, OP6);
  not not_29 (not_29_out, OP5);
  not not_30 (not_30_out, OP3);
  not not_31 (not_31_out, OP2);
  not not_32 (not_32_out, F13);
  not not_33 (not_33_out, F12);
  not not_34 (not_34_out, OP6);
  not not_35 (not_35_out, OP5);
  not not_36 (not_36_out, OP3);
  not not_37 (not_37_out, OP2);
  not not_38 (not_38_out, F25);
  not not_39 (not_39_out, F13);
  not not_40 (not_40_out, OP6);
  not not_41 (not_41_out, OP5);
  not not_42 (not_42_out, OP3);
  not not_43 (not_43_out, OP2);
  not not_44 (not_44_out, F14);
  not not_45 (not_45_out, F12);
  not not_46 (not_46_out, OP6);
  not not_47 (not_47_out, OP5);
  not not_48 (not_48_out, OP4);
  not not_49 (not_49_out, OP3);
  not not_50 (not_50_out, OP2);
  not not_51 (not_51_out, F14);
  not not_52 (not_52_out, F12);
  not not_53 (not_53_out, OP6);
  not not_54 (not_54_out, OP4);
  not not_55 (not_55_out, OP3);
  not not_56 (not_56_out, OP2);
  not not_57 (not_57_out, F14);
  not not_58 (not_58_out, F13);
  not not_59 (not_59_out, F12);
  not not_60 (not_60_out, OP4);
  not not_61 (not_61_out, OP3);
  not not_62 (not_62_out, OP2);
  not not_63 (not_63_out, F14);
  not not_64 (not_64_out, F13);
  not not_65 (not_65_out, OP4);
  not not_66 (not_66_out, OP3);
  not not_67 (not_67_out, OP2);
  not not_68 (not_68_out, OP4);
  not not_69 (not_69_out, F14);
  not not_70 (not_70_out, F13);
  not not_71 (not_71_out, F12);
  not not_72 (not_72_out, OP4);
  not not_73 (not_73_out, OP3);
  not not_74 (not_74_out, OP3);
  not not_75 (not_75_out, OP2);
  not not_76 (not_76_out, F30);
  not not_77 (not_77_out, F25);
  not not_78 (not_78_out, F13);
  not not_79 (not_79_out, F12);
  not not_80 (not_80_out, OP6);
  not not_81 (not_81_out, OP3);
  not not_82 (not_82_out, OP2);
  not not_83 (not_83_out, F14);
  not not_84 (not_84_out, F13);
  not not_85 (not_85_out, OP6);
  not not_86 (not_86_out, OP5);
  not not_87 (not_87_out, OP4);
  not not_88 (not_88_out, OP3);
  not not_89 (not_89_out, OP2);
  not not_90 (not_90_out, F25);
  not not_91 (not_91_out, F14);
  not not_92 (not_92_out, F13);
  not not_93 (not_93_out, F12);
  not not_94 (not_94_out, OP6);
  not not_95 (not_95_out, OP3);
  not not_96 (not_96_out, OP2);
  not not_97 (not_97_out, F30);
  not not_98 (not_98_out, F25);
  not not_99 (not_99_out, OP6);
  not not_100 (not_100_out, OP3);
  not not_101 (not_101_out, OP2);
  not not_102 (not_102_out, F30);
  not not_103 (not_103_out, F25);
  not not_104 (not_104_out, F14);
  not not_105 (not_105_out, F12);
  not not_106 (not_106_out, OP6);
  not not_107 (not_107_out, OP3);
  not not_108 (not_108_out, OP2);
  not not_109 (not_109_out, OP6);
  not not_110 (not_110_out, OP5);
  not not_111 (not_111_out, OP3);
  not not_112 (not_112_out, OP2);
  not not_113 (not_113_out, F30);
  not not_114 (not_114_out, F25);
  not not_115 (not_115_out, F13);
  not not_116 (not_116_out, OP6);
  not not_117 (not_117_out, OP5);
  not not_118 (not_118_out, OP3);
  not not_119 (not_119_out, OP2);
  not not_120 (not_120_out, F14);
  not not_121 (not_121_out, F13);
  not not_122 (not_122_out, F12);
  not not_123 (not_123_out, OP4);
  not not_124 (not_124_out, OP3);
  not not_125 (not_125_out, OP2);
  not not_126 (not_126_out, F14);
  not not_127 (not_127_out, F13);
  not not_128 (not_128_out, OP4);
  not not_129 (not_129_out, OP3);
  not not_130 (not_130_out, OP2);
  not not_131 (not_131_out, OP3);
  not not_132 (not_132_out, OP2);
  not not_133 (not_133_out, F30);
  not not_134 (not_134_out, F25);
  not not_135 (not_135_out, F13);
  not not_136 (not_136_out, OP6);
  not not_137 (not_137_out, OP3);
  not not_138 (not_138_out, OP2);
  not not_139 (not_139_out, F30);
  not not_140 (not_140_out, F25);
  not not_141 (not_141_out, F14);
  not not_142 (not_142_out, F13);
  not not_143 (not_143_out, F12);
  not not_144 (not_144_out, OP6);
  not not_145 (not_145_out, OP3);
  not not_146 (not_146_out, OP2);
  not not_147 (not_147_out, F25);
  not not_148 (not_148_out, F14);
  not not_149 (not_149_out, F13);
  not not_150 (not_150_out, F12);
  not not_151 (not_151_out, OP6);
  not not_152 (not_152_out, OP3);
  not not_153 (not_153_out, OP2);
  not not_154 (not_154_out, F30);
  not not_155 (not_155_out, F25);
  not not_156 (not_156_out, OP6);
  not not_157 (not_157_out, OP3);
  not not_158 (not_158_out, OP2);
  not not_159 (not_159_out, F30);
  not not_160 (not_160_out, F25);
  not not_161 (not_161_out, F14);
  not not_162 (not_162_out, OP6);
  not not_163 (not_163_out, OP3);
  not not_164 (not_164_out, OP2);
  not not_165 (not_165_out, F14);
  not not_166 (not_166_out, F13);
  not not_167 (not_167_out, F12);
  not not_168 (not_168_out, OP6);
  not not_169 (not_169_out, OP5);
  not not_170 (not_170_out, OP3);
  not not_171 (not_171_out, OP2);
  not not_172 (not_172_out, OP6);
  not not_173 (not_173_out, OP5);
  not not_174 (not_174_out, OP3);
  not not_175 (not_175_out, OP2);
  not not_176 (not_176_out, F14);
  not not_177 (not_177_out, F12);
  not not_178 (not_178_out, OP6);
  not not_179 (not_179_out, OP5);
  not not_180 (not_180_out, OP3);
  not not_181 (not_181_out, OP2);
  not not_182 (not_182_out, F14);
  not not_183 (not_183_out, F12);
  not not_184 (not_184_out, OP6);
  not not_185 (not_185_out, OP5);
  not not_186 (not_186_out, OP4);
  not not_187 (not_187_out, OP3);
  not not_188 (not_188_out, OP2);
  not not_189 (not_189_out, F14);
  not not_190 (not_190_out, F12);
  not not_191 (not_191_out, OP6);
  not not_192 (not_192_out, OP4);
  not not_193 (not_193_out, OP3);
  not not_194 (not_194_out, OP2);
  not not_195 (not_195_out, OP4);
  not not_196 (not_196_out, F14);
  not not_197 (not_197_out, F13);
  not not_198 (not_198_out, F12);
  not not_199 (not_199_out, OP4);
  not not_200 (not_200_out, OP3);
  not not_201 (not_201_out, OP3);
  not not_202 (not_202_out, OP2);
  not not_203 (not_203_out, F14);
  not not_204 (not_204_out, F13);
  not not_205 (not_205_out, OP6);
  not not_206 (not_206_out, OP5);
  not not_207 (not_207_out, OP4);
  not not_208 (not_208_out, OP3);
  not not_209 (not_209_out, OP2);
  not not_210 (not_210_out, F12);
  not not_211 (not_211_out, OP4);
  not not_212 (not_212_out, OP3);
  not not_213 (not_213_out, OP2);
  not not_214 (not_214_out, F30);
  not not_215 (not_215_out, F25);
  not not_216 (not_216_out, F12);
  not not_217 (not_217_out, OP6);
  not not_218 (not_218_out, OP3);
  not not_219 (not_219_out, OP2);
  not not_220 (not_220_out, F30);
  not not_221 (not_221_out, F25);
  not not_222 (not_222_out, F14);
  not not_223 (not_223_out, F12);
  not not_224 (not_224_out, OP6);
  not not_225 (not_225_out, OP3);
  not not_226 (not_226_out, OP2);
  not not_227 (not_227_out, F30);
  not not_228 (not_228_out, F25);
  not not_229 (not_229_out, F14);
  not not_230 (not_230_out, OP6);
  not not_231 (not_231_out, OP3);
  not not_232 (not_232_out, OP2);
  not not_233 (not_233_out, F12);
  not not_234 (not_234_out, OP6);
  not not_235 (not_235_out, OP5);
  not not_236 (not_236_out, OP3);
  not not_237 (not_237_out, OP2);
  not not_238 (not_238_out, F13);
  not not_239 (not_239_out, F12);
  not not_240 (not_240_out, OP6);
  not not_241 (not_241_out, OP5);
  not not_242 (not_242_out, OP3);
  not not_243 (not_243_out, OP2);
  not not_244 (not_244_out, F14);
  not not_245 (not_245_out, F12);
  not not_246 (not_246_out, OP6);
  not not_247 (not_247_out, OP5);
  not not_248 (not_248_out, OP3);
  not not_249 (not_249_out, OP2);
  not not_250 (not_250_out, F14);
  not not_251 (not_251_out, F13);
  not not_252 (not_252_out, F12);
  not not_253 (not_253_out, OP4);
  not not_254 (not_254_out, OP3);
  not not_255 (not_255_out, OP2);
  not not_256 (not_256_out, F14);
  not not_257 (not_257_out, F13);
  not not_258 (not_258_out, OP4);
  not not_259 (not_259_out, OP3);
  not not_260 (not_260_out, OP2);
  not not_261 (not_261_out, F12);
  not not_262 (not_262_out, OP3);
  not not_263 (not_263_out, OP2);
  not not_264 (not_264_out, F30);
  not not_265 (not_265_out, F25);
  not not_266 (not_266_out, F13);
  not not_267 (not_267_out, F12);
  not not_268 (not_268_out, OP6);
  not not_269 (not_269_out, OP3);
  not not_270 (not_270_out, OP2);
  not not_271 (not_271_out, F12);
  not not_272 (not_272_out, OP4);
  not not_273 (not_273_out, OP3);
  not not_274 (not_274_out, OP2);
  and and_1 (and_1_out, not_1_out, not_2_out, not_3_out, not_4_out, not_5_out, not_6_out, OP5, OP4, not_7_out, not_8_out);
  and and_2 (and_2_out, not_9_out, not_10_out, F14, F13, F12, not_11_out, OP5, OP4, not_12_out, not_13_out);
  and and_3 (and_3_out, not_14_out, not_15_out, not_16_out, F13, not_17_out, not_18_out, OP5, OP4, not_19_out, not_20_out);
  and and_4 (and_4_out, not_21_out, not_22_out, not_23_out, not_24_out, not_25_out, OP4, not_26_out, not_27_out);
  and and_5 (and_5_out, F14, F13, F12, not_28_out, not_29_out, OP4, not_30_out, not_31_out);
  and and_6 (and_6_out, F14, not_32_out, not_33_out, not_34_out, not_35_out, OP4, not_36_out, not_37_out);
  and and_7 (and_7_out, F30, not_38_out, F14, not_39_out, F12, not_40_out, not_41_out, OP4, not_42_out, not_43_out);
  and and_8 (and_8_out, not_44_out, F13, not_45_out, not_46_out, not_47_out, not_48_out, not_49_out, not_50_out);
  and and_9 (and_9_out, not_51_out, F13, not_52_out, not_53_out, OP5, not_54_out, not_55_out, not_56_out);
  and and_10 (and_10_out, not_57_out, not_58_out, not_59_out, OP6, OP5, not_60_out, not_61_out, not_62_out);
  and and_11 (and_11_out, not_63_out, not_64_out, F12, OP6, OP5, not_65_out, not_66_out, not_67_out);
  and and_12 (and_12_out, OP6, OP5, not_68_out, OP3, OP2);
  and and_13 (and_13_out, not_69_out, not_70_out, not_71_out, OP6, OP5, not_72_out, not_73_out, OP2);
  and and_14 (and_14_out, F14, F13, F12, OP6, OP5, OP4, not_74_out, not_75_out);
  and and_15 (and_15_out, not_76_out, not_77_out, F14, not_78_out, not_79_out, not_80_out, OP5, OP4, not_81_out, not_82_out);
  and and_16 (and_16_out, not_83_out, not_84_out, F12, not_85_out, not_86_out, not_87_out, not_88_out, not_89_out);
  and and_17 (and_17_out, F30, not_90_out, not_91_out, not_92_out, not_93_out, not_94_out, OP5, OP4, not_95_out, not_96_out);
  and and_18 (and_18_out, not_97_out, not_98_out, F14, F13, F12, not_99_out, OP5, OP4, not_100_out, not_101_out);
  and and_19 (and_19_out, not_102_out, not_103_out, not_104_out, F13, not_105_out, not_106_out, OP5, OP4, not_107_out, not_108_out);
  and and_20 (and_20_out, F14, F13, F12, not_109_out, not_110_out, OP4, not_111_out, not_112_out);
  and and_21 (and_21_out, not_113_out, not_114_out, F14, not_115_out, F12, not_116_out, not_117_out, OP4, not_118_out, not_119_out);
  and and_22 (and_22_out, not_120_out, not_121_out, not_122_out, OP6, OP5, not_123_out, not_124_out, not_125_out);
  and and_23 (and_23_out, not_126_out, not_127_out, F12, OP6, OP5, not_128_out, not_129_out, not_130_out);
  and and_24 (and_24_out, F14, F13, F12, OP6, OP5, OP4, not_131_out, not_132_out);
  and and_25 (and_25_out, not_133_out, not_134_out, F14, not_135_out, F12, not_136_out, OP5, OP4, not_137_out, not_138_out);
  and and_26 (and_26_out, not_139_out, not_140_out, not_141_out, not_142_out, not_143_out, not_144_out, OP5, OP4, not_145_out, not_146_out);
  and and_27 (and_27_out, F30, not_147_out, not_148_out, not_149_out, not_150_out, not_151_out, OP5, OP4, not_152_out, not_153_out);
  and and_28 (and_28_out, not_154_out, not_155_out, F14, F13, F12, not_156_out, OP5, OP4, not_157_out, not_158_out);
  and and_29 (and_29_out, not_159_out, not_160_out, not_161_out, F13, F12, not_162_out, OP5, OP4, not_163_out, not_164_out);
  and and_30 (and_30_out, not_165_out, not_166_out, not_167_out, not_168_out, not_169_out, OP4, not_170_out, not_171_out);
  and and_31 (and_31_out, F14, F13, F12, not_172_out, not_173_out, OP4, not_174_out, not_175_out);
  and and_32 (and_32_out, not_176_out, F13, not_177_out, not_178_out, not_179_out, OP4, not_180_out, not_181_out);
  and and_33 (and_33_out, not_182_out, F13, not_183_out, not_184_out, not_185_out, not_186_out, not_187_out, not_188_out);
  and and_34 (and_34_out, not_189_out, F13, not_190_out, not_191_out, OP5, not_192_out, not_193_out, not_194_out);
  and and_35 (and_35_out, OP6, OP5, not_195_out, OP3, OP2);
  and and_36 (and_36_out, not_196_out, not_197_out, not_198_out, OP6, OP5, not_199_out, not_200_out, OP2);
  and and_37 (and_37_out, F14, F13, F12, OP6, OP5, OP4, not_201_out, not_202_out);
  and and_38 (and_38_out, not_203_out, not_204_out, F12, not_205_out, not_206_out, not_207_out, not_208_out, not_209_out);
  and and_39 (and_39_out, F14, F13, not_210_out, OP6, OP5, not_211_out, not_212_out, not_213_out);
  and and_40 (and_40_out, not_214_out, not_215_out, F14, F13, not_216_out, not_217_out, OP5, OP4, not_218_out, not_219_out);
  and and_41 (and_41_out, not_220_out, not_221_out, not_222_out, F13, not_223_out, not_224_out, OP5, OP4, not_225_out, not_226_out);
  and and_42 (and_42_out, not_227_out, not_228_out, not_229_out, F13, F12, not_230_out, OP5, OP4, not_231_out, not_232_out);
  and and_43 (and_43_out, F14, F13, not_233_out, not_234_out, not_235_out, OP4, not_236_out, not_237_out);
  and and_44 (and_44_out, F14, not_238_out, not_239_out, not_240_out, not_241_out, OP4, not_242_out, not_243_out);
  and and_45 (and_45_out, not_244_out, F13, not_245_out, not_246_out, not_247_out, OP4, not_248_out, not_249_out);
  and and_46 (and_46_out, not_250_out, not_251_out, not_252_out, OP6, OP5, not_253_out, not_254_out, not_255_out);
  and and_47 (and_47_out, not_256_out, not_257_out, F12, OP6, OP5, not_258_out, not_259_out, not_260_out);
  and and_48 (and_48_out, F14, F13, not_261_out, OP6, OP5, OP4, not_262_out, not_263_out);
  and and_49 (and_49_out, not_264_out, not_265_out, F14, not_266_out, not_267_out, not_268_out, OP5, OP4, not_269_out, not_270_out);
  and and_50 (and_50_out, F14, F13, not_271_out, OP6, OP5, not_272_out, not_273_out, not_274_out);
  or or_1 (S0, and_1_out, and_2_out, and_3_out, and_4_out, and_5_out, and_6_out, and_7_out, and_8_out, and_9_out, and_10_out, and_11_out, and_12_out, and_13_out, and_14_out, and_15_out, and_16_out);
  or or_2 (S1, and_17_out, and_18_out, and_19_out, and_20_out, and_21_out, and_22_out, and_23_out, and_24_out, and_25_out);
  or or_3 (S2, and_26_out, and_27_out, and_28_out, and_29_out, and_30_out, and_31_out, and_32_out, and_33_out, and_34_out, and_35_out, and_36_out, and_37_out, and_38_out, and_39_out);
  or or_4 (S3, and_40_out, and_41_out, and_42_out, and_43_out, and_44_out, and_45_out, and_46_out, and_47_out, and_48_out, and_49_out, and_50_out);
endmodule

// 控制信号生成
module \控制信号自动生成  (
  input  OP2,
  input  OP3,
  input  OP4,
  input  OP5,
  input  OP6,
  input  F12,
  input  F13,
  input  F14,
  input  F25,
  input  F30,
  output MemToReg,
  output MemWrite,
  output ALU_SRC,
  output RegWrite,
  output ecall,
  output S_Type,
  output BEQ,
  output BNE,
  output JALR,
  output JAL,
  output BLTU,
  output CSR,
  output LH,
  output LUI
);

  wire and_1_out, and_2_out, and_4_out, and_5_out, and_6_out, and_7_out, and_8_out, and_9_out, and_10_out,
       and_11_out, and_12_out, and_13_out, and_14_out, and_15_out, and_16_out, and_17_out, and_18_out,
       and_19_out, and_20_out, and_21_out, and_22_out, and_23_out, and_24_out, and_25_out, and_26_out,
       and_27_out, and_28_out, and_29_out, and_30_out, and_31_out, and_32_out, and_33_out, and_34_out,
       and_35_out, and_36_out, and_37_out, and_45_out, and_46_out, not_1_out, not_2_out, not_3_out,
       not_4_out, not_5_out, not_6_out, not_7_out, not_8_out, not_9_out, not_10_out, not_11_out, not_12_out,
       not_13_out, not_14_out, not_15_out, not_16_out, not_17_out, not_18_out, not_19_out, not_20_out,
       not_21_out, not_22_out, not_23_out, not_24_out, not_25_out, not_26_out, not_27_out, not_28_out,
       not_29_out, not_30_out, not_31_out, not_32_out, not_33_out, not_34_out, not_35_out, not_36_out,
       not_37_out, not_38_out, not_39_out, not_40_out, not_41_out, not_42_out, not_43_out, not_44_out,
       not_45_out, not_46_out, not_47_out, not_48_out, not_49_out, not_50_out, not_51_out, not_52_out,
       not_53_out, not_54_out, not_55_out, not_56_out, not_57_out, not_58_out, not_59_out, not_60_out,
       not_61_out, not_62_out, not_63_out, not_64_out, not_65_out, not_66_out, not_67_out, not_68_out,
       not_69_out, not_70_out, not_71_out, not_72_out, not_73_out, not_74_out, not_75_out, not_76_out,
       not_77_out, not_78_out, not_79_out, not_80_out, not_81_out, not_82_out, not_83_out, not_84_out,
       not_85_out, not_86_out, not_87_out, not_88_out, not_89_out, not_90_out, not_91_out, not_92_out,
       not_93_out, not_94_out, not_95_out, not_96_out, not_97_out, not_98_out, not_99_out, not_100_out,
       not_101_out, not_102_out, not_103_out, not_104_out, not_105_out, not_106_out, not_107_out,
       not_108_out, not_109_out, not_110_out, not_111_out, not_112_out, not_113_out, not_114_out,
       not_115_out, not_116_out, not_117_out, not_118_out, not_119_out, not_120_out, not_121_out,
       not_122_out, not_123_out, not_124_out, not_125_out, not_126_out, not_127_out, not_128_out,
       not_129_out, not_130_out, not_131_out, not_132_out, not_133_out, not_134_out, not_135_out,
       not_136_out, not_137_out, not_138_out, not_139_out, not_140_out, not_141_out, not_142_out,
       not_143_out, not_144_out, not_145_out, not_146_out, not_147_out, not_148_out, not_149_out,
       not_150_out, not_151_out, not_152_out, not_153_out, not_154_out, not_155_out, not_156_out,
       not_157_out, not_158_out, not_159_out, not_160_out, not_161_out, not_162_out, not_163_out,
       not_164_out, not_165_out, not_166_out, not_167_out, not_168_out, not_169_out, not_170_out,
       not_171_out, not_172_out, not_173_out, not_174_out, not_175_out, not_176_out, not_177_out,
       not_178_out, not_179_out, not_180_out, not_181_out, not_182_out, not_183_out, not_184_out,
       not_185_out, not_186_out, not_187_out, not_188_out, not_189_out, not_190_out, not_191_out,
       not_192_out, not_193_out, not_194_out, not_195_out, not_196_out, not_197_out, not_198_out,
       not_199_out, not_200_out, not_201_out, not_202_out, not_203_out, not_204_out, not_205_out,
       not_206_out, not_207_out, not_208_out, not_209_out, not_210_out, not_211_out, not_212_out,
       not_213_out, not_214_out, not_215_out, not_216_out, not_217_out, not_218_out, not_219_out,
       not_220_out, not_221_out, not_222_out, not_223_out, not_224_out, not_225_out, not_226_out,
       not_227_out, not_228_out, not_229_out, not_230_out, not_231_out, not_232_out, not_233_out,
       not_234_out, not_235_out, not_236_out, not_237_out, not_238_out, not_239_out, not_240_out,
       not_241_out, not_242_out, not_243_out, not_244_out, not_245_out, not_246_out, not_247_out,
       not_248_out, not_249_out, not_250_out, not_251_out, not_252_out, not_253_out, not_254_out,
       not_255_out, not_256_out, not_257_out, not_258_out, not_259_out, not_260_out, not_261_out,
       not_262_out, not_263_out, not_264_out, not_265_out, not_266_out;

  not not_1 (not_1_out, F14);
  not not_2 (not_2_out, F12);
  not not_3 (not_3_out, OP6);
  not not_4 (not_4_out, OP5);
  not not_5 (not_5_out, OP4);
  not not_6 (not_6_out, OP3);
  not not_7 (not_7_out, OP2);
  not not_8 (not_8_out, F14);
  not not_9 (not_9_out, F13);
  not not_10 (not_10_out, OP6);
  not not_11 (not_11_out, OP5);
  not not_12 (not_12_out, OP4);
  not not_13 (not_13_out, OP3);
  not not_14 (not_14_out, OP2);
  not not_15 (not_15_out, F14);
  not not_16 (not_16_out, F12);
  not not_17 (not_17_out, OP6);
  not not_18 (not_18_out, OP4);
  not not_19 (not_19_out, OP3);
  not not_20 (not_20_out, OP2);
  not not_21 (not_21_out, F14);
  not not_22 (not_22_out, F13);
  not not_23 (not_23_out, F12);
  not not_24 (not_24_out, OP6);
  not not_25 (not_25_out, OP5);
  not not_26 (not_26_out, OP3);
  not not_27 (not_27_out, OP2);
  not not_28 (not_28_out, OP6);
  not not_29 (not_29_out, OP5);
  not not_30 (not_30_out, OP3);
  not not_31 (not_31_out, OP2);
  not not_32 (not_32_out, F12);
  not not_33 (not_33_out, OP6);
  not not_34 (not_34_out, OP5);
  not not_35 (not_35_out, OP3);
  not not_36 (not_36_out, OP2);
  not not_37 (not_37_out, F13);
  not not_38 (not_38_out, F12);
  not not_39 (not_39_out, OP6);
  not not_40 (not_40_out, OP5);
  not not_41 (not_41_out, OP3);
  not not_42 (not_42_out, OP2);
  not not_43 (not_43_out, F14);
  not not_44 (not_44_out, F12);
  not not_45 (not_45_out, OP6);
  not not_46 (not_46_out, OP5);
  not not_47 (not_47_out, OP3);
  not not_48 (not_48_out, OP2);
  not not_49 (not_49_out, F14);
  not not_50 (not_50_out, F13);
  not not_51 (not_51_out, OP6);
  not not_52 (not_52_out, OP5);
  not not_53 (not_53_out, OP3);
  not not_54 (not_54_out, OP2);
  not not_55 (not_55_out, F30);
  not not_56 (not_56_out, F25);
  not not_57 (not_57_out, F13);
  not not_58 (not_58_out, OP6);
  not not_59 (not_59_out, OP5);
  not not_60 (not_60_out, OP3);
  not not_61 (not_61_out, OP2);
  not not_62 (not_62_out, F25);
  not not_63 (not_63_out, F13);
  not not_64 (not_64_out, OP6);
  not not_65 (not_65_out, OP5);
  not not_66 (not_66_out, OP3);
  not not_67 (not_67_out, OP2);
  not not_68 (not_68_out, F14);
  not not_69 (not_69_out, F12);
  not not_70 (not_70_out, OP6);
  not not_71 (not_71_out, OP5);
  not not_72 (not_72_out, OP4);
  not not_73 (not_73_out, OP3);
  not not_74 (not_74_out, OP2);
  not not_75 (not_75_out, F14);
  not not_76 (not_76_out, F12);
  not not_77 (not_77_out, OP6);
  not not_78 (not_78_out, OP4);
  not not_79 (not_79_out, OP3);
  not not_80 (not_80_out, OP2);
  not not_81 (not_81_out, F14);
  not not_82 (not_82_out, F13);
  not not_83 (not_83_out, F12);
  not not_84 (not_84_out, OP4);
  not not_85 (not_85_out, OP3);
  not not_86 (not_86_out, F14);
  not not_87 (not_87_out, F13);
  not not_88 (not_88_out, OP6);
  not not_89 (not_89_out, OP5);
  not not_90 (not_90_out, OP4);
  not not_91 (not_91_out, OP3);
  not not_92 (not_92_out, OP2);
  not not_93 (not_93_out, F30);
  not not_94 (not_94_out, F25);
  not not_95 (not_95_out, F14);
  not not_96 (not_96_out, F13);
  not not_97 (not_97_out, F12);
  not not_98 (not_98_out, OP6);
  not not_99 (not_99_out, OP3);
  not not_100 (not_100_out, OP2);
  not not_101 (not_101_out, F25);
  not not_102 (not_102_out, F14);
  not not_103 (not_103_out, F13);
  not not_104 (not_104_out, F12);
  not not_105 (not_105_out, OP6);
  not not_106 (not_106_out, OP3);
  not not_107 (not_107_out, OP2);
  not not_108 (not_108_out, F30);
  not not_109 (not_109_out, F25);
  not not_110 (not_110_out, OP6);
  not not_111 (not_111_out, OP3);
  not not_112 (not_112_out, OP2);
  not not_113 (not_113_out, F30);
  not not_114 (not_114_out, F25);
  not not_115 (not_115_out, F12);
  not not_116 (not_116_out, OP6);
  not not_117 (not_117_out, OP3);
  not not_118 (not_118_out, OP2);
  not not_119 (not_119_out, F30);
  not not_120 (not_120_out, F25);
  not not_121 (not_121_out, F14);
  not not_122 (not_122_out, F12);
  not not_123 (not_123_out, OP6);
  not not_124 (not_124_out, OP3);
  not not_125 (not_125_out, OP2);
  not not_126 (not_126_out, F30);
  not not_127 (not_127_out, F25);
  not not_128 (not_128_out, F14);
  not not_129 (not_129_out, OP6);
  not not_130 (not_130_out, OP3);
  not not_131 (not_131_out, OP2);
  not not_132 (not_132_out, F14);
  not not_133 (not_133_out, F13);
  not not_134 (not_134_out, F12);
  not not_135 (not_135_out, OP6);
  not not_136 (not_136_out, OP5);
  not not_137 (not_137_out, OP3);
  not not_138 (not_138_out, OP2);
  not not_139 (not_139_out, OP6);
  not not_140 (not_140_out, OP5);
  not not_141 (not_141_out, OP3);
  not not_142 (not_142_out, OP2);
  not not_143 (not_143_out, F12);
  not not_144 (not_144_out, OP6);
  not not_145 (not_145_out, OP5);
  not not_146 (not_146_out, OP3);
  not not_147 (not_147_out, OP2);
  not not_148 (not_148_out, F13);
  not not_149 (not_149_out, F12);
  not not_150 (not_150_out, OP6);
  not not_151 (not_151_out, OP5);
  not not_152 (not_152_out, OP3);
  not not_153 (not_153_out, OP2);
  not not_154 (not_154_out, F14);
  not not_155 (not_155_out, F12);
  not not_156 (not_156_out, OP6);
  not not_157 (not_157_out, OP5);
  not not_158 (not_158_out, OP3);
  not not_159 (not_159_out, OP2);
  not not_160 (not_160_out, F14);
  not not_161 (not_161_out, F13);
  not not_162 (not_162_out, OP6);
  not not_163 (not_163_out, OP5);
  not not_164 (not_164_out, OP3);
  not not_165 (not_165_out, OP2);
  not not_166 (not_166_out, F30);
  not not_167 (not_167_out, F25);
  not not_168 (not_168_out, F13);
  not not_169 (not_169_out, OP6);
  not not_170 (not_170_out, OP5);
  not not_171 (not_171_out, OP3);
  not not_172 (not_172_out, OP2);
  not not_173 (not_173_out, F25);
  not not_174 (not_174_out, F13);
  not not_175 (not_175_out, OP6);
  not not_176 (not_176_out, OP5);
  not not_177 (not_177_out, OP3);
  not not_178 (not_178_out, OP2);
  not not_179 (not_179_out, F14);
  not not_180 (not_180_out, F12);
  not not_181 (not_181_out, OP6);
  not not_182 (not_182_out, OP5);
  not not_183 (not_183_out, OP4);
  not not_184 (not_184_out, OP3);
  not not_185 (not_185_out, OP2);
  not not_186 (not_186_out, OP4);
  not not_187 (not_187_out, F14);
  not not_188 (not_188_out, F13);
  not not_189 (not_189_out, F12);
  not not_190 (not_190_out, OP4);
  not not_191 (not_191_out, OP3);
  not not_192 (not_192_out, F30);
  not not_193 (not_193_out, F25);
  not not_194 (not_194_out, F14);
  not not_195 (not_195_out, F13);
  not not_196 (not_196_out, OP6);
  not not_197 (not_197_out, OP3);
  not not_198 (not_198_out, OP2);
  not not_199 (not_199_out, F30);
  not not_200 (not_200_out, F25);
  not not_201 (not_201_out, F13);
  not not_202 (not_202_out, F12);
  not not_203 (not_203_out, OP6);
  not not_204 (not_204_out, OP3);
  not not_205 (not_205_out, OP2);
  not not_206 (not_206_out, F14);
  not not_207 (not_207_out, F13);
  not not_208 (not_208_out, OP6);
  not not_209 (not_209_out, OP5);
  not not_210 (not_210_out, OP4);
  not not_211 (not_211_out, OP3);
  not not_212 (not_212_out, OP2);
  not not_213 (not_213_out, OP6);
  not not_214 (not_214_out, OP3);
  not not_215 (not_215_out, F30);
  not not_216 (not_216_out, F25);
  not not_217 (not_217_out, F13);
  not not_218 (not_218_out, OP6);
  not not_219 (not_219_out, OP3);
  not not_220 (not_220_out, OP2);
  not not_221 (not_221_out, F14);
  not not_222 (not_222_out, F13);
  not not_223 (not_223_out, F12);
  not not_224 (not_224_out, OP3);
  not not_225 (not_225_out, OP2);
  not not_226 (not_226_out, F14);
  not not_227 (not_227_out, F12);
  not not_228 (not_228_out, OP6);
  not not_229 (not_229_out, OP4);
  not not_230 (not_230_out, OP3);
  not not_231 (not_231_out, OP2);
  not not_232 (not_232_out, F14);
  not not_233 (not_233_out, F13);
  not not_234 (not_234_out, F12);
  not not_235 (not_235_out, OP4);
  not not_236 (not_236_out, OP3);
  not not_237 (not_237_out, OP2);
  not not_238 (not_238_out, F14);
  not not_239 (not_239_out, F13);
  not not_240 (not_240_out, OP4);
  not not_241 (not_241_out, OP3);
  not not_242 (not_242_out, OP2);
  not not_243 (not_243_out, F14);
  not not_244 (not_244_out, F13);
  not not_245 (not_245_out, F12);
  not not_246 (not_246_out, OP4);
  not not_247 (not_247_out, OP3);
  not not_248 (not_248_out, OP4);
  not not_249 (not_249_out, F12);
  not not_250 (not_250_out, OP4);
  not not_251 (not_251_out, OP3);
  not not_252 (not_252_out, OP2);
  not not_253 (not_253_out, F12);
  not not_254 (not_254_out, OP3);
  not not_255 (not_255_out, OP2);
  not not_256 (not_256_out, OP3);
  not not_257 (not_257_out, OP2);
  not not_258 (not_258_out, F14);
  not not_259 (not_259_out, F13);
  not not_260 (not_260_out, OP6);
  not not_261 (not_261_out, OP5);
  not not_262 (not_262_out, OP4);
  not not_263 (not_263_out, OP3);
  not not_264 (not_264_out, OP2);
  not not_265 (not_265_out, OP6);
  not not_266 (not_266_out, OP3);
  and and_1 (and_1_out, not_1_out, F13, not_2_out, not_3_out, not_4_out, not_5_out, not_6_out, not_7_out);
  and and_2 (and_2_out, not_8_out, not_9_out, F12, not_10_out, not_11_out, not_12_out, not_13_out, not_14_out);
  and and_3 (MemWrite, not_15_out, F13, not_16_out, not_17_out, OP5, not_18_out, not_19_out, not_20_out);
  and and_4 (and_4_out, not_21_out, not_22_out, not_23_out, not_24_out, not_25_out, OP4, not_26_out, not_27_out);
  and and_5 (and_5_out, F14, F13, F12, not_28_out, not_29_out, OP4, not_30_out, not_31_out);
  and and_6 (and_6_out, F14, F13, not_32_out, not_33_out, not_34_out, OP4, not_35_out, not_36_out);
  and and_7 (and_7_out, F14, not_37_out, not_38_out, not_39_out, not_40_out, OP4, not_41_out, not_42_out);
  and and_8 (and_8_out, not_43_out, F13, not_44_out, not_45_out, not_46_out, OP4, not_47_out, not_48_out);
  and and_9 (and_9_out, not_49_out, not_50_out, F12, not_51_out, not_52_out, OP4, not_53_out, not_54_out);
  and and_10 (and_10_out, not_55_out, not_56_out, F14, not_57_out, F12, not_58_out, not_59_out, OP4, not_60_out, not_61_out);
  and and_11 (and_11_out, F30, not_62_out, F14, not_63_out, F12, not_64_out, not_65_out, OP4, not_66_out, not_67_out);
  and and_12 (and_12_out, not_68_out, F13, not_69_out, not_70_out, not_71_out, not_72_out, not_73_out, not_74_out);
  and and_13 (and_13_out, not_75_out, F13, not_76_out, not_77_out, OP5, not_78_out, not_79_out, not_80_out);
  and and_14 (and_14_out, not_81_out, not_82_out, not_83_out, OP6, OP5, not_84_out, not_85_out, OP2);
  and and_15 (and_15_out, not_86_out, not_87_out, F12, not_88_out, not_89_out, not_90_out, not_91_out, not_92_out);
  and and_16 (and_16_out, not_93_out, not_94_out, not_95_out, not_96_out, not_97_out, not_98_out, OP5, OP4, not_99_out, not_100_out);
  and and_17 (and_17_out, F30, not_101_out, not_102_out, not_103_out, not_104_out, not_105_out, OP5, OP4, not_106_out, not_107_out);
  and and_18 (and_18_out, not_108_out, not_109_out, F14, F13, F12, not_110_out, OP5, OP4, not_111_out, not_112_out);
  and and_19 (and_19_out, not_113_out, not_114_out, F14, F13, not_115_out, not_116_out, OP5, OP4, not_117_out, not_118_out);
  and and_20 (and_20_out, not_119_out, not_120_out, not_121_out, F13, not_122_out, not_123_out, OP5, OP4, not_124_out, not_125_out);
  and and_21 (and_21_out, not_126_out, not_127_out, not_128_out, F13, F12, not_129_out, OP5, OP4, not_130_out, not_131_out);
  and and_22 (and_22_out, not_132_out, not_133_out, not_134_out, not_135_out, not_136_out, OP4, not_137_out, not_138_out);
  and and_23 (and_23_out, F14, F13, F12, not_139_out, not_140_out, OP4, not_141_out, not_142_out);
  and and_24 (and_24_out, F14, F13, not_143_out, not_144_out, not_145_out, OP4, not_146_out, not_147_out);
  and and_25 (and_25_out, F14, not_148_out, not_149_out, not_150_out, not_151_out, OP4, not_152_out, not_153_out);
  and and_26 (and_26_out, not_154_out, F13, not_155_out, not_156_out, not_157_out, OP4, not_158_out, not_159_out);
  and and_27 (and_27_out, not_160_out, not_161_out, F12, not_162_out, not_163_out, OP4, not_164_out, not_165_out);
  and and_28 (and_28_out, not_166_out, not_167_out, F14, not_168_out, F12, not_169_out, not_170_out, OP4, not_171_out, not_172_out);
  and and_29 (and_29_out, F30, not_173_out, F14, not_174_out, F12, not_175_out, not_176_out, OP4, not_177_out, not_178_out);
  and and_30 (and_30_out, not_179_out, F13, not_180_out, not_181_out, not_182_out, not_183_out, not_184_out, not_185_out);
  and and_31 (and_31_out, OP6, OP5, not_186_out, OP3, OP2);
  and and_32 (and_32_out, not_187_out, not_188_out, not_189_out, OP6, OP5, not_190_out, not_191_out, OP2);
  and and_33 (and_33_out, not_192_out, not_193_out, not_194_out, not_195_out, F12, not_196_out, OP5, OP4, not_197_out, not_198_out);
  and and_34 (and_34_out, not_199_out, not_200_out, F14, not_201_out, not_202_out, not_203_out, OP5, OP4, not_204_out, not_205_out);
  and and_35 (and_35_out, not_206_out, not_207_out, F12, not_208_out, not_209_out, not_210_out, not_211_out, not_212_out);
  and and_36 (and_36_out, not_213_out, OP5, OP4, not_214_out, OP2);
  and and_37 (and_37_out, not_215_out, not_216_out, F14, not_217_out, F12, not_218_out, OP5, OP4, not_219_out, not_220_out);
  and and_38 (ecall, not_221_out, not_222_out, not_223_out, OP6, OP5, OP4, not_224_out, not_225_out);
  and and_39 (S_Type, not_226_out, F13, not_227_out, not_228_out, OP5, not_229_out, not_230_out, not_231_out);
  and and_40 (BEQ, not_232_out, not_233_out, not_234_out, OP6, OP5, not_235_out, not_236_out, not_237_out);
  and and_41 (BNE, not_238_out, not_239_out, F12, OP6, OP5, not_240_out, not_241_out, not_242_out);
  and and_42 (JALR, not_243_out, not_244_out, not_245_out, OP6, OP5, not_246_out, not_247_out, OP2);
  and and_43 (JAL, OP6, OP5, not_248_out, OP3, OP2);
  and and_44 (BLTU, F14, F13, not_249_out, OP6, OP5, not_250_out, not_251_out, not_252_out);
  and and_45 (and_45_out, F14, F13, not_253_out, OP6, OP5, OP4, not_254_out, not_255_out);
  and and_46 (and_46_out, F14, F13, F12, OP6, OP5, OP4, not_256_out, not_257_out);
  and and_47 (LH, not_258_out, not_259_out, F12, not_260_out, not_261_out, not_262_out, not_263_out, not_264_out);
  and and_48 (LUI, not_265_out, OP5, OP4, not_266_out, OP2);
  or or_1 (MemToReg, and_1_out, and_2_out);
  or or_2 (CSR, and_45_out, and_46_out);
  or or_3 (ALU_SRC, and_4_out, and_5_out, and_6_out, and_7_out, and_8_out, and_9_out, and_10_out, and_11_out, and_12_out, and_13_out, and_14_out, and_15_out);
  or or_4 (RegWrite, and_16_out, and_17_out, and_18_out, and_19_out, and_20_out, and_21_out, and_22_out, and_23_out, and_24_out, and_25_out, and_26_out, and_27_out, and_28_out, and_29_out, and_30_out, and_31_out, and_32_out, and_33_out, and_34_out, and_35_out, and_36_out, and_37_out);
endmodule

// ALU
module ALU (
  input  [31:0] X,
  input  [31:0] Y,
  input  [3:0] AluOP,
  output out_4,
  output Equal,
  output out_6,
  output [31:0] Result,
  output [31:0] Result_2
);

  wire [0:0] comparator_1_lt, comparator_2_lt;
  wire [31:0] adder_1_out, AND_out, divider_1_out, divider_1_rem, multiplier_1_cout, multiplier_1_out,
       NOR_out, OR_out, shifter_1_out, shifter_2_out, shifter_3_out, subtractor_1_out, XOR_out;

  assign AND_out = X & Y;  // AND_Gate AND, 32 bits wide
  assign OR_out = X | Y;  // OR_Gate OR, 32 bits wide
  Shifter #(.width(32), .shift("ll")) shifter_1 (.in(X), .\dist (Y[4:0]), .out(shifter_1_out));
  Shifter #(.width(32), .shift("ar")) shifter_2 (.in(X), .\dist (Y[4:0]), .out(shifter_2_out));
  Shifter #(.width(32), .shift("lr")) shifter_3 (.in(X), .\dist (Y[4:0]), .out(shifter_3_out));
  Multiplier #(.width(32)) multiplier_1 (.a(X), .b(Y), .out(multiplier_1_out), .cout(multiplier_1_cout));  // open: cin
  Divider #(.width(32)) divider_1 (.a(X), .b(Y), .out(divider_1_out), .rem(divider_1_rem));  // open: upper
  Adder #(.width(32)) adder_1 (.a(X), .b(Y), .out(adder_1_out));  // open: cin, cout
  Subtractor #(.width(32)) subtractor_1 (.a(X), .b(Y), .out(subtractor_1_out));  // open: bin, bout
  assign XOR_out = X ^ Y;  // XOR_Gate XOR, 32 bits wide
  assign NOR_out = ~(X | Y);  // NOR_Gate NOR, 32 bits wide
  Comparator #(.width(32), .mode("twosComplement")) comparator_1 (
    .a(X), .b(Y), .eq(Equal), .lt(comparator_1_lt[0]));  // open: gt
  Comparator #(.width(32), .mode("unsigned")) comparator_2 (.a(X), .b(Y), .lt(comparator_2_lt[0]));  // open: gt, eq
  Multiplexer #(.select(4), .width(32), .disabled("Z"), .enable("false")) multiplexer_1 (
    .in0(shifter_1_out), .in1(shifter_2_out), .in2(shifter_3_out), .in3(multiplier_1_out),
    .in4(divider_1_out), .in5(adder_1_out), .in6(subtractor_1_out), .in7(AND_out), .in8(OR_out),
    .in9(XOR_out), .in10(NOR_out), .in11({{31{1'b0}}, comparator_1_lt[0]}),
    .in12({{31{1'b0}}, comparator_2_lt[0]}), .in13({32{1'b0}}), .in14({32{1'b0}}), .in15({32{1'b0}}),
    .out(Result), .sel(AluOP));
  Multiplexer #(.select(4), .width(32), .disabled("Z"), .enable("false")) multiplexer_2 (
    .in0({32{1'b0}}), .in1({32{1'b0}}), .in2({32{1'b0}}), .in3(multiplier_1_cout), .in4(divider_1_rem),
    .in5({32{1'b0}}), .in6({32{1'b0}}), .in7({32{1'b0}}), .in8({32{1'b0}}), .in9({32{1'b0}}),
    .in10({32{1'b0}}), .in11({32{1'b0}}), .in12({32{1'b0}}), .in13({32{1'b0}}), .in14({32{1'b0}}),
    .in15({32{1'b0}}), .out(Result_2), .sel(AluOP));
  Multiplexer #(.select(4), .width(1), .disabled("Z"), .enable("false")) multiplexer_3 (
    .in0(1'b0), .in1(1'b0), .in2(1'b0), .in3(1'b0), .in4(1'b0), .in5(1'b0), .in6(1'b0), .in7(1'b0),
    .in8(1'b0), .in9(1'b0), .in10(1'b0), .in11(comparator_1_lt[0]), .in12(comparator_2_lt[0]), .in13(1'b0),
    .in14(1'b0), .in15(1'b0), .out(out_6), .sel(AluOP));
  not not_1 (out_4, out_6);

  // Other names for the same wires on the sheet: Result2[31:0] = Result_2; S[3:0] = AluOP; tunnel = out_6;
  //   tunnel_t = out_4

  // Notes on the sheet:
  //   不要改变此引脚区域内容，也不要改变ALU封装形式
  //   输入引脚
  //   输出引脚
endmodule

module Regifile (
  input  [31:0] Din,
  input  Clk,
  input  WE,
  input  [4:0] R1_num,
  input  [4:0] W_num,
  input  [4:0] R2_num,
  output [31:0] R1,
  output [31:0] R2
);

  // RegisterFile registerfile_1: pin names not known; wires that end beside it: Din, Clk, WE, W_num, R1_num, R2_num, R1, R2
endmodule

module \理想流水线  (
  output RegWrite,
  output MemWrite,
  output [31:0] IF_PC,
  output [31:0] ID_PC,
  output [31:0] EX_PC,
  output [31:0] M_PC,
  output [31:0] WB_PC,
  output [31:0] RDin,
  output [31:0] MDin,
  output [31:0] LedData
);

  wire Beq, BLTU, Bne, CLK, clock_1_out, comparator_1_eq, comparator_1_lt, comparator_2_eq, d_ff_1_q, Equal,
       EX_CSR, EX_ecall, ex_mem_1_ex_csr, ex_mem_1_ex_jal, ex_mem_1_ex_jalr, ex_mem_1_ex_lh,
       ex_mem_1_ex_memtoreg, ex_mem_1_ex_regwrite, ex_mem_1_mem_halt, GE, Go, halt, ID_ecall,
       id_ex_1_ex_alusrcb, id_ex_1_ex_lh, id_ex_1_ex_memtoreg, id_ex_1_ex_memwrite, id_ex_1_ex_regwrite,
       id_ex_1_ex_s_type, IR1, IR2, IR3, JAL, JALR, nand_1_out, newcontrol_1_out_4, newcontrol_1_out_5,
       newcontrol_1_out_6, newcontrol_1_out_7, newcontrol_1_out_8, newcontrol_1_out_9, newcontrol_1_out_10,
       newcontrol_1_out_11, newcontrol_1_out_12, newcontrol_1_out_14, newcontrol_1_out_15,
       newcontrol_1_out_16, newcontrol_1_out_17, not_1_out, not_2_out, not_3_out, not_4_out, register_2_q,
       RST, URET, W1, W2, W3, WB_CSR, WB_JAL, WB_JALR, WB_LH, WB_MemToReg, whichpc_1_out_9;
  wire [1:0] undriven;
  wire [3:0] id_ex_1_ex_aluop, newcontrol_1_out_13;
  wire [4:0] ex_mem_1_mem_rd, EX_rs1, id_ex_1_ex_rd, multiplexer_2_out, multiplexer_3_out, WB_rd;
  wire [11:0] EX_imm12, EX_imms, immb;
  wire [12:0] CNT_num;
  wire [15:0] \LoadUse次数 , \总周期数 , \插入气泡数 , \无条件分支数 , \条件分支成功数 ;
  wire [19:0] immuj;
  wire [31:0] alu_bin_1_alu_bin, CSR_out, DM_Dout, EX_ALU_Res, EX_CSR_out, EX_IR, ex_mem_1_mem_alu_res,
       ex_mem_1_mem_csr_out, EX_Reg_R1, EX_Reg_R2, ID_IR, IF_IR, MEM_IR, multiplexer_1_out,
       multiplexer_4_out, pc_in_1_pc_2, ram_1_data, regifile_1_r1, regifile_1_r2, register_1_q, WB_ALU_Res,
       WB_IR;

  Button \u_总复位  (.out(RST));
  Button _1 (.out(IR1));
  Button _2 (.out(IR2));
  Button _3 (.out(IR3));
  // Probe on \总周期数 
  // Probe on \总周期数 
  Button \u_继续运行  (.out(Go));
  LED #(.active("true")) led_1 (.in(W1));
  LED #(.active("true")) led_2 (.in(W2));
  LED #(.active("true")) led_3 (.in(W3));
  Hex_Digit_Display hex_digit_display_1 (.value(LedData[31:28]));  // open: dp
  // Probe on IF_PC[19:0]
  // RiscV_Probe riscv_probe_1: pin names not known; wires that end beside it: IF_IR
  WhichPC whichpc_1 (
    .out_9(whichpc_1_out_9), .GE(GE), .BLTU(BLTU), .URET(URET), .JALR(JALR), .JAL(JAL), .Beq(Beq), .Bne(Bne),
    .Equal(Equal));
  Multiplexer #(.select(1), .width(32), .disabled("Z"), .enable("false")) multiplexer_1 (
    .in0(EX_PC), .in1(IF_PC), .out(multiplexer_1_out), .sel(whichpc_1_out_9));
  Hex_Digit_Display hex_digit_display_2 (.value(LedData[27:24]));  // open: dp
  Hex_Digit_Display hex_digit_display_3 (.value(LedData[23:20]));  // open: dp
  // Probe on ID_PC[19:0]
  // RiscV_Probe riscv_probe_2: pin names not known; wires that end beside it: ID_IR
  Hex_Digit_Display hex_digit_display_4 (.value(LedData[19:16]));  // open: dp
  Hex_Digit_Display hex_digit_display_5 (.value(LedData[15:12]));  // open: dp
  PC_in pc_in_1 (
    .PC(multiplexer_1_out), .immb(immb), .immuj(immuj), .ALU_Res(EX_ALU_Res), .\中断编号 (undriven), .GE(GE),
    .BLTU(BLTU), .URET(URET), .JALR(JALR), .JAL(JAL), .Beq(Beq), .Bne(Bne), .Equal(Equal), .\中断触发 (1'b0),
    .PC_2(pc_in_1_pc_2));  // open: EPC
  not not_1 (not_1_out, halt);
  Hex_Digit_Display hex_digit_display_6 (.value(LedData[11:8]));  // open: dp
  Hex_Digit_Display hex_digit_display_7 (.value(LedData[7:4]));  // open: dp
  // Probe on EX_PC[19:0]
  // RiscV_Probe riscv_probe_3: pin names not known; wires that end beside it: EX_IR
  Register #(.width(32), .trigger("rising"), .Select("low")) PC (
    .D(pc_in_1_pc_2), .en(not_1_out), .Q(IF_PC), .clk(CLK), .clr(RST));
  Hex_Digit_Display hex_digit_display_8 (.value(LedData[3:0]));  // open: dp
  not not_2 (not_2_out, halt);
  Counter #(.width(16), .max('hffff), .ongoal("wrap"), .trigger("rising"), .behavior("new")) counter_1 (
    .count(not_2_out), .Q(\总周期数 ), .clk(CLK), .clr(RST));  // open: load, D, carry, preset, down
  // Probe on \总周期数 
  // Probe on M_PC[19:0]
  // RiscV_Probe riscv_probe_4: pin names not known; wires that end beside it: MEM_IR
  // Probe on \总周期数 
  // Probe on \无条件分支数 
  // Probe on \条件分支成功数 
  // Probe on \插入气泡数 
  // Probe on \LoadUse次数 
  ROM #(.addrWidth(10), .dataWidth(32), .Select("high")) rom_1 (.addr(IF_PC[11:2]), .data(IF_IR));
  // Probe on IF_PC[11:0]
  // Probe on WB_PC[19:0]
  // RiscV_Probe riscv_probe_5: pin names not known; wires that end beside it: WB_IR
  IF_ID if_id_1 (.IF_PC(IF_PC), .IF_IR(IF_IR), .ID_PC(ID_PC), .ID_IR(ID_IR), .CLK(CLK), .halt(halt));  // open: Flush
  // Probe on ID_PC[11:0]
  // Probe on EX_PC[11:0]
  // RiscV_Probe riscv_probe_6: pin names not known; wires that end beside it: ID_IR
  // Probe on M_PC[11:0]
  D_Flip_Flop #(.trigger("high"), .Pre_Clr_Positions("LEGACY"), .NegatePresetClear("false"), .enable("true"), .NewFFLayout("false")) d_ff_1 (.Q(d_ff_1_q));  // open: clk, D, Qn, preset, en, reset
  // Probe on 13'hc
  Multiplexer #(.select(1), .width(5), .disabled("Z"), .enable("false")) multiplexer_2 (
    .in0(ID_IR[19:15]), .in1(5'b10001), .out(multiplexer_2_out), .sel(ID_ecall));
  Multiplexer #(.select(1), .width(5), .disabled("Z"), .enable("false")) multiplexer_3 (
    .in0(ID_IR[24:20]), .in1(5'b01010), .out(multiplexer_3_out), .sel(ID_ecall));
  Reg_Din reg_din_1 (
    .DM_Dout(DM_Dout), .PC(WB_PC), .CSR_out(CSR_out), .ALU_Res(WB_ALU_Res), .LH(WB_LH),
    .MemToReg(WB_MemToReg), .CSR(WB_CSR), .JAL(WB_JAL), .JALR(WB_JALR), .RDin(RDin));
  // Probe on WB_PC[11:0]
  Comparator #(.width(13), .mode("twosComplement")) comparator_1 (
    .a(CNT_num), .b(13'hc), .eq(comparator_1_eq), .lt(comparator_1_lt));  // open: gt
  Clock #(.highDuration(1), .lowDuration(1)) clock_1 (.out(clock_1_out));
  Regifile regifile_1 (
    .Din(RDin), .Clk(CLK), .R1(regifile_1_r1), .R2(regifile_1_r2), .WE(RegWrite), .W_num(WB_rd),
    .R1_num(multiplexer_2_out), .R2_num(multiplexer_3_out));
  nand nand_1 (nand_1_out, d_ff_1_q, comparator_1_eq);
  Counter #(.width(13), .max('h1fff), .ongoal("stay"), .trigger("rising"), .behavior("old")) counter_2 (
    .count(comparator_1_lt), .Q(CNT_num), .clk(clock_1_out));  // open: load, D, carry, clr, preset
  newcontrol newcontrol_1 (
    .out_4(newcontrol_1_out_4), .out_6(newcontrol_1_out_6), .out_8(newcontrol_1_out_8),
    .out_10(newcontrol_1_out_10), .out_12(newcontrol_1_out_12), .out_14(newcontrol_1_out_14),
    .in_1(ID_IR[21]), .in_2(ID_IR[6:2]), .in_3({ID_IR[30], ID_IR[25], ID_IR[14:12]}),
    .out_5(newcontrol_1_out_5), .out_7(newcontrol_1_out_7), .out_9(newcontrol_1_out_9),
    .out_11(newcontrol_1_out_11), .out_13(newcontrol_1_out_13), .out_15(newcontrol_1_out_15),
    .out_16(newcontrol_1_out_16), .out_17(newcontrol_1_out_17), .out_18(ID_ecall));
  assign CLK = nand_1_out ? clock_1_out : 1'bz;  // Controlled_Buffer controlled_buffer_1
  Pull_Resistor #(.pull(1)) pull_resistor_1 (.node(CLK));
  Register #(.width(32), .trigger("rising"), .Select("low")) register_1 (
    .D(WB_ALU_Res), .en(WB_CSR), .Q(register_1_q), .clk(CLK), .clr(RST));
  ID_EX id_ex_1 (
    .ID_PC(ID_PC), .ID_IR(ID_IR), .ID_rs1(ID_IR[19:15]), .ID_rd(ID_IR[11:7]), .ID_imm12(ID_IR[31:20]),
    .ID_imms({ID_IR[31:25], ID_IR[11:7]}), .ID_immb({ID_IR[31], ID_IR[7], ID_IR[30:25], ID_IR[11:8]}),
    .ID_immuj({ID_IR[31], ID_IR[19:12], ID_IR[20], ID_IR[30:21]}), .ID_Beq(newcontrol_1_out_5),
    .ID_Bne(newcontrol_1_out_7), .ID_MemToReg(newcontrol_1_out_9), .ID_MemWrite(newcontrol_1_out_11),
    .ID_ALUOP(newcontrol_1_out_13), .ID_ALUSrcB(newcontrol_1_out_15), .ID_RegWrite(newcontrol_1_out_16),
    .ID_S_type(newcontrol_1_out_17), .ID_JAL(newcontrol_1_out_4), .ID_JALR(newcontrol_1_out_6),
    .ID_URET(newcontrol_1_out_8), .ID_BLTU(newcontrol_1_out_10), .ID_CSR(newcontrol_1_out_12),
    .ID_LH(newcontrol_1_out_14), .ID_ecall(ID_ecall), .ID_Reg_R2(regifile_1_r2), .ID_CSR_out(register_1_q),
    .EX_PC(EX_PC), .EX_IR(EX_IR), .EX_rs1(EX_rs1), .EX_rd(id_ex_1_ex_rd), .EX_imm12(EX_imm12),
    .EX_imms(EX_imms), .EX_immb(immb), .EX_immuj(immuj), .EX_Beq(Beq), .EX_Bne(Bne),
    .EX_MemToReg(id_ex_1_ex_memtoreg), .EX_MemWrite(id_ex_1_ex_memwrite), .EX_ALUOP(id_ex_1_ex_aluop),
    .EX_ALUSrcB(id_ex_1_ex_alusrcb), .EX_RegWrite(id_ex_1_ex_regwrite), .EX_S_type(id_ex_1_ex_s_type),
    .EX_JAL(JAL), .EX_JALR(JALR), .EX_URET(URET), .EX_BLTU(BLTU), .EX_CSR(EX_CSR), .EX_LH(id_ex_1_ex_lh),
    .EX_ecall(EX_ecall), .EX_Reg_R2(EX_Reg_R2), .EX_CSR_out(EX_CSR_out), .CLK(CLK),
    .ID_Reg_R1(regifile_1_r1), .EX_Reg_R1(EX_Reg_R1), .halt(halt));  // open: Flush, Rt_MEM_2, Rs_MEM_2, Rs_WB_2, Rt_WB_2, Rt_MEM, Rs_MEM, Rs_WB, Rt_WB
  Multiplexer #(.select(1), .width(32), .disabled("Z"), .enable("false")) multiplexer_4 (
    .in0(EX_Reg_R1), .in1(EX_CSR_out), .out(multiplexer_4_out), .sel(EX_CSR));
  ALU_Bin alu_bin_1 (
    .Reg_R2(EX_Reg_R2), .immb(EX_imm12), .rs1(EX_rs1), .imms(EX_imms), .CSR(EX_CSR),
    .S_type(id_ex_1_ex_s_type), .AluSrcB(id_ex_1_ex_alusrcb), .ALU_Bin(alu_bin_1_alu_bin));
  Comparator #(.width(32), .mode("twosComplement")) comparator_2 (
    .a(32'h22), .b(EX_Reg_R1), .eq(comparator_2_eq));  // open: gt, lt
  ALU alu_1 (
    .X(multiplexer_4_out), .Y(alu_bin_1_alu_bin), .AluOP(id_ex_1_ex_aluop), .Equal(Equal),
    .Result(EX_ALU_Res), .out_4(GE));  // open: Result_2, out_6
  not not_3 (not_3_out, comparator_2_eq);
  Register #(.width(1), .trigger("rising"), .Select("low")) register_2 (
    .D(not_3_out), .en(EX_ecall), .Q(register_2_q), .clk(CLK), .clr(Go));
  Register #(.width(32), .trigger("rising"), .Select("low")) register_3 (
    .D(EX_Reg_R2), .en(comparator_2_eq), .Q(LedData), .clk(CLK), .clr(RST));
  EX_MEM ex_mem_1 (
    .EX_PC(EX_PC), .EX_IR(EX_IR), .EX_rd(id_ex_1_ex_rd), .ID_MemToReg(id_ex_1_ex_memtoreg),
    .ID_MemWrite(id_ex_1_ex_memwrite), .ID_RegWrite(id_ex_1_ex_regwrite), .ID_CSR(EX_CSR),
    .ID_LH(id_ex_1_ex_lh), .EX_Reg_R2(EX_Reg_R2), .EX_ALU_Res(EX_ALU_Res), .MEM_PC(M_PC), .MEM_IR(MEM_IR),
    .MEM_rd(ex_mem_1_mem_rd), .EX_MemToReg(ex_mem_1_ex_memtoreg), .EX_MemWrite(MemWrite),
    .EX_RegWrite(ex_mem_1_ex_regwrite), .EX_CSR(ex_mem_1_ex_csr), .EX_LH(ex_mem_1_ex_lh), .MEM_Reg_R2(MDin),
    .MEM_ALU_Res(ex_mem_1_mem_alu_res), .CLK(CLK), .halt(halt), .ID_JALR(JALR), .EX_JALR(ex_mem_1_ex_jalr),
    .ID_JAL(JAL), .EX_JAL(ex_mem_1_ex_jal), .EX_CSR_out(EX_CSR_out), .MEM_CSR_out(ex_mem_1_mem_csr_out),
    .EX_halt(register_2_q), .MEM_halt(ex_mem_1_mem_halt));  // open: Flush
  not not_4 (not_4_out, MemWrite);
  RAM #(.addrWidth(10), .dataWidth(32), .bus("separate"), .Select("high")) ram_1 (
    .addr(ex_mem_1_mem_alu_res[11:2]), .din(MDin), .data(ram_1_data), .str(MemWrite), .clk(CLK),
    .ld(not_4_out), .clr(RST));  // open: sel
  MEM_WB mem_wb_1 (
    .MEM_PC(M_PC), .MEM_IR(MEM_IR), .MEM_rd(ex_mem_1_mem_rd), .ID_MemToReg(ex_mem_1_ex_memtoreg),
    .ID_RegWrite(ex_mem_1_ex_regwrite), .ID_JAL(ex_mem_1_ex_jal), .ID_JALR(ex_mem_1_ex_jalr),
    .ID_CSR(ex_mem_1_ex_csr), .ID_LH(ex_mem_1_ex_lh), .MEM_ALU_Res(ex_mem_1_mem_alu_res), .WB_PC(WB_PC),
    .WB_IR(WB_IR), .WB_rd(WB_rd), .EX_MemToReg(WB_MemToReg), .EX_RegWrite(RegWrite), .EX_JAL(WB_JAL),
    .EX_JALR(WB_JALR), .EX_CSR(WB_CSR), .EX_LH(WB_LH), .WB_ALU_Res(WB_ALU_Res), .in_15(halt), .in_16(CLK),
    .MEM_DM_Dput(ram_1_data), .WB_DM_Dout(DM_Dout), .MEM_CSR_out(ex_mem_1_mem_csr_out), .WB_CSR_out(CSR_out),
    .MEM_halt(ex_mem_1_mem_halt), .WB_halt(halt));  // open: Flush

  // Other names for the same wires on the sheet: rd[4:0] = ID_IR[11:7]; ID_rs2[4:0] = ID_IR[24:20];
  //   ID_rs1[4:0] = ID_IR[19:15]; MEM_PC[31:0] = M_PC

  // Notes on the sheet:
  //   中断源
  //   时空图监测，可删除
  //   中断等待指示
  //   数码管输出
  //   指令存储器
  //   指令字
  //   contents of rom_1 (hex, n*v repeats v):
  //   413 493 913 993 46413 14e493 296913 39e993 842023 942223 1242423 1342623 a00893 493 913 993 73
  //   控制位
  //   指令探针
  //   流水调试日志用
  //   暂停节拍，不能为0
  //   用这个时钟源需要去掉电路中的其他时钟源
  //   戳工具置1进入计数暂停模式，ctrl+k时钟自动运行到对应节拍暂停
  //   ctrl+k关闭时钟连续运行，将控制位置零，进入单步调试模式调试
  //   可计数暂停的时钟源
  //   为方便自动评测，需要输出流水线各段保存的PC值，注意是PC不是PC+4，另外ID段寄存器写入信息，Mem段内存写入信息也要输出
  //   数据存储器
endmodule

module \气泡流水线  (
  output RegWrite,
  output MemWrite,
  output [31:0] IF_PC,
  output [31:0] ID_PC,
  output [31:0] EX_PC,
  output [31:0] M_PC,
  output [31:0] WB_PC,
  output [31:0] RDin,
  output [31:0] MDin,
  output [31:0] LedData
);

  wire and_1_out, and_2_out, and_3_out, and_4_out, and_5_out, and_6_out, Beq, BLTU, Bne, CLK, clock_1_out,
       comparator_1_eq, comparator_1_lt, comparator_2_eq, d_ff_1_q, DataHazzard, Equal, EX_CSR, EX_ecall,
       ex_mem_1_ex_csr, ex_mem_1_ex_jal, ex_mem_1_ex_jalr, ex_mem_1_ex_lh, ex_mem_1_ex_memtoreg,
       ex_mem_1_mem_halt, EX_RegWrite, Flush, GE, Go, halt, ID_ecall, id_ex_1_ex_alusrcb, id_ex_1_ex_lh,
       id_ex_1_ex_memtoreg, id_ex_1_ex_memwrite, id_ex_1_ex_s_type, id_ex_1_rs_wb_2, IR1, IR2, IR3, JAL,
       JALR, MEM_RegWrite, multiplexer_2_out, multiplexer_3_out, nand_1_out, newcontrol_1_out_4,
       newcontrol_1_out_5, newcontrol_1_out_6, newcontrol_1_out_7, newcontrol_1_out_8, newcontrol_1_out_9,
       newcontrol_1_out_10, newcontrol_1_out_11, newcontrol_1_out_12, newcontrol_1_out_14,
       newcontrol_1_out_15, newcontrol_1_out_16, newcontrol_1_out_17, not_1_out, not_2_out, not_3_out,
       not_5_out, not_6_out, not_7_out, not_8_out, not_9_out, not_10_out, not_11_out, or_1_out, or_2_out,
       or_3_out, or_4_out, register_2_q, RST, URET, W1, W2, W3, WB_CSR, WB_JAL, WB_JALR, WB_LH, WB_MemToReg,
       whichpc_1_out_9;
  wire [1:0] undriven;
  wire [3:0] id_ex_1_ex_aluop, newcontrol_1_out_13;
  wire [4:0] EX_rd, EX_rs1, MEM_rd, rrs1, rrs2, WB_rd;
  wire [11:0] EX_imm12, EX_imms, immb;
  wire [12:0] CNT_num;
  wire [15:0] \LoadUse次数 , \总周期数 , \插入气泡数 , \无条件分支数 , \条件分支成功数 ;
  wire [19:0] immuj;
  wire [31:0] alu_bin_1_alu_bin, CSR_out, DM_Dout, EX_ALU_Res, EX_CSR_out, EX_IR, ex_mem_1_mem_alu_res,
       ex_mem_1_mem_csr_out, EX_Reg_R1, EX_Reg_R2, ID_IR, IF_IR, MEM_IR, multiplexer_1_out,
       multiplexer_6_out, pc_in_1_pc_2, ram_1_data, regifile_1_r1, regifile_1_r2, register_1_q, WB_ALU_Res,
       WB_IR;

  Button \u_总复位  (.out(RST));
  Button _1 (.out(IR1));
  Button _2 (.out(IR2));
  Button _3 (.out(IR3));
  // Probe on \总周期数 
  // Probe on \总周期数 
  Button \u_继续运行  (.out(Go));
  LED #(.active("true")) led_1 (.in(W1));
  LED #(.active("true")) led_2 (.in(W2));
  LED #(.active("true")) led_3 (.in(W3));
  not not_1 (not_1_out, halt);
  or or_1 (or_1_out, JALR, JAL);
  not not_2 (not_2_out, halt);
  or or_2 (or_2_out, Flush, DataHazzard);
  Hex_Digit_Display hex_digit_display_1 (.value(LedData[31:28]));  // open: dp
  // Probe on IF_PC[19:0]
  // RiscV_Probe riscv_probe_1: pin names not known; wires that end beside it: IF_IR
  Counter #(.width(16), .max('hffff), .ongoal("wrap"), .trigger("rising"), .behavior("new")) counter_1 (
    .count(not_1_out), .Q(\总周期数 ), .clk(CLK), .clr(RST));  // open: load, D, carry, preset, down
  Counter #(.width(16), .max('hffff), .ongoal("wrap"), .trigger("rising"), .behavior("new")) counter_2 (
    .count(1'b0), .Q(\LoadUse次数 ), .clk(CLK), .clr(RST));  // open: load, D, carry, preset, down
  or or_3 (or_3_out, JALR, JAL);
  Counter #(.width(16), .max('hffff), .ongoal("wrap"), .trigger("rising"), .behavior("new")) counter_3 (
    .count(or_3_out), .Q(\无条件分支数 ), .clk(CLK), .clr(RST));  // open: load, D, carry, preset, down
  and and_1 (and_1_out, Flush, not_3_out);
  not not_3 (not_3_out, or_1_out);
  and and_2 (and_2_out, not_2_out, or_2_out);
  Counter #(.width(16), .max('hffff), .ongoal("wrap"), .trigger("rising"), .behavior("new")) counter_4 (
    .count(and_2_out), .Q(\插入气泡数 ), .clk(CLK), .clr(RST));  // open: load, D, carry, preset, down
  Hex_Digit_Display hex_digit_display_2 (.value(LedData[27:24]));  // open: dp
  Hex_Digit_Display hex_digit_display_3 (.value(LedData[23:20]));  // open: dp
  // Probe on ID_PC[19:0]
  // RiscV_Probe riscv_probe_2: pin names not known; wires that end beside it: ID_IR
  Counter #(.width(16), .max('hffff), .ongoal("wrap"), .trigger("rising"), .behavior("new")) counter_5 (
    .count(and_1_out), .Q(\条件分支成功数 ), .clk(CLK), .clr(RST));  // open: load, D, carry, preset, down
  Hex_Digit_Display hex_digit_display_4 (.value(LedData[15:12]));  // open: dp
  Hex_Digit_Display hex_digit_display_5 (.value(LedData[19:16]));  // open: dp
  WhichPC whichpc_1 (
    .out_9(whichpc_1_out_9), .GE(GE), .BLTU(BLTU), .URET(URET), .JALR(JALR), .JAL(JAL), .Beq(Beq), .Bne(Bne),
    .Equal(Equal));
  not not_4 (Flush, whichpc_1_out_9);
  Multiplexer #(.select(1), .width(32), .disabled("Z"), .enable("false")) multiplexer_1 (
    .in0(EX_PC), .in1(IF_PC), .out(multiplexer_1_out), .sel(whichpc_1_out_9));
  Hex_Digit_Display hex_digit_display_6 (.value(LedData[11:8]));  // open: dp
  Hex_Digit_Display hex_digit_display_7 (.value(LedData[7:4]));  // open: dp
  // Probe on EX_PC[19:0]
  // RiscV_Probe riscv_probe_3: pin names not known; wires that end beside it: EX_IR
  Hex_Digit_Display hex_digit_display_8 (.value(LedData[3:0]));  // open: dp
  PC_in pc_in_1 (
    .PC(multiplexer_1_out), .immb(immb), .immuj(immuj), .ALU_Res(EX_ALU_Res), .\中断编号 (undriven), .GE(GE),
    .BLTU(BLTU), .URET(URET), .JALR(JALR), .JAL(JAL), .Beq(Beq), .Bne(Bne), .Equal(Equal), .\中断触发 (1'b0),
    .PC_2(pc_in_1_pc_2));  // open: EPC
  not not_5 (not_5_out, multiplexer_2_out);
  Multiplexer #(.select(1), .width(1), .disabled("Z"), .enable("false")) multiplexer_2 (
    .in0(and_3_out), .in1(halt), .out(multiplexer_2_out), .sel(halt));
  and and_3 (and_3_out, not_6_out, DataHazzard);
  not not_6 (not_6_out, Flush);
  // Probe on \总周期数 
  // Probe on M_PC[19:0]
  // RiscV_Probe riscv_probe_4: pin names not known; wires that end beside it: MEM_IR
  Register #(.width(32), .trigger("rising"), .Select("low")) PC (
    .D(pc_in_1_pc_2), .en(not_5_out), .Q(IF_PC), .clk(CLK), .clr(RST));
  // Probe on \总周期数 
  // Probe on \无条件分支数 
  // Probe on \条件分支成功数 
  // Probe on \插入气泡数 
  // Probe on \LoadUse次数 
  // Probe on IF_PC[11:0]
  // Probe on WB_PC[19:0]
  // RiscV_Probe riscv_probe_5: pin names not known; wires that end beside it: WB_IR
  // Probe on EX_PC[11:0]
  // Probe on ID_PC[11:0]
  ROM #(.addrWidth(10), .dataWidth(32), .Select("high")) rom_1 (.addr(IF_PC[11:2]), .data(IF_IR));
  // Probe on M_PC[11:0]
  D_Flip_Flop #(.trigger("high"), .Pre_Clr_Positions("LEGACY"), .NegatePresetClear("false"), .enable("true"), .NewFFLayout("false")) d_ff_1 (.Q(d_ff_1_q));  // open: clk, D, Qn, preset, en, reset
  // Probe on 13'he00
  IF_ID if_id_1 (
    .IF_PC(IF_PC), .IF_IR(IF_IR), .ID_PC(ID_PC), .ID_IR(ID_IR), .CLK(CLK), .halt(multiplexer_3_out),
    .Flush(Flush));
  Multiplexer #(.select(1), .width(1), .disabled("Z"), .enable("false")) multiplexer_3 (
    .in0(and_4_out), .in1(halt), .out(multiplexer_3_out), .sel(halt));
  and and_4 (and_4_out, not_7_out, DataHazzard);
  not not_7 (not_7_out, Flush);
  // Probe on WB_PC[11:0]
  Comparator #(.width(13), .mode("twosComplement")) comparator_1 (
    .a(CNT_num), .b(13'he00), .eq(comparator_1_eq), .lt(comparator_1_lt));  // open: gt
  Clock #(.highDuration(1), .lowDuration(1)) clock_1 (.out(clock_1_out));
  // RiscV_Probe riscv_probe_6: pin names not known; wires that end beside it: ID_IR
  Multiplexer #(.select(1), .width(5), .disabled("Z"), .enable("false")) multiplexer_4 (
    .in0(ID_IR[19:15]), .in1(5'b10001), .out(rrs1), .sel(ID_ecall));
  Multiplexer #(.select(1), .width(5), .disabled("Z"), .enable("false")) multiplexer_5 (
    .in0(ID_IR[24:20]), .in1(5'b01010), .out(rrs2), .sel(ID_ecall));
  nand nand_1 (nand_1_out, d_ff_1_q, comparator_1_eq);
  Counter #(.width(13), .max('h1fff), .ongoal("stay"), .trigger("rising"), .behavior("old")) counter_6 (
    .count(comparator_1_lt), .Q(CNT_num), .clk(clock_1_out));  // open: load, D, carry, clr, preset
  Reg_Din reg_din_1 (
    .DM_Dout(DM_Dout), .PC(WB_PC), .CSR_out(CSR_out), .ALU_Res(WB_ALU_Res), .LH(WB_LH),
    .MemToReg(WB_MemToReg), .CSR(WB_CSR), .JAL(WB_JAL), .JALR(WB_JALR), .RDin(RDin));
  assign CLK = nand_1_out ? clock_1_out : 1'bz;  // Controlled_Buffer controlled_buffer_1
  Regifile regifile_1 (
    .Din(RDin), .Clk(CLK), .R1(regifile_1_r1), .R2(regifile_1_r2), .WE(RegWrite), .W_num(WB_rd),
    .R1_num(rrs1), .R2_num(rrs2));
  Pull_Resistor #(.pull(1)) pull_resistor_1 (.node(CLK));
  newcontrol newcontrol_1 (
    .out_4(newcontrol_1_out_4), .out_6(newcontrol_1_out_6), .out_8(newcontrol_1_out_8),
    .out_10(newcontrol_1_out_10), .out_12(newcontrol_1_out_12), .out_14(newcontrol_1_out_14),
    .in_1(ID_IR[21]), .in_2(ID_IR[6:2]), .in_3({ID_IR[30], ID_IR[25], ID_IR[14:12]}),
    .out_5(newcontrol_1_out_5), .out_7(newcontrol_1_out_7), .out_9(newcontrol_1_out_9),
    .out_11(newcontrol_1_out_11), .out_13(newcontrol_1_out_13), .out_15(newcontrol_1_out_15),
    .out_16(newcontrol_1_out_16), .out_17(newcontrol_1_out_17), .out_18(ID_ecall));
  Register #(.width(32), .trigger("rising"), .Select("low")) register_1 (
    .D(WB_ALU_Res), .en(WB_CSR), .Q(register_1_q), .clk(CLK), .clr(RST));
  DataHazzard datahazzard_1 (
    .ERegwrite(EX_RegWrite), .IDrs1(rrs1), .Erd(EX_rd), .IDrs2(rrs2), .MRegWrite(MEM_RegWrite), .Mrd(MEM_rd),
    .DataHazzard(DataHazzard), .OPcode(ID_IR[6:2]), .ID_ecall(ID_ecall));
  ID_EX id_ex_1 (
    .ID_PC(ID_PC), .ID_IR(ID_IR), .ID_rs1(ID_IR[19:15]), .ID_rd(ID_IR[11:7]), .ID_imm12(ID_IR[31:20]),
    .ID_imms({ID_IR[31:25], ID_IR[11:7]}), .ID_immb({ID_IR[31], ID_IR[7], ID_IR[30:25], ID_IR[11:8]}),
    .ID_immuj({ID_IR[31], ID_IR[19:12], ID_IR[20], ID_IR[30:21]}), .ID_Beq(newcontrol_1_out_5),
    .ID_Bne(newcontrol_1_out_7), .ID_MemToReg(newcontrol_1_out_9), .ID_MemWrite(newcontrol_1_out_11),
    .ID_ALUOP(newcontrol_1_out_13), .ID_ALUSrcB(newcontrol_1_out_15), .ID_RegWrite(newcontrol_1_out_16),
    .ID_S_type(newcontrol_1_out_17), .ID_JAL(newcontrol_1_out_4), .ID_JALR(newcontrol_1_out_6),
    .ID_URET(newcontrol_1_out_8), .ID_BLTU(newcontrol_1_out_10), .ID_CSR(newcontrol_1_out_12),
    .ID_LH(newcontrol_1_out_14), .ID_ecall(ID_ecall), .ID_Reg_R2(regifile_1_r2), .ID_CSR_out(register_1_q),
    .EX_PC(EX_PC), .EX_IR(EX_IR), .EX_rs1(EX_rs1), .EX_rd(EX_rd), .EX_imm12(EX_imm12), .EX_imms(EX_imms),
    .EX_immb(immb), .EX_immuj(immuj), .EX_Beq(Beq), .EX_Bne(Bne), .EX_MemToReg(id_ex_1_ex_memtoreg),
    .EX_MemWrite(id_ex_1_ex_memwrite), .EX_ALUOP(id_ex_1_ex_aluop), .EX_ALUSrcB(id_ex_1_ex_alusrcb),
    .EX_RegWrite(EX_RegWrite), .EX_S_type(id_ex_1_ex_s_type), .EX_JAL(JAL), .EX_JALR(JALR), .EX_URET(URET),
    .EX_BLTU(BLTU), .EX_CSR(EX_CSR), .EX_LH(id_ex_1_ex_lh), .EX_ecall(EX_ecall), .EX_Reg_R2(EX_Reg_R2),
    .EX_CSR_out(EX_CSR_out), .CLK(CLK), .ID_Reg_R1(regifile_1_r1), .EX_Reg_R1(EX_Reg_R1), .halt(halt),
    .Flush(or_4_out), .Rs_WB_2(id_ex_1_rs_wb_2));  // open: Rt_MEM_2, Rs_MEM_2, Rt_WB_2, Rt_MEM, Rs_MEM, Rs_WB, Rt_WB
  or or_4 (or_4_out, Flush, DataHazzard);
  Multiplexer #(.select(1), .width(32), .disabled("Z"), .enable("false")) multiplexer_6 (
    .in0(EX_Reg_R1), .in1(EX_CSR_out), .out(multiplexer_6_out), .sel(EX_CSR));
  ALU_Bin alu_bin_1 (
    .Reg_R2(EX_Reg_R2), .immb(EX_imm12), .rs1(EX_rs1), .imms(EX_imms), .CSR(EX_CSR),
    .S_type(id_ex_1_ex_s_type), .AluSrcB(id_ex_1_ex_alusrcb), .ALU_Bin(alu_bin_1_alu_bin));
  ALU alu_1 (
    .X(multiplexer_6_out), .Y(alu_bin_1_alu_bin), .AluOP(id_ex_1_ex_aluop), .Equal(Equal),
    .Result(EX_ALU_Res), .out_4(GE));  // open: Result_2, out_6
  not not_8 (not_8_out, comparator_2_eq);
  Comparator #(.width(32), .mode("twosComplement")) comparator_2 (
    .a(32'h22), .b(EX_Reg_R1), .eq(comparator_2_eq));  // open: gt, lt
  Register #(.width(1), .trigger("rising"), .Select("low")) register_2 (
    .D(not_8_out), .en(EX_ecall), .Q(register_2_q), .clk(CLK), .clr(Go));
  Register #(.width(32), .trigger("rising"), .Select("low")) register_3 (
    .D(EX_Reg_R2), .en(comparator_2_eq), .Q(LedData), .clk(CLK), .clr(RST));
  EX_MEM ex_mem_1 (
    .EX_PC(EX_PC), .EX_IR(EX_IR), .EX_rd(EX_rd), .ID_MemToReg(id_ex_1_ex_memtoreg),
    .ID_MemWrite(id_ex_1_ex_memwrite), .ID_RegWrite(EX_RegWrite), .ID_CSR(EX_CSR), .ID_LH(id_ex_1_ex_lh),
    .EX_Reg_R2(EX_Reg_R2), .EX_ALU_Res(EX_ALU_Res), .MEM_PC(M_PC), .MEM_IR(MEM_IR), .MEM_rd(MEM_rd),
    .EX_MemToReg(ex_mem_1_ex_memtoreg), .EX_MemWrite(MemWrite), .EX_RegWrite(MEM_RegWrite),
    .EX_CSR(ex_mem_1_ex_csr), .EX_LH(ex_mem_1_ex_lh), .MEM_Reg_R2(MDin), .MEM_ALU_Res(ex_mem_1_mem_alu_res),
    .CLK(CLK), .halt(and_5_out), .ID_JALR(JALR), .EX_JALR(ex_mem_1_ex_jalr), .ID_JAL(JAL),
    .EX_JAL(ex_mem_1_ex_jal), .EX_CSR_out(EX_CSR_out), .MEM_CSR_out(ex_mem_1_mem_csr_out),
    .EX_halt(register_2_q), .MEM_halt(ex_mem_1_mem_halt));  // open: Flush
  and and_5 (and_5_out, not_9_out, halt);
  not not_9 (not_9_out, Go);
  not not_10 (not_10_out, MemWrite);
  RAM #(.addrWidth(10), .dataWidth(32), .bus("separate"), .Select("high")) ram_1 (
    .addr(ex_mem_1_mem_alu_res[11:2]), .din(MDin), .data(ram_1_data), .str(MemWrite), .clk(CLK),
    .ld(not_10_out), .clr(RST));  // open: sel
  MEM_WB mem_wb_1 (
    .MEM_PC(M_PC), .MEM_IR(MEM_IR), .MEM_rd(MEM_rd), .ID_MemToReg(ex_mem_1_ex_memtoreg),
    .ID_RegWrite(MEM_RegWrite), .ID_JAL(ex_mem_1_ex_jal), .ID_JALR(ex_mem_1_ex_jalr),
    .ID_CSR(ex_mem_1_ex_csr), .ID_LH(ex_mem_1_ex_lh), .MEM_ALU_Res(ex_mem_1_mem_alu_res), .WB_PC(WB_PC),
    .WB_IR(WB_IR), .WB_rd(WB_rd), .EX_MemToReg(WB_MemToReg), .EX_RegWrite(RegWrite), .EX_JAL(WB_JAL),
    .EX_JALR(WB_JALR), .EX_CSR(WB_CSR), .EX_LH(WB_LH), .WB_ALU_Res(WB_ALU_Res), .in_15(and_6_out),
    .in_16(CLK), .MEM_DM_Dput(ram_1_data), .WB_DM_Dout(DM_Dout), .MEM_CSR_out(ex_mem_1_mem_csr_out),
    .WB_CSR_out(CSR_out), .MEM_halt(ex_mem_1_mem_halt), .WB_halt(halt));  // open: Flush
  and and_6 (and_6_out, not_11_out, halt);
  not not_11 (not_11_out, Go);

  // Other names for the same wires on the sheet: rd[4:0] = ID_IR[11:7]; ID_rs2[4:0] = ID_IR[24:20];
  //   ID_rs1[4:0] = ID_IR[19:15]; ID_OPcode[4:0] = ID_IR[6:2]; MEM_PC[31:0] = M_PC

  // Notes on the sheet:
  //   中断源
  //   时空图监测，可删除
  //   中断等待指示
  //   数码管输出
  //   指令存储器
  //   控制位
  //   指令字
  //   contents of rom_1 (hex, n*v repeats v):
  //   100493 100006f 100493 200913 300993 100006f 100493 200913 300993 100006f 100493 200913 300993
  //   100006f 100493 200913 300993 3d8000ef 100413 100493 1f49493 900533 2200893 73 24d493 48463 fedff06f
  //   900533 2200893 73 100493 249493 900533 2200893 73 48463 fedff06f 100493 1f49493 900533 2200893 73
  //   4034d493 900533 2200893 73 4044d493 900533 2200893 73 4044d493 900533 2200893 73 4044d493 900533
  //   2200893 73 4044d493 900533 2200893 73 4044d493 900533 2200893 73 4044d493 900533 2200893 73 4044d493
  //   900533 2200893 73 100413 1f41993 41f9d993 433 c00913 300b13 140413 f47413 800293 100313 499993
  //   89e9b3 1300533 2200893 73 406282b3 fe0294e3 140413 f00f93 1f47433 1c41413 800293 100313 49d993
  //   89e9b3 1300533 2200893 73 406282b3 fe0294e3 1c45413 406b0b33 b0463 f95ff06f 2b3 fff2c293 829293
  //   ff2e293 500533 2200893 73 fff00413 493 84a023 140413 448493 84a023 140413 448493 84a023 140413
  //   448493 84a023 140413 448493 84a023 140413 448493 84a023 140413 448493 84a023 140413 448493 84a023
  //   140413 448493 84a023 140413 448493 84a023 140413 448493 84a023 140413 448493 84a023 140413 448493
  //   84a023 140413 448493 84a023 140413 448493 84a023 140413 448493 84a023 140413 448493 140413 433
  //   3c00493 42983 4aa03 149a2b3 28663 134a023 1442023 ffc48493 fe9412e3 800533 2200893 73 440413 3c00493
  //   fc9416e3 3200893 73 100293 300313 800493 849493 7648493 900533 2200893 73 800e13 5494b3 6494b3
  //   900533 2200893 73 fffe0e13 fe0e14e3 a00893 73 fff00293 7700493 849493 7748493 900533 2200893 73
  //   1000e13 54c4b3 900533 2200893 73 fffe0e13 fe0e16e3 a00893 73 313 1000e13 8400493 849493 8348493
  //   400913 891913 490913 849493 8248493 849493 8148493 891913 490913 891913 490913 932023 12484b3 430313
  //   fffe0e13 fe0e18e3 2000e13 313 31483 900533 2200893 73 230313 fffe0e13 fe0e14e3 a00893 73 ff100493
  //   900533 2200893 73 148493 fe9068e3 900533 2200893 73 a00893 73 a00893 73 413 140413 800533 2200893 73
  //   240413 800533 2200893 73 340413 800533 2200893 73 440413 800533 2200893 73 540413 800533 2200893 73
  //   640413 800533 2200893 73 740413 800533 2200893 73 840413 800533 2200893 2200893 73 8067
  //   流水调试日志用
  //   暂停节拍，不能为0
  //   戳工具置1进入计数暂停模式，ctrl+k时钟自动运行到对应节拍暂停
  //   ctrl+k关闭时钟连续运行，将控制位置零，进入单步调试模式调试
  //   指令探针
  //   可计数暂停的时钟源
  //   为方便自动评测，需要输出流水线各段保存的PC值，注意是PC不是PC+4，另外ID段寄存器写入信息，Mem段内存写入信息也要输出
  //   数据存储器
endmodule

module \重定向流水线  (
  output RegWrite,
  output MemWrite,
  output [31:0] IF_PC,
  output [31:0] ID_PC,
  output [31:0] EX_PC,
  output [31:0] M_PC,
  output [31:0] WB_PC,
  output [31:0] RDin,
  output [31:0] MDin,
  output [31:0] LedData
);

  wire and_1_out, and_2_out, and_3_out, and_4_out, and_5_out, and_6_out, and_7_out, Beq, BLTU, Bne, CLK,
       clock_1_out, comparator_1_eq, comparator_1_lt, comparator_2_eq, d_ff_1_q, Equal, EX_CSR, EX_ecall,
       ex_mem_1_ex_csr, ex_mem_1_ex_jal, ex_mem_1_ex_jalr, ex_mem_1_ex_lh, ex_mem_1_ex_memtoreg,
       ex_mem_1_mem_halt, EX_MemToReg, EX_RegWrite, Flush, GE, Go, halt, ID_ecall, id_ex_1_ex_alusrcb,
       id_ex_1_ex_lh, id_ex_1_ex_memwrite, id_ex_1_ex_s_type, IR1, IR2, IR3, JAL, JALR, Load_Use,
       MEM_RegWrite, multiplexer_2_out, multiplexer_3_out, nand_1_out, newcontrol_1_out_4,
       newcontrol_1_out_5, newcontrol_1_out_6, newcontrol_1_out_7, newcontrol_1_out_8, newcontrol_1_out_9,
       newcontrol_1_out_10, newcontrol_1_out_11, newcontrol_1_out_12, newcontrol_1_out_14,
       newcontrol_1_out_15, newcontrol_1_out_16, newcontrol_1_out_17, not_1_out, not_2_out, not_4_out,
       not_5_out, not_6_out, not_7_out, not_8_out, not_9_out, not_10_out, not_11_out, not_12_out, or_1_out,
       or_2_out, or_3_out, or_4_out, redirect_1_rs_mem, redirect_1_rs_wb, redirect_1_rt_mem,
       redirect_1_rt_wb, register_2_q, Rs_MEM, Rs_WB, RST, Rt_MEM, Rt_WB, URET, W1, W2, W3, WB_CSR, WB_JAL,
       WB_JALR, WB_LH, WB_MemToReg, whichpc_1_out_9;
  wire [1:0] undriven;
  wire [3:0] id_ex_1_ex_aluop, newcontrol_1_out_13;
  wire [4:0] EX_rd, EX_rs1, MEM_rd, rrs1, rrs2, WB_rd;
  wire [11:0] EX_imm12, EX_imms, immb;
  wire [12:0] CNT_num;
  wire [15:0] \LoadUse次数 , \总周期数 , \插入气泡数 , \无条件分支数 , \条件分支成功数 ;
  wire [19:0] immuj;
  wire [31:0] alu_bin_1_alu_bin, CSR_out, DM_Dout, EX_ALU_Res, EX_CSR_out, EX_IR, ex_mem_1_mem_csr_out,
       EX_Reg_R1, EX_Reg_R2, ID_CSR_out, ID_IR, ID_Reg_R1, IF_IR, MEM_ALU_Res, MEM_IR, multiplexer_1_out,
       multiplexer_6_out, multiplexer_7_out, multiplexer_8_out, pc_in_1_pc_2, ram_1_data, redirect_Reg_R1,
       redirect_Reg_R2, regifile_1_r2, WB_ALU_Res, WB_IR;

  Button \u_总复位  (.out(RST));
  Button _1 (.out(IR1));
  Button _2 (.out(IR2));
  Button _3 (.out(IR3));
  // Probe on \总周期数 
  // Probe on \总周期数 
  Button \u_继续运行  (.out(Go));
  LED #(.active("true")) led_1 (.in(W1));
  LED #(.active("true")) led_2 (.in(W2));
  LED #(.active("true")) led_3 (.in(W3));
  not not_1 (not_1_out, halt);
  or or_1 (or_1_out, JALR, JAL);
  or or_2 (or_2_out, Flush, Load_Use);
  Hex_Digit_Display hex_digit_display_1 (.value(LedData[31:28]));  // open: dp
  // Probe on IF_PC[19:0]
  // RiscV_Probe riscv_probe_1: pin names not known; wires that end beside it: IF_IR
  Counter #(.width(16), .max('hffff), .ongoal("wrap"), .trigger("rising"), .behavior("new")) counter_1 (
    .count(not_1_out), .Q(\总周期数 ), .clk(CLK), .clr(RST));  // open: load, D, carry, preset, down
  Counter #(.width(16), .max('hffff), .ongoal("wrap"), .trigger("rising"), .behavior("new")) counter_2 (
    .count(Load_Use), .Q(\LoadUse次数 ), .clk(CLK), .clr(RST));  // open: load, D, carry, preset, down
  or or_3 (or_3_out, JALR, JAL);
  Counter #(.width(16), .max('hffff), .ongoal("wrap"), .trigger("rising"), .behavior("new")) counter_3 (
    .count(or_3_out), .Q(\无条件分支数 ), .clk(CLK), .clr(RST));  // open: load, D, carry, preset, down
  and and_1 (and_1_out, Flush, not_2_out);
  not not_2 (not_2_out, or_1_out);
  Counter #(.width(16), .max('hffff), .ongoal("wrap"), .trigger("rising"), .behavior("new")) counter_4 (
    .count(or_2_out), .Q(\插入气泡数 ), .clk(CLK), .clr(RST));  // open: load, D, carry, preset, down
  Hex_Digit_Display hex_digit_display_2 (.value(LedData[27:24]));  // open: dp
  Hex_Digit_Display hex_digit_display_3 (.value(LedData[23:20]));  // open: dp
  // Probe on ID_PC[19:0]
  // RiscV_Probe riscv_probe_2: pin names not known; wires that end beside it: ID_IR
  WhichPC whichpc_1 (
    .out_9(whichpc_1_out_9), .GE(GE), .BLTU(BLTU), .URET(URET), .JALR(JALR), .JAL(JAL), .Beq(Beq), .Bne(Bne),
    .Equal(Equal));
  not not_3 (Flush, whichpc_1_out_9);
  Counter #(.width(16), .max('hffff), .ongoal("wrap"), .trigger("rising"), .behavior("new")) counter_5 (
    .count(and_1_out), .Q(\条件分支成功数 ), .clk(CLK), .clr(RST));  // open: load, D, carry, preset, down
  Hex_Digit_Display hex_digit_display_4 (.value(LedData[15:12]));  // open: dp
  Hex_Digit_Display hex_digit_display_5 (.value(LedData[19:16]));  // open: dp
  Multiplexer #(.select(1), .width(32), .disabled("Z"), .enable("false")) multiplexer_1 (
    .in0(EX_PC), .in1(IF_PC), .out(multiplexer_1_out), .sel(whichpc_1_out_9));
  Hex_Digit_Display hex_digit_display_6 (.value(LedData[11:8]));  // open: dp
  Hex_Digit_Display hex_digit_display_7 (.value(LedData[7:4]));  // open: dp
  // Probe on EX_PC[19:0]
  // RiscV_Probe riscv_probe_3: pin names not known; wires that end beside it: EX_IR
  Hex_Digit_Display hex_digit_display_8 (.value(LedData[3:0]));  // open: dp
  PC_in pc_in_1 (
    .PC(multiplexer_1_out), .immb(immb), .immuj(immuj), .ALU_Res(EX_ALU_Res), .\中断编号 (undriven), .GE(GE),
    .BLTU(BLTU), .URET(URET), .JALR(JALR), .JAL(JAL), .Beq(Beq), .Bne(Bne), .Equal(Equal), .\中断触发 (1'b0),
    .PC_2(pc_in_1_pc_2));  // open: EPC
  not not_4 (not_4_out, multiplexer_2_out);
  Multiplexer #(.select(1), .width(1), .disabled("Z"), .enable("false")) multiplexer_2 (
    .in0(and_2_out), .in1(and_3_out), .out(multiplexer_2_out), .sel(halt));
  and and_2 (and_2_out, not_5_out, Load_Use);
  not not_5 (not_5_out, Flush);
  not not_6 (not_6_out, Go);
  // Probe on \总周期数 
  // Probe on M_PC[19:0]
  // RiscV_Probe riscv_probe_4: pin names not known; wires that end beside it: MEM_IR
  Register #(.width(32), .trigger("rising"), .Select("low")) PC (
    .D(pc_in_1_pc_2), .en(not_4_out), .Q(IF_PC), .clk(CLK), .clr(RST));
  and and_3 (and_3_out, not_6_out, halt);
  // Probe on \总周期数 
  // Probe on \无条件分支数 
  // Probe on \条件分支成功数 
  // Probe on \插入气泡数 
  // Probe on \LoadUse次数 
  // Probe on IF_PC[11:0]
  // Probe on WB_PC[19:0]
  // RiscV_Probe riscv_probe_5: pin names not known; wires that end beside it: WB_IR
  // Probe on EX_PC[11:0]
  // Probe on ID_PC[11:0]
  ROM #(.addrWidth(10), .dataWidth(32), .Select("high")) rom_1 (.addr(IF_PC[11:2]), .data(IF_IR));
  // Probe on M_PC[11:0]
  D_Flip_Flop #(.trigger("high"), .Pre_Clr_Positions("LEGACY"), .NegatePresetClear("false"), .enable("true"), .NewFFLayout("false")) d_ff_1 (.Q(d_ff_1_q));  // open: clk, D, Qn, preset, en, reset
  // Probe on 13'h8ea
  IF_ID if_id_1 (
    .IF_PC(IF_PC), .IF_IR(IF_IR), .ID_PC(ID_PC), .ID_IR(ID_IR), .CLK(CLK), .halt(multiplexer_3_out),
    .Flush(Flush));
  Multiplexer #(.select(1), .width(1), .disabled("Z"), .enable("false")) multiplexer_3 (
    .in0(Load_Use), .in1(and_4_out), .out(multiplexer_3_out), .sel(halt));
  and and_4 (and_4_out, not_7_out, halt);
  not not_7 (not_7_out, Go);
  Multiplexer #(.select(1), .width(5), .disabled("Z"), .enable("false")) multiplexer_4 (
    .in0(ID_IR[19:15]), .in1(5'b10001), .out(rrs1), .sel(ID_ecall));
  Multiplexer #(.select(1), .width(5), .disabled("Z"), .enable("false")) multiplexer_5 (
    .in0(ID_IR[24:20]), .in1(5'b01010), .out(rrs2), .sel(ID_ecall));
  // Probe on WB_PC[11:0]
  Comparator #(.width(13), .mode("twosComplement")) comparator_1 (
    .a(CNT_num), .b(13'h8ea), .eq(comparator_1_eq), .lt(comparator_1_lt));  // open: gt
  Clock #(.highDuration(1), .lowDuration(1)) clock_1 (.out(clock_1_out));
  // RiscV_Probe riscv_probe_6: pin names not known; wires that end beside it: ID_IR
  Reg_Din reg_din_1 (
    .DM_Dout(DM_Dout), .PC(WB_PC), .CSR_out(CSR_out), .ALU_Res(WB_ALU_Res), .LH(WB_LH),
    .MemToReg(WB_MemToReg), .CSR(WB_CSR), .JAL(WB_JAL), .JALR(WB_JALR), .RDin(RDin));
  nand nand_1 (nand_1_out, d_ff_1_q, comparator_1_eq);
  Counter #(.width(13), .max('h1fff), .ongoal("stay"), .trigger("rising"), .behavior("old")) counter_6 (
    .count(comparator_1_lt), .Q(CNT_num), .clk(clock_1_out));  // open: load, D, carry, clr, preset
  Regifile regifile_1 (
    .Din(RDin), .Clk(CLK), .R1(ID_Reg_R1), .R2(regifile_1_r2), .WE(RegWrite), .W_num(WB_rd), .R1_num(rrs1),
    .R2_num(rrs2));
  assign CLK = nand_1_out ? clock_1_out : 1'bz;  // Controlled_Buffer controlled_buffer_1
  Register #(.width(32), .trigger("rising"), .Select("low")) register_1 (
    .D(WB_ALU_Res), .en(WB_CSR), .Q(ID_CSR_out), .clk(CLK), .clr(RST));
  Pull_Resistor #(.pull(1)) pull_resistor_1 (.node(CLK));
  newcontrol newcontrol_1 (
    .out_4(newcontrol_1_out_4), .out_6(newcontrol_1_out_6), .out_8(newcontrol_1_out_8),
    .out_10(newcontrol_1_out_10), .out_12(newcontrol_1_out_12), .out_14(newcontrol_1_out_14),
    .in_1(ID_IR[21]), .in_2(ID_IR[6:2]), .in_3({ID_IR[30], ID_IR[25], ID_IR[14:12]}),
    .out_5(newcontrol_1_out_5), .out_7(newcontrol_1_out_7), .out_9(newcontrol_1_out_9),
    .out_11(newcontrol_1_out_11), .out_13(newcontrol_1_out_13), .out_15(newcontrol_1_out_15),
    .out_16(newcontrol_1_out_16), .out_17(newcontrol_1_out_17), .out_18(ID_ecall));
  redirect redirect_1 (
    .ERegwrite(EX_RegWrite), .IDrs1(rrs1), .Erd(EX_rd), .IDrs2(rrs2), .Mrd(MEM_rd), .MRegWrite(MEM_RegWrite),
    .OPcode(ID_IR[6:2]), .Rt_MEM(redirect_1_rt_mem), .Rs_MEM(redirect_1_rs_mem), .Rs_WB(redirect_1_rs_wb),
    .Rt_WB(redirect_1_rt_wb), .ID_ecall(ID_ecall));
  Load_Use load_use_1 (
    .ERegwrite(EX_RegWrite), .IDrs1(rrs1), .Erd(EX_rd), .IDrs2(rrs2), .OPcode1(ID_IR[6:2]),
    .LoadUse(Load_Use), .EX_MemToReg(EX_MemToReg));
  or or_4 (or_4_out, Load_Use, Flush);
  ID_EX id_ex_1 (
    .ID_PC(ID_PC), .ID_IR(ID_IR), .ID_rs1(ID_IR[19:15]), .ID_rd(ID_IR[11:7]), .ID_imm12(ID_IR[31:20]),
    .ID_imms({ID_IR[31:25], ID_IR[11:7]}), .ID_immb({ID_IR[31], ID_IR[7], ID_IR[30:25], ID_IR[11:8]}),
    .ID_immuj({ID_IR[31], ID_IR[19:12], ID_IR[20], ID_IR[30:21]}), .ID_Beq(newcontrol_1_out_5),
    .ID_Bne(newcontrol_1_out_7), .ID_MemToReg(newcontrol_1_out_9), .ID_MemWrite(newcontrol_1_out_11),
    .ID_ALUOP(newcontrol_1_out_13), .ID_ALUSrcB(newcontrol_1_out_15), .ID_RegWrite(newcontrol_1_out_16),
    .ID_S_type(newcontrol_1_out_17), .ID_JAL(newcontrol_1_out_4), .ID_JALR(newcontrol_1_out_6),
    .ID_URET(newcontrol_1_out_8), .ID_BLTU(newcontrol_1_out_10), .ID_CSR(newcontrol_1_out_12),
    .ID_LH(newcontrol_1_out_14), .ID_ecall(ID_ecall), .ID_Reg_R2(regifile_1_r2), .ID_CSR_out(ID_CSR_out),
    .EX_PC(EX_PC), .EX_IR(EX_IR), .EX_rs1(EX_rs1), .EX_rd(EX_rd), .EX_imm12(EX_imm12), .EX_imms(EX_imms),
    .EX_immb(immb), .EX_immuj(immuj), .EX_Beq(Beq), .EX_Bne(Bne), .EX_MemToReg(EX_MemToReg),
    .EX_MemWrite(id_ex_1_ex_memwrite), .EX_ALUOP(id_ex_1_ex_aluop), .EX_ALUSrcB(id_ex_1_ex_alusrcb),
    .EX_RegWrite(EX_RegWrite), .EX_S_type(id_ex_1_ex_s_type), .EX_JAL(JAL), .EX_JALR(JALR), .EX_URET(URET),
    .EX_BLTU(BLTU), .EX_CSR(EX_CSR), .EX_LH(id_ex_1_ex_lh), .EX_ecall(EX_ecall), .EX_Reg_R2(EX_Reg_R2),
    .EX_CSR_out(EX_CSR_out), .CLK(CLK), .ID_Reg_R1(ID_Reg_R1), .EX_Reg_R1(EX_Reg_R1), .halt(and_5_out),
    .Flush(or_4_out), .Rt_MEM_2(Rt_MEM), .Rs_MEM_2(Rs_MEM), .Rs_WB_2(Rs_WB), .Rt_WB_2(Rt_WB),
    .Rt_MEM(redirect_1_rt_mem), .Rs_MEM(redirect_1_rs_mem), .Rs_WB(redirect_1_rs_wb), .Rt_WB(redirect_1_rt_wb));
  and and_5 (and_5_out, not_8_out, halt);
  not not_8 (not_8_out, Go);
  Multiplexer #(.select(1), .width(32), .disabled("Z"), .enable("false")) multiplexer_6 (
    .in0(EX_Reg_R2), .in1(RDin), .out(multiplexer_6_out), .sel(Rt_WB));
  Multiplexer #(.select(1), .width(32), .disabled("Z"), .enable("false")) multiplexer_7 (
    .in0(EX_Reg_R1), .in1(RDin), .out(multiplexer_7_out), .sel(Rs_WB));
  Multiplexer #(.select(1), .width(32), .disabled("Z"), .enable("false")) multiplexer_8 (
    .in0(redirect_Reg_R1), .in1(EX_CSR_out), .out(multiplexer_8_out), .sel(EX_CSR));
  ALU_Bin alu_bin_1 (
    .Reg_R2(redirect_Reg_R2), .immb(EX_imm12), .rs1(EX_rs1), .imms(EX_imms), .CSR(EX_CSR),
    .S_type(id_ex_1_ex_s_type), .AluSrcB(id_ex_1_ex_alusrcb), .ALU_Bin(alu_bin_1_alu_bin));
  Multiplexer #(.select(1), .width(32), .disabled("Z"), .enable("false")) multiplexer_9 (
    .in0(multiplexer_7_out), .in1(MEM_ALU_Res), .out(redirect_Reg_R1), .sel(Rs_MEM));
  Multiplexer #(.select(1), .width(32), .disabled("Z"), .enable("false")) multiplexer_10 (
    .in0(multiplexer_6_out), .in1(MEM_ALU_Res), .out(redirect_Reg_R2), .sel(Rt_MEM));
  ALU alu_1 (
    .X(multiplexer_8_out), .Y(alu_bin_1_alu_bin), .AluOP(id_ex_1_ex_aluop), .Equal(Equal),
    .Result(EX_ALU_Res), .out_4(GE));  // open: Result_2, out_6
  not not_9 (not_9_out, comparator_2_eq);
  Comparator #(.width(32), .mode("twosComplement")) comparator_2 (
    .a(32'h22), .b(redirect_Reg_R1), .eq(comparator_2_eq));  // open: gt, lt
  Register #(.width(1), .trigger("rising"), .Select("low")) register_2 (
    .D(not_9_out), .en(EX_ecall), .Q(register_2_q), .clk(CLK), .clr(Go));
  Register #(.width(32), .trigger("rising"), .Select("low")) register_3 (
    .D(redirect_Reg_R2), .en(comparator_2_eq), .Q(LedData), .clk(CLK), .clr(RST));
  EX_MEM ex_mem_1 (
    .EX_PC(EX_PC), .EX_IR(EX_IR), .EX_rd(EX_rd), .ID_MemToReg(EX_MemToReg),
    .ID_MemWrite(id_ex_1_ex_memwrite), .ID_RegWrite(EX_RegWrite), .ID_CSR(EX_CSR), .ID_LH(id_ex_1_ex_lh),
    .EX_Reg_R2(redirect_Reg_R2), .EX_ALU_Res(EX_ALU_Res), .MEM_PC(M_PC), .MEM_IR(MEM_IR), .MEM_rd(MEM_rd),
    .EX_MemToReg(ex_mem_1_ex_memtoreg), .EX_MemWrite(MemWrite), .EX_RegWrite(MEM_RegWrite),
    .EX_CSR(ex_mem_1_ex_csr), .EX_LH(ex_mem_1_ex_lh), .MEM_Reg_R2(MDin), .MEM_ALU_Res(MEM_ALU_Res),
    .CLK(CLK), .halt(and_6_out), .ID_JALR(JALR), .EX_JALR(ex_mem_1_ex_jalr), .ID_JAL(JAL),
    .EX_JAL(ex_mem_1_ex_jal), .EX_CSR_out(EX_CSR_out), .MEM_CSR_out(ex_mem_1_mem_csr_out),
    .EX_halt(register_2_q), .MEM_halt(ex_mem_1_mem_halt));  // open: Flush
  and and_6 (and_6_out, not_10_out, halt);
  not not_10 (not_10_out, Go);
  not not_11 (not_11_out, MemWrite);
  RAM #(.addrWidth(10), .dataWidth(32), .bus("separate"), .Select("high")) ram_1 (
    .addr(MEM_ALU_Res[11:2]), .din(MDin), .data(ram_1_data), .str(MemWrite), .clk(CLK), .ld(not_11_out),
    .clr(RST));  // open: sel
  MEM_WB mem_wb_1 (
    .MEM_PC(M_PC), .MEM_IR(MEM_IR), .MEM_rd(MEM_rd), .ID_MemToReg(ex_mem_1_ex_memtoreg),
    .ID_RegWrite(MEM_RegWrite), .ID_JAL(ex_mem_1_ex_jal), .ID_JALR(ex_mem_1_ex_jalr),
    .ID_CSR(ex_mem_1_ex_csr), .ID_LH(ex_mem_1_ex_lh), .MEM_ALU_Res(MEM_ALU_Res), .WB_PC(WB_PC),
    .WB_IR(WB_IR), .WB_rd(WB_rd), .EX_MemToReg(WB_MemToReg), .EX_RegWrite(RegWrite), .EX_JAL(WB_JAL),
    .EX_JALR(WB_JALR), .EX_CSR(WB_CSR), .EX_LH(WB_LH), .WB_ALU_Res(WB_ALU_Res), .in_15(and_7_out),
    .in_16(CLK), .MEM_DM_Dput(ram_1_data), .WB_DM_Dout(DM_Dout), .MEM_CSR_out(ex_mem_1_mem_csr_out),
    .WB_CSR_out(CSR_out), .MEM_halt(ex_mem_1_mem_halt), .WB_halt(halt));  // open: Flush
  and and_7 (and_7_out, not_12_out, halt);
  not not_12 (not_12_out, Go);

  // Other names for the same wires on the sheet: rd[4:0] = ID_IR[11:7]; ID_rs2[4:0] = ID_IR[24:20];
  //   ID_rs1[4:0] = ID_IR[19:15]; ID_OPcode[4:0] = ID_IR[6:2]; MEM_PC[31:0] = M_PC

  // Notes on the sheet:
  //   中断源
  //   时空图监测，可删除
  //   中断等待指示
  //   数码管输出
  //   指令存储器
  //   控制位
  //   指令字
  //   contents of rom_1 (hex, n*v repeats v):
  //   100493 100006f 100493 200913 300993 100006f 100493 200913 300993 100006f 100493 200913 300993
  //   100006f 100493 200913 300993 3d8000ef 100413 100493 1f49493 900533 2200893 73 24d493 48463 fedff06f
  //   900533 2200893 73 100493 249493 900533 2200893 73 48463 fedff06f 100493 1f49493 900533 2200893 73
  //   4034d493 900533 2200893 73 4044d493 900533 2200893 73 4044d493 900533 2200893 73 4044d493 900533
  //   2200893 73 4044d493 900533 2200893 73 4044d493 900533 2200893 73 4044d493 900533 2200893 73 4044d493
  //   900533 2200893 73 100413 1f41993 41f9d993 433 c00913 300b13 140413 f47413 800293 100313 499993
  //   89e9b3 1300533 2200893 73 406282b3 fe0294e3 140413 f00f93 1f47433 1c41413 800293 100313 49d993
  //   89e9b3 1300533 2200893 73 406282b3 fe0294e3 1c45413 406b0b33 b0463 f95ff06f 2b3 fff2c293 829293
  //   ff2e293 500533 2200893 73 fff00413 493 84a023 140413 448493 84a023 140413 448493 84a023 140413
  //   448493 84a023 140413 448493 84a023 140413 448493 84a023 140413 448493 84a023 140413 448493 84a023
  //   140413 448493 84a023 140413 448493 84a023 140413 448493 84a023 140413 448493 84a023 140413 448493
  //   84a023 140413 448493 84a023 140413 448493 84a023 140413 448493 84a023 140413 448493 140413 433
  //   3c00493 42983 4aa03 149a2b3 28663 134a023 1442023 ffc48493 fe9412e3 800533 2200893 73 440413 3c00493
  //   fc9416e3 3200893 73 100293 300313 800493 849493 7648493 900533 2200893 73 800e13 5494b3 6494b3
  //   900533 2200893 73 fffe0e13 fe0e14e3 a00893 73 fff00293 7700493 849493 7748493 900533 2200893 73
  //   1000e13 54c4b3 900533 2200893 73 fffe0e13 fe0e16e3 a00893 73 313 1000e13 8400493 849493 8348493
  //   400913 891913 490913 849493 8248493 849493 8148493 891913 490913 891913 490913 932023 12484b3 430313
  //   fffe0e13 fe0e18e3 2000e13 313 31483 900533 2200893 73 230313 fffe0e13 fe0e14e3 a00893 73 ff100493
  //   900533 2200893 73 148493 fe9068e3 900533 2200893 73 a00893 73 a00893 73 413 140413 800533 2200893 73
  //   240413 800533 2200893 73 340413 800533 2200893 73 440413 800533 2200893 73 540413 800533 2200893 73
  //   640413 800533 2200893 73 740413 800533 2200893 73 840413 800533 2200893 2200893 73 8067
  //   流水调试日志用
  //   暂停节拍，不能为0
  //   戳工具置1进入计数暂停模式，ctrl+k时钟自动运行到对应节拍暂停
  //   ctrl+k关闭时钟连续运行，将控制位置零，进入单步调试模式调试
  //   指令探针
  //   可计数暂停的时钟源
  //   为方便自动评测，需要输出流水线各段保存的PC值，注意是PC不是PC+4，另外ID段寄存器写入信息，Mem段内存写入信息也要输出
  //   数据存储器
endmodule
module \中断按键参考电路  (
  input  \同步清零信号 ,
  output \与中断屏蔽位与 
);

  wire \_1号中断_out , and_1_out, clock_1_out, d_ff_1_q, or_1_out, or_2_out;

  Clock #(.highDuration(1), .lowDuration(1)) clock_1 (.out(clock_1_out));
  Button \_1号中断  (.out(\_1号中断_out ));
  or or_1 (or_1_out, \与中断屏蔽位与 , d_ff_1_q);
  LED #(.active("true")) \_1号中断等待指示灯  (.in(or_1_out));
  D_Flip_Flop #(.trigger("rising"), .Pre_Clr_Positions("LEGACY"), .NegatePresetClear("false"), .enable("true"), .NewFFLayout("false")) d_ff_1 (
    .clk(\_1号中断_out ), .D(1'b1), .Q(d_ff_1_q), .reset(\与中断屏蔽位与 ));  // open: Qn, preset, en
  or or_2 (or_2_out, d_ff_1_q, \与中断屏蔽位与 );
  and and_1 (and_1_out, or_2_out, ~\同步清零信号 );  // AND_Gate
  D_Flip_Flop #(.trigger("rising"), .Pre_Clr_Positions("LEGACY"), .NegatePresetClear("false"), .enable("true"), .NewFFLayout("false")) IR1 (
    .clk(clock_1_out), .D(and_1_out), .Q(\与中断屏蔽位与 ));  // open: Qn, preset, en, reset

  // Notes on the sheet:
  //   中断信号采样参考电路
  //   Reset 
endmodule

module \单周期_单级中断  (
  input  IR1,
  input  IR2,
  input  IR3,
  output RegWrite,
  output MemWrite,
  output [31:0] PC,
  output [31:0] IR,
  output [31:0] RDin,
  output [31:0] MDin,
  output [31:0] LedData
);

  wire AluSrcB, and_1_out, and_2_out, Beq, BLTU, Bne, CLK, clock_1_out, comparator_1_eq, comparator_2_eq,
       comparator_3_eq, comparator_4_eq, comparator_6_eq, comparator_6_lt, controlled_inverter_1_out,
       controlled_inverter_2_out, controlled_inverter_3_out, CSR, d_ff_2_q, d_ff_2_qn, d_ff_3_q, ecall,
       ecall_e, Equal, GE, Go, halt, IE, IR1_t, IR2_t, IR3_t, IRA, IRB, IRC, JAL, JALR, LH, MemToReg,
       multiplexer_4_out, nand_1_out, not_1_out, not_2_out, not_3_out, not_4_out, not_5_out, not_6_out,
       not_7_out, not_8_out, nW1, nW2, nW3, or_1_out, or_2_out, or_3_out, RST, s_type, URET, W1, W2, W3,
       \中断响应 , \中断触发 , \中断请求 ;
  wire [1:0] \中断号 ;
  wire [3:0] \单周期硬布线控制器_1_alu_op ;
  wire [4:0] multiplexer_3_out, multiplexer_5_out, multiplexer_6_out;
  wire [12:0] CNT_num;
  wire [15:0] \总周期数 ;
  wire [31:0] alu_bin_1_alu_bin, ALU_Res, CSR_out, DM_Dout, EPC, multiplexer_8_out, pc_in_1_pc_2,
       pc_in_2_pc_2, RDinr, reg_din_1_rdin, regifile_1_r1;

  Button \u_继续运行  (.out(Go));
  Button _1 (.out(IRA));
  Button _2 (.out(IRB));
  Button _3 (.out(IRC));
  LED #(.active("true")) led_1 (.in(W1));
  LED #(.active("true")) led_2 (.in(W2));
  LED #(.active("true")) led_3 (.in(W3));
  not not_1 (not_1_out, halt);
  Hex_Digit_Display hex_digit_display_1 (.value(LedData[31:28]));  // open: dp
  Comparator #(.width(16), .mode("twosComplement")) comparator_1 (
    .a(16'h23b), .b(\总周期数 ), .eq(comparator_1_eq));  // open: gt, lt
  Comparator #(.width(16), .mode("twosComplement")) comparator_2 (
    .a(\总周期数 ), .b(16'h1), .eq(comparator_2_eq));  // open: gt, lt
  Comparator #(.width(16), .mode("twosComplement")) comparator_3 (
    .a(\总周期数 ), .b(16'h4), .eq(comparator_3_eq));  // open: gt, lt
  Comparator #(.width(16), .mode("twosComplement")) comparator_4 (
    .a(\总周期数 ), .b(16'h7), .eq(comparator_4_eq));  // open: gt, lt
  not not_2 (not_2_out, \中断触发 );
  Counter #(.width(16), .max('hffff), .ongoal("wrap"), .trigger("rising"), .behavior("new")) counter_1 (
    .count(not_1_out), .Q(\总周期数 ), .clk(CLK), .clr(RST));  // open: load, D, carry, preset, down
  Hex_Digit_Display hex_digit_display_2 (.value(LedData[23:20]));  // open: dp
  Hex_Digit_Display hex_digit_display_3 (.value(LedData[27:24]));  // open: dp
  or or_1 (or_1_out, comparator_1_eq, comparator_2_eq);
  assign controlled_inverter_1_out = or_1_out ? ~CLK : 1'bz;  // Controlled_Inverter controlled_inverter_1
  assign controlled_inverter_2_out = comparator_3_eq ? ~CLK : 1'bz;  // Controlled_Inverter controlled_inverter_2
  assign controlled_inverter_3_out = comparator_4_eq ? ~CLK : 1'bz;  // Controlled_Inverter controlled_inverter_3
  or or_2 (or_2_out, nW1, nW2, nW3);
  D_Flip_Flop #(.trigger("rising"), .Pre_Clr_Positions("LEGACY"), .NegatePresetClear("false"), .enable("true"), .NewFFLayout("false")) u_IE (
    .clk(CLK), .D(not_2_out), .Q(IE), .en(not_3_out), .reset(RST));  // open: Qn, preset
  not not_3 (not_3_out, \中断响应 );
  Hex_Digit_Display hex_digit_display_4 (.value(LedData[19:16]));  // open: dp
  Hex_Digit_Display hex_digit_display_5 (.value(LedData[15:12]));  // open: dp
  Pull_Resistor #(.pull(0)) pull_resistor_1 (.node(controlled_inverter_1_out));
  Pull_Resistor #(.pull(0)) pull_resistor_2 (.node(controlled_inverter_2_out));
  Pull_Resistor #(.pull(0)) pull_resistor_3 (.node(controlled_inverter_3_out));
  and and_1 (and_1_out, or_2_out, IE);
  Hex_Digit_Display hex_digit_display_6 (.value(LedData[7:4]));  // open: dp
  Hex_Digit_Display hex_digit_display_7 (.value(LedData[11:8]));  // open: dp
  // Probe on \总周期数 
  D_Flip_Flop #(.trigger("falling"), .Pre_Clr_Positions("LEGACY"), .NegatePresetClear("false"), .enable("true"), .NewFFLayout("false")) d_ff_1 (
    .clk(CLK), .D(and_1_out), .Q(\中断触发 ));  // open: Qn, preset, en, reset
  PC_in pc_in_1 (
    .PC(PC), .immb({IR[31], IR[7], IR[30:25], IR[11:8]}), .immuj({IR[31], IR[19:12], IR[20], IR[30:21]}),
    .ALU_Res(ALU_Res), .\中断编号 (\中断号 ), .EPC(EPC), .GE(GE), .BLTU(BLTU), .URET(URET), .JALR(JALR), .JAL(JAL),
    .Beq(Beq), .Bne(Bne), .Equal(Equal), .\中断触发 (\中断触发 ), .PC_2(pc_in_1_pc_2));
  PC_in pc_in_2 (
    .PC(PC), .immb({IR[31], IR[7], IR[30:25], IR[11:8]}), .immuj({IR[31], IR[19:12], IR[20], IR[30:21]}),
    .ALU_Res(ALU_Res), .\中断编号 (\中断号 ), .EPC(EPC), .GE(GE), .BLTU(BLTU), .URET(URET), .JALR(JALR), .JAL(JAL),
    .Beq(Beq), .Bne(Bne), .Equal(Equal), .\中断触发 (1'b0), .PC_2(pc_in_2_pc_2));
  Hex_Digit_Display hex_digit_display_8 (.value(LedData[3:0]));  // open: dp
  not not_4 (not_4_out, halt);
  and and_2 (and_2_out, not_5_out, \中断触发 );
  not not_5 (not_5_out, \中断响应 );
  // ICS ics_1: pin names not known; wires that end beside it: IR1_t, IR2_t, IR3_t, 4'b1110, URET, CLK, \中断请求 , \中断号 , W1, W2, W3, nW1, nW2, nW3, nW3, nW3
  D_Flip_Flop #(.trigger("rising"), .Pre_Clr_Positions("LEGACY"), .NegatePresetClear("false"), .enable("true"), .NewFFLayout("false")) d_ff_2 (
    .clk(CLK), .D(\中断触发 ), .Q(d_ff_2_q), .Qn(d_ff_2_qn), .en(or_3_out));  // open: preset, reset
  or or_3 (or_3_out, URET, not_6_out);
  not not_6 (not_6_out, \中断响应 );
  Register #(.width(32), .trigger("rising"), .Select("low")) u_PC (
    .D(pc_in_1_pc_2), .en(not_4_out), .Q(PC), .clk(CLK), .clr(RST));
  Register #(.width(32), .trigger("rising"), .Select("low")) register_1 (
    .D(pc_in_2_pc_2), .en(and_2_out), .Q(EPC), .clk(CLK), .clr(RST));
  or or_4 (IR1_t, IR1, IRA);
  Multiplexer #(.select(1), .width(1), .disabled("Z"), .enable("false")) multiplexer_1 (
    .in0(d_ff_2_q), .in1(1'b0), .out(\中断响应 ), .sel(URET));
  or or_5 (IR2_t, IR2, IRB);
  // RiscV_Probe riscv_probe_1: pin names not known; wires that end beside it: d_ff_2_qn, IR
  Multiplexer #(.select(1), .width(32), .disabled("Z"), .enable("false")) multiplexer_2 (
    .in0({32{1'b0}}), .in1(RDinr), .out(RDin), .sel(RegWrite));
  ROM #(.addrWidth(10), .dataWidth(32), .Select("high")) rom_1 (.addr(PC[11:2]), .data(IR));
  or or_6 (IR3_t, IR3, IRC);
  \单周期硬布线控制器  \u_单周期硬布线控制器_1  (
    .Funct({IR[30], IR[25], IR[14:12]}), .OP(IR[6:2]), .ALU_OP(\单周期硬布线控制器_1_alu_op ), .MemToReg(MemToReg),
    .MemWrite(MemWrite), .ALU_SRC(AluSrcB), .RegWrite(RegWrite), .ecall(ecall), .S_type(s_type), .Jalr(JALR),
    .Beq(Beq), .JAL(JAL), .Bne(Bne), .in_3(IR[21]), .uret(URET), .BLTU(BLTU), .CSR(CSR), .LH(LH));  // open: LUI
  Multiplexer #(.select(1), .width(5), .disabled("Z"), .enable("false")) multiplexer_3 (
    .in0(IR[11:7]), .in1(5'b00010), .out(multiplexer_3_out), .sel(1'b0));
  Multiplexer #(.select(1), .width(1), .disabled("Z"), .enable("false")) multiplexer_4 (
    .in0(RegWrite), .out(multiplexer_4_out), .sel(1'b0));  // open: in1
  Multiplexer #(.select(1), .width(5), .disabled("Z"), .enable("false")) multiplexer_5 (
    .in0(IR[19:15]), .in1(5'b10001), .out(multiplexer_5_out), .sel(ecall));
  Multiplexer #(.select(1), .width(5), .disabled("Z"), .enable("false")) multiplexer_6 (
    .in0(IR[24:20]), .in1(5'b01010), .out(multiplexer_6_out), .sel(ecall));
  Multiplexer #(.select(1), .width(32), .disabled("Z"), .enable("false")) multiplexer_7 (
    .in0(reg_din_1_rdin), .in1(32'h2000), .out(RDinr), .sel(1'b0));
  Reg_Din reg_din_1 (
    .DM_Dout(DM_Dout), .PC(PC), .CSR_out(CSR_out), .ALU_Res(ALU_Res), .LH(LH), .MemToReg(MemToReg),
    .CSR(CSR), .JAL(JAL), .JALR(JALR), .RDin(reg_din_1_rdin));
  Regifile regifile_1 (
    .Din(RDinr), .Clk(CLK), .R1(regifile_1_r1), .R2(MDin), .WE(multiplexer_4_out), .W_num(multiplexer_3_out),
    .R1_num(multiplexer_5_out), .R2_num(multiplexer_6_out));
  Register #(.width(32), .trigger("rising"), .Select("low")) register_2 (
    .D(MDin), .en(ecall_e), .Q(LedData), .clk(CLK), .clr(RST));
  Comparator #(.width(32), .mode("twosComplement")) comparator_5 (
    .a(32'h22), .b(regifile_1_r1), .eq(ecall_e));  // open: gt, lt
  Multiplexer #(.select(1), .width(32), .disabled("Z"), .enable("false")) multiplexer_8 (
    .in0(regifile_1_r1), .in1(CSR_out), .out(multiplexer_8_out), .sel(CSR));
  ALU_Bin alu_bin_1 (
    .Reg_R2(MDin), .immb(IR[31:20]), .rs1(IR[19:15]), .imms({IR[31:25], IR[11:7]}), .CSR(CSR),
    .S_type(s_type), .AluSrcB(AluSrcB), .ALU_Bin(alu_bin_1_alu_bin));
  not not_7 (not_7_out, ecall_e);
  ALU alu_1 (
    .X(multiplexer_8_out), .Y(alu_bin_1_alu_bin), .AluOP(\单周期硬布线控制器_1_alu_op ), .Equal(Equal),
    .Result(ALU_Res), .out_4(GE));  // open: Result_2, out_6
  Register #(.width(32), .trigger("rising"), .Select("low")) register_3 (
    .D(ALU_Res), .en(CSR), .Q(CSR_out), .clk(CLK), .clr(RST));
  D_Flip_Flop #(.trigger("high"), .Pre_Clr_Positions("LEGACY"), .NegatePresetClear("false"), .enable("true"), .NewFFLayout("false")) d_ff_3 (.Q(d_ff_3_q));  // open: clk, D, Qn, preset, en, reset
  // Probe on 13'hb9
  Register #(.width(1), .trigger("rising"), .Select("low")) register_4 (
    .D(not_7_out), .en(ecall), .Q(halt), .clk(CLK), .clr(Go));
  Comparator #(.width(13), .mode("twosComplement")) comparator_6 (
    .a(CNT_num), .b(13'hb9), .eq(comparator_6_eq), .lt(comparator_6_lt));  // open: gt
  Clock #(.highDuration(1), .lowDuration(1)) clock_1 (.out(clock_1_out));
  Counter #(.width(13), .max('h1fff), .ongoal("stay"), .trigger("rising"), .behavior("old")) counter_2 (
    .count(comparator_6_lt), .Q(CNT_num), .clk(clock_1_out));  // open: load, D, carry, clr, preset
  RAM #(.addrWidth(10), .dataWidth(32), .bus("separate"), .Select("high")) ram_1 (
    .addr(ALU_Res[11:2]), .din(MDin), .data(DM_Dout), .str(MemWrite), .clk(CLK), .ld(not_8_out), .clr(RST));  // open: sel
  not not_8 (not_8_out, MemWrite);
  nand nand_1 (nand_1_out, d_ff_3_q, comparator_6_eq);
  assign CLK = nand_1_out ? clock_1_out : 1'bz;  // Controlled_Buffer controlled_buffer_1
  Pull_Resistor #(.pull(1)) pull_resistor_4 (.node(CLK));

  // Other names for the same wires on the sheet: immb[11:0] = {IR[31], IR[7], IR[30:25], IR[11:8]};
  //   imms[11:0] = {IR[31:25], IR[11:7]}; rd[4:0] = IR[11:7]; imm12[11:0] = IR[31:20];
  //   immuj[19:0] = {IR[31], IR[19:12], IR[20], IR[30:21]}; rs2[4:0] = IR[24:20]; shamt[5:0] = IR[25:20];
  //   rs1[4:0] = IR[19:15]; Reg_R2[31:0] = MDin

  // Notes on the sheet:
  //   中断源
  //   中断等待指示
  //   总复位信号应将除ROM以外所有存储组件全部清零
  //   单级中断测试信号模拟器
  //   数码管输出
  //   数码管输出应该用寄存器锁存，否则显示数据只能一闪而过
  //   指令探针
  //   指令存储器
  //   指令字
  //   contents of rom_1 (hex, n*v repeats v):
  //   7d000113 100413 1f41993 41f9d993 433 c00913 800b13 140413 f47413 800293 100313 499993 89e9b3 1300533
  //   2200893 73 406282b3 fe0294e3 140413 f00f93 1f47433 1c41413 800293 100313 49d993 89e9b3 1300533
  //   2200893 73 406282b3 fe0294e3 1c45413 406b0b33 b0463 f95ff06f 2b3 fff2c293 1029293 fff2e293 500533
  //   2200893 73 f5dff06f 1112023 410113 a12023 410113 812023 410113 1312023 410113 1412023 410113 1512023
  //   410113 1612023 410113 100b13 300a13 100a93 1600433 441413 14469b3 1300533 2200893 73 fe0416e3
  //   415a0a33 fe0a10e3 ffc10113 12b03 ffc10113 12a83 ffc10113 12a03 ffc10113 12983 ffc10113 12403
  //   ffc10113 12503 ffc10113 12883 200073 1112023 410113 a12023 410113 812023 410113 1312023 410113
  //   1412023 410113 1512023 410113 1612023 410113 200b13 300a13 100a93 1600433 441413 14469b3 1300533
  //   2200893 73 fe0416e3 415a0a33 fe0a10e3 ffc10113 12b03 ffc10113 12a83 ffc10113 12a03 ffc10113 12983
  //   ffc10113 12403 ffc10113 12503 ffc10113 12883 200073 1112023 410113 a12023 410113 812023 410113
  //   1312023 410113 1412023 410113 1512023 410113 1612023 410113 300b13 300a13 100a93 1600433 441413
  //   14469b3 1300533 2200893 73 fe0416e3 415a0a33 fe0a10e3 ffc10113 12b03 ffc10113 12a83 ffc10113 12a03
  //   ffc10113 12983 ffc10113 12403 ffc10113 12503 ffc10113 12883 200073
  //   JAL
  //   JALR
  //   URET
  //   Beq
  //   Bne
  //   MemToReg
  //   MemWrite
  //   AluOP
  //   AluSrcB
  //   RegWrite
  //   为方便自动评测，需要输出PC，IR，寄存器堆写如数据RDin
  //   RAM写使能MemWrite、RAM写入数据MDin等信号
  //   控制位
  //   暂停节拍，不能为0
  //   戳工具置1进入计数暂停模式，ctrl+k时钟自动运行到对应节拍暂停
  //   ctrl+k关闭时钟连续运行，将控制位置零，进入单步调试模式调试
  //   数据存储器
  //   可计数暂停的时钟源
endmodule

module \单周期_多级中断  (
  input  IR1,
  input  IR2,
  input  IR3,
  output RegWrite,
  output MemWrite,
  output [31:0] PC,
  output [31:0] IR,
  output [31:0] RDin,
  output [31:0] MDin,
  output [31:0] LedData
);

  wire AluSrcB, and_4_out, and_5_out, and_6_out, and_7_out, Beq, BLTU, Bne, clear1, CLK, clock_1_out,
       comparator_1_eq, comparator_2_eq, comparator_3_eq, comparator_4_eq, comparator_5_eq, comparator_6_eq,
       comparator_7_eq, comparator_8_eq, comparator_10_eq, comparator_11_eq, comparator_12_eq,
       comparator_13_eq, comparator_14_eq, comparator_14_lt, controlled_inverter_1_out,
       controlled_inverter_2_out, controlled_inverter_3_out, CSR, d_ff_2_q, d_ff_3_q, d_ff_4_q, d_ff_6_q,
       ecall, ecall_e, empty, Equal, GE, Go, halt, IE, interrupt_block_1_pass, IR1_t, IR2_t, IR3_t, IRA, IRB,
       IRC, JAL, JALR, LH, MemToReg, MIE, multiplexer_8_out, multiplexer_9_out, nand_1_out, not_1_out,
       not_2_out, not_3_out, not_4_out, not_5_out, not_6_out, not_7_out, not_8_out, nW1, nW2, nW3, or_1_out,
       or_2_out, or_6_out, or_7_out, priority_encoder_1_en_out, register_1_q, register_2_q, register_3_q,
       RST, rst1, rst2, rst3, s_type, URET, W1, W2, W3, \中断响应 , \中断触发 , \中断请求 , \回主程序 ;
  wire [1:0] priority_encoder_1_out, \中断号 , \中断程序号 , \中断编号 ;
  wire [3:0] ALUOP;
  wire [4:0] multiplexer_4_out, multiplexer_5_out, multiplexer_6_out;
  wire [12:0] CNT_num;
  wire [15:0] \总周期数 ;
  wire [31:0] alu_bin_1_alu_bin, ALU_Res, CSR_out, DM_Dout, EPC, multiplexer_11_out, pc_in_1_pc_2,
       pc_in_2_pc_2, RDinr, reg_din_1_rdin, regifile_1_r1;

  Button \u_继续运行  (.out(Go));
  Button _1 (.out(IRA));
  Button _2 (.out(IRB));
  Button _3 (.out(IRC));
  LED #(.active("true")) led_1 (.in(W1));
  LED #(.active("true")) led_2 (.in(W2));
  LED #(.active("true")) led_3 (.in(W3));
  Hex_Digit_Display hex_digit_display_1 (.value(LedData[31:28]));  // open: dp
  Comparator #(.width(2), .mode("twosComplement")) comparator_1 (
    .a(\中断号 ), .b(2'b01), .eq(comparator_1_eq));  // open: gt, lt
  Comparator #(.width(2), .mode("twosComplement")) comparator_2 (
    .a(\中断号 ), .b(2'b10), .eq(comparator_2_eq));  // open: gt, lt
  Comparator #(.width(2), .mode("twosComplement")) comparator_3 (
    .a(\中断号 ), .b(2'b11), .eq(comparator_3_eq));  // open: gt, lt
  D_Flip_Flop #(.trigger("falling"), .Pre_Clr_Positions("LEGACY"), .NegatePresetClear("false"), .enable("true"), .NewFFLayout("false")) d_ff_1 (
    .clk(\中断请求 ), .D(1'b1), .Q(\回主程序 ), .reset(clear1));  // open: Qn, preset, en
  not not_1 (not_1_out, halt);
  Counter #(.width(16), .max('hffff), .ongoal("wrap"), .trigger("rising"), .behavior("new")) counter_1 (
    .count(not_1_out), .Q(\总周期数 ), .clk(CLK), .clr(RST));  // open: load, D, carry, preset, down
  Comparator #(.width(16), .mode("twosComplement")) comparator_4 (
    .a(16'h258), .b(\总周期数 ), .eq(comparator_4_eq));  // open: gt, lt
  Comparator #(.width(16), .mode("twosComplement")) comparator_5 (
    .a(\总周期数 ), .b(16'h1), .eq(comparator_5_eq));  // open: gt, lt
  Comparator #(.width(16), .mode("twosComplement")) comparator_6 (
    .a(\总周期数 ), .b(16'h4), .eq(comparator_6_eq));  // open: gt, lt
  Comparator #(.width(16), .mode("twosComplement")) comparator_7 (
    .a(\总周期数 ), .b(16'h7), .eq(comparator_7_eq));  // open: gt, lt
  Comparator #(.width(16), .mode("twosComplement")) comparator_8 (
    .a(\总周期数 ), .b(16'h241), .eq(comparator_8_eq));  // open: gt, lt
  Hex_Digit_Display hex_digit_display_2 (.value(LedData[23:20]));  // open: dp
  Hex_Digit_Display hex_digit_display_3 (.value(LedData[27:24]));  // open: dp
  Register #(.width(1), .trigger("falling"), .Select("low")) register_1 (
    .D(comparator_1_eq), .en(comparator_1_eq), .Q(register_1_q), .clk(\中断触发 ), .clr(d_ff_2_q));
  Register #(.width(1), .trigger("falling"), .Select("low")) register_2 (
    .D(comparator_2_eq), .en(comparator_2_eq), .Q(register_2_q), .clk(\中断触发 ), .clr(d_ff_3_q));
  Register #(.width(1), .trigger("falling"), .Select("low")) register_3 (
    .D(comparator_3_eq), .en(comparator_3_eq), .Q(register_3_q), .clk(\中断触发 ), .clr(d_ff_4_q));
  or or_1 (or_1_out, comparator_4_eq, comparator_5_eq);
  assign controlled_inverter_1_out = or_1_out ? ~CLK : 1'bz;  // Controlled_Inverter controlled_inverter_1
  assign controlled_inverter_2_out = comparator_6_eq ? ~CLK : 1'bz;  // Controlled_Inverter controlled_inverter_2
  or or_2 (or_2_out, comparator_7_eq, comparator_8_eq);
  assign controlled_inverter_3_out = or_2_out ? ~CLK : 1'bz;  // Controlled_Inverter controlled_inverter_3
  Hex_Digit_Display hex_digit_display_4 (.value(LedData[19:16]));  // open: dp
  Hex_Digit_Display hex_digit_display_5 (.value(LedData[15:12]));  // open: dp
  D_Flip_Flop #(.trigger("rising"), .Pre_Clr_Positions("LEGACY"), .NegatePresetClear("false"), .enable("true"), .NewFFLayout("false")) d_ff_2 (
    .clk(CLK), .D(rst1), .Q(d_ff_2_q));  // open: Qn, preset, en, reset
  D_Flip_Flop #(.trigger("rising"), .Pre_Clr_Positions("LEGACY"), .NegatePresetClear("false"), .enable("true"), .NewFFLayout("false")) d_ff_3 (
    .clk(CLK), .D(rst2), .Q(d_ff_3_q));  // open: Qn, preset, en, reset
  D_Flip_Flop #(.trigger("rising"), .Pre_Clr_Positions("LEGACY"), .NegatePresetClear("false"), .enable("true"), .NewFFLayout("false")) d_ff_4 (
    .clk(CLK), .D(rst3), .Q(d_ff_4_q));  // open: Qn, preset, en, reset
  Pull_Resistor #(.pull(0)) pull_resistor_1 (.node(controlled_inverter_1_out));
  Pull_Resistor #(.pull(0)) pull_resistor_2 (.node(controlled_inverter_2_out));
  Pull_Resistor #(.pull(0)) pull_resistor_3 (.node(controlled_inverter_3_out));
  Hex_Digit_Display hex_digit_display_6 (.value(LedData[11:8]));  // open: dp
  Hex_Digit_Display hex_digit_display_7 (.value(LedData[7:4]));  // open: dp
  // Probe on \总周期数 
  Hex_Digit_Display hex_digit_display_8 (.value(LedData[3:0]));  // open: dp
  Multiplexer #(.select(1), .width(2), .disabled("Z"), .enable("false")) multiplexer_1 (
    .in0(priority_encoder_1_out), .in1(2'b00), .out(\中断程序号 ), .sel(priority_encoder_1_en_out));
  Priority_Encoder #(.select(2), .disabled("Z")) priority_encoder_1 (
    .in1(register_1_q), .in2(register_2_q), .in3(register_3_q), .out(priority_encoder_1_out),
    .en_out(priority_encoder_1_en_out));  // open: in0, gs, en_in
  Comparator #(.width(2), .mode("twosComplement")) comparator_9 (
    .a(priority_encoder_1_out), .b(2'b00), .eq(empty));  // open: gt, lt
  Comparator #(.width(2), .mode("twosComplement")) comparator_10 (
    .a(priority_encoder_1_out), .b(2'b01), .eq(comparator_10_eq));  // open: gt, lt
  Comparator #(.width(2), .mode("twosComplement")) comparator_11 (
    .a(priority_encoder_1_out), .b(2'b10), .eq(comparator_11_eq));  // open: gt, lt
  Comparator #(.width(2), .mode("twosComplement")) comparator_12 (
    .a(priority_encoder_1_out), .b(2'b11), .eq(comparator_12_eq));  // open: gt, lt
  or or_3 (IR1_t, IR1, IRA);
  and and_1 (rst1, comparator_10_eq, URET);
  and and_2 (rst2, comparator_11_eq, URET);
  and and_3 (rst3, comparator_12_eq, URET);
  or or_4 (IR2_t, IR2, IRB);
  PC_in pc_in_1 (
    .PC(PC), .immb({IR[31], IR[7], IR[30:25], IR[11:8]}), .immuj({IR[31], IR[19:12], IR[20], IR[30:21]}),
    .ALU_Res(ALU_Res), .\中断编号 (\中断号 ), .EPC(EPC), .GE(GE), .BLTU(BLTU), .URET(URET), .JALR(JALR), .JAL(JAL),
    .Beq(Beq), .Bne(Bne), .Equal(Equal), .\中断触发 (1'b0), .PC_2(pc_in_1_pc_2));
  and and_4 (and_4_out, \中断触发 , IE);
  not not_2 (not_2_out, URET);
  Interrupt_Block interrupt_block_1 (
    .In3(nW3), .In2(nW2), .In1(nW1), .s1(\中断程序号 [1]), .s0(\中断程序号 [0]), .pass(interrupt_block_1_pass));
  PC_in pc_in_2 (
    .PC(PC), .immb({IR[31], IR[7], IR[30:25], IR[11:8]}), .immuj({IR[31], IR[19:12], IR[20], IR[30:21]}),
    .ALU_Res(ALU_Res), .\中断编号 (\中断号 ), .EPC(EPC), .GE(GE), .BLTU(BLTU), .URET(URET), .JALR(JALR), .JAL(JAL),
    .Beq(Beq), .Bne(Bne), .Equal(Equal), .\中断触发 (\中断触发 ), .PC_2(pc_in_2_pc_2));
  or or_5 (IR3_t, IR3, IRC);
  Multiplexer #(.select(1), .width(32), .disabled("Z"), .enable("false")) multiplexer_2 (
    .in0({32{1'b0}}), .in1(RDinr), .out(RDin), .sel(RegWrite));
  Register #(.width(1), .trigger("rising"), .Select("low")) register_4 (
    .D(and_4_out), .en(not_3_out), .Q(\中断响应 ), .clk(CLK), .clr(or_6_out));
  not not_3 (not_3_out, and_5_out);
  and and_5 (and_5_out, not_2_out, \中断响应 );
  and and_6 (and_6_out, interrupt_block_1_pass, IE);
  not not_4 (not_4_out, halt);
  or or_6 (or_6_out, URET, and_7_out);
  and and_7 (and_7_out, MIE, CSR);
  D_Flip_Flop #(.trigger("falling"), .Pre_Clr_Positions("LEGACY"), .NegatePresetClear("false"), .enable("true"), .NewFFLayout("false")) d_ff_5 (
    .clk(CLK), .D(and_6_out), .Q(\中断触发 ));  // open: Qn, preset, en, reset
  Register #(.width(32), .trigger("rising"), .Select("low")) u_PC (
    .D(pc_in_2_pc_2), .en(not_4_out), .Q(PC), .clk(CLK), .clr(RST));
  multi_Interrupt_jump multi_interrupt_jump_1 (
    .\中断程序号 (\中断程序号 ), .nextPC(pc_in_1_pc_2), .EPC(EPC), .CLK(CLK), .\中断号 (\中断号 ), .URET(URET),
    .\中断触发 (\中断触发 ), .clear1(clear1));
  // RiscV_Probe riscv_probe_1: pin names not known; wires that end beside it: IR
  ICM icm_1 (
    .\_1号中断 (IR1_t), .\_1号中断指示灯 (W1), .\_2号中断 (IR2_t), .\_2号中断指示灯 (W2), .\_3号中断 (IR3_t), .\_3号中断指示灯 (W3),
    .\中断号 (\中断编号 ), .in_3(4'b1110), .\中断请求 (\中断请求 ), .CLK(CLK), .\同步清零信号 (URET), .new_w3(nW3), .new_w2(nW2),
    .new_w1(nW1));
  Multiplexer #(.select(1), .width(2), .disabled("Z"), .enable("false")) multiplexer_3 (
    .in0(2'b00), .in1(\中断编号 ), .out(\中断号 ), .sel(\中断请求 ));
  ROM #(.addrWidth(10), .dataWidth(32), .Select("high")) rom_1 (.addr(PC[11:2]), .data(IR));
  \单周期硬布线控制器  \u_单周期硬布线控制器_1  (
    .Funct({IR[30], IR[25], IR[14:12]}), .OP(IR[6:2]), .ALU_OP(ALUOP), .MemToReg(MemToReg),
    .MemWrite(MemWrite), .ALU_SRC(AluSrcB), .RegWrite(RegWrite), .ecall(ecall), .S_type(s_type), .Jalr(JALR),
    .Beq(Beq), .JAL(JAL), .Bne(Bne), .in_3(IR[21]), .uret(URET), .BLTU(BLTU), .CSR(CSR), .LH(LH));  // open: LUI
  Multiplexer #(.select(1), .width(5), .disabled("Z"), .enable("false")) multiplexer_4 (
    .in0(IR[19:15]), .in1(5'b10001), .out(multiplexer_4_out), .sel(ecall));
  Multiplexer #(.select(1), .width(5), .disabled("Z"), .enable("false")) multiplexer_5 (
    .in0(IR[24:20]), .in1(5'b01010), .out(multiplexer_5_out), .sel(ecall));
  Multiplexer #(.select(1), .width(5), .disabled("Z"), .enable("false")) multiplexer_6 (
    .in0(IR[11:7]), .in1(5'b00010), .out(multiplexer_6_out), .sel(1'b0));
  Multiplexer #(.select(1), .width(32), .disabled("Z"), .enable("false")) multiplexer_7 (
    .in0(reg_din_1_rdin), .in1(32'h2000), .out(RDinr), .sel(1'b0));
  Reg_Din reg_din_1 (
    .DM_Dout(DM_Dout), .PC(PC), .CSR_out(CSR_out), .ALU_Res(ALU_Res), .LH(LH), .MemToReg(MemToReg),
    .CSR(CSR), .JAL(JAL), .JALR(JALR), .RDin(reg_din_1_rdin));
  D_Flip_Flop #(.trigger("high"), .Pre_Clr_Positions("LEGACY"), .NegatePresetClear("false"), .enable("true"), .NewFFLayout("false")) d_ff_6 (.Q(d_ff_6_q));  // open: clk, D, Qn, preset, en, reset
  // Probe on 13'h232
  not not_5 (not_5_out, \中断触发 );
  not not_6 (not_6_out, \中断响应 );
  Comparator #(.width(4), .mode("twosComplement")) comparator_13 (
    .a(ALUOP), .b(4'b1000), .eq(comparator_13_eq));  // open: gt, lt
  Multiplexer #(.select(1), .width(1), .disabled("Z"), .enable("false")) multiplexer_8 (
    .in0(RegWrite), .out(multiplexer_8_out), .sel(1'b0));  // open: in1
  Comparator #(.width(13), .mode("twosComplement")) comparator_14 (
    .a(CNT_num), .b(13'h232), .eq(comparator_14_eq), .lt(comparator_14_lt));  // open: gt
  Clock #(.highDuration(1), .lowDuration(1)) clock_1 (.out(clock_1_out));
  Multiplexer #(.select(1), .width(1), .disabled("Z"), .enable("false")) multiplexer_9 (
    .in0(not_5_out), .in1(MIE), .out(multiplexer_9_out), .sel(CSR));
  Register #(.width(1), .trigger("rising"), .Select("low")) u_IE (
    .D(multiplexer_9_out), .en(or_7_out), .Q(IE), .clk(CLK), .clr(RST));
  or or_7 (or_7_out, CSR, not_6_out);
  Multiplexer #(.select(1), .width(1), .disabled("Z"), .enable("false")) multiplexer_10 (
    .in0(1'b0), .in1(1'b1), .out(MIE), .sel(comparator_13_eq));
  Regifile regifile_1 (
    .Din(RDinr), .Clk(CLK), .R1(regifile_1_r1), .R2(MDin), .WE(multiplexer_8_out), .W_num(multiplexer_6_out),
    .R1_num(multiplexer_4_out), .R2_num(multiplexer_5_out));
  Counter #(.width(13), .max('h1fff), .ongoal("stay"), .trigger("rising"), .behavior("old")) counter_2 (
    .count(comparator_14_lt), .Q(CNT_num), .clk(clock_1_out));  // open: load, D, carry, clr, preset
  Comparator #(.width(32), .mode("twosComplement")) comparator_15 (
    .a(32'h22), .b(regifile_1_r1), .eq(ecall_e));  // open: gt, lt
  Multiplexer #(.select(1), .width(32), .disabled("Z"), .enable("false")) multiplexer_11 (
    .in0(regifile_1_r1), .in1(CSR_out), .out(multiplexer_11_out), .sel(CSR));
  ALU_Bin alu_bin_1 (
    .Reg_R2(MDin), .immb(IR[31:20]), .rs1(IR[19:15]), .imms({IR[31:25], IR[11:7]}), .CSR(CSR),
    .S_type(s_type), .AluSrcB(AluSrcB), .ALU_Bin(alu_bin_1_alu_bin));
  nand nand_1 (nand_1_out, d_ff_6_q, comparator_14_eq);
  not not_7 (not_7_out, ecall_e);
  assign CLK = nand_1_out ? clock_1_out : 1'bz;  // Controlled_Buffer controlled_buffer_1
  Pull_Resistor #(.pull(1)) pull_resistor_4 (.node(CLK));
  Register #(.width(1), .trigger("rising"), .Select("low")) register_5 (
    .D(not_7_out), .en(ecall), .Q(halt), .clk(CLK), .clr(Go));
  ALU alu_1 (
    .X(multiplexer_11_out), .Y(alu_bin_1_alu_bin), .AluOP(ALUOP), .Equal(Equal), .Result(ALU_Res), .out_4(GE));  // open: Result_2, out_6
  Register #(.width(32), .trigger("rising"), .Select("low")) u_LedData (
    .D(MDin), .en(ecall_e), .Q(LedData), .clk(CLK), .clr(RST));
  not not_8 (not_8_out, MemWrite);
  Register #(.width(32), .trigger("rising"), .Select("low")) u_CSR (
    .D(ALU_Res), .en(CSR), .Q(CSR_out), .clk(CLK), .clr(RST));
  RAM #(.addrWidth(10), .dataWidth(32), .bus("separate"), .Select("high")) ram_1 (
    .addr(ALU_Res[11:2]), .din(MDin), .data(DM_Dout), .str(MemWrite), .clk(CLK), .ld(not_8_out), .clr(RST));  // open: sel

  // Other names for the same wires on the sheet: immb[11:0] = {IR[31], IR[7], IR[30:25], IR[11:8]};
  //   imms[11:0] = {IR[31:25], IR[11:7]}; rd[4:0] = IR[11:7]; imm12[11:0] = IR[31:20];
  //   immuj[19:0] = {IR[31], IR[19:12], IR[20], IR[30:21]}; rs2[4:0] = IR[24:20]; rs1[4:0] = IR[19:15];
  //   Reg_R2[31:0] = MDin

  // Notes on the sheet:
  //   中断源
  //   中断等待指示
  //   总复位信号应将除ROM以外所有存储组件全部清零
  //   多级中断测试信号模拟器
  //   数码管输出
  //   数码管输出应该用寄存器锁存，否则显示数据只能一闪而过
  //   指令探针
  //   指令存储器
  //   为方便自动评测，需要输出PC，IR，寄存器堆写如数据RDin
  //   指令字
  //   RAM写使能MemWrite、RAM写入数据MDin等信号
  //   JAL
  //   JALR
  //   URET
  //   contents of rom_1 (hex, n*v repeats v):
  //   7d000113 100413 1f41993 41f9d993 433 c00913 800b13 140413 f47413 800293 100313 499993 89e9b3 1300533
  //   2200893 73 406282b3 fe0294e3 140413 f00f93 1f47433 1c41413 800293 100313 49d993 89e9b3 1300533
  //   2200893 73 406282b3 fe0294e3 1c45413 406b0b33 b0463 f95ff06f 2b3 fff2c293 1029293 fff2e293 500533
  //   2200893 73 f5dff06f 1112023 410113 a12023 410113 812023 410113 1312023 410113 1412023 410113 1512023
  //   410113 1612023 410113 40e073 100b13 300a13 100a93 1600433 441413 14469b3 1300533 2200893 73 fe0416e3
  //   415a0a33 fe0a10e3 40f073 ffc10113 12b03 ffc10113 12a83 ffc10113 12a03 ffc10113 12983 ffc10113 12403
  //   ffc10113 12503 ffc10113 12883 200073 1112023 410113 a12023 410113 812023 410113 1312023 410113
  //   1412023 410113 1512023 410113 1612023 410113 40e073 200b13 300a13 100a93 1600433 441413 14469b3
  //   1300533 2200893 73 fe0416e3 415a0a33 fe0a10e3 40f073 ffc10113 12b03 ffc10113 12a83 ffc10113 12a03
  //   ffc10113 12983 ffc10113 12403 ffc10113 12503 ffc10113 12883 200073 1112023 410113 a12023 410113
  //   812023 410113 1312023 410113 1412023 410113 1512023 410113 1612023 410113 40e073 300b13 300a13
  //   100a93 1600433 441413 14469b3 1300533 2200893 73 fe0416e3 415a0a33 fe0a10e3 40f073 ffc10113 12b03
  //   ffc10113 12a83 ffc10113 12a03 ffc10113 12983 ffc10113 12403 ffc10113 12503 ffc10113 12883 200073
  //   Beq
  //   Bne
  //   AluOP
  //   AluSrcB
  //   RegWrite
  //   MemToReg
  //   MemWrite
  //   控制位
  //   暂停节拍，不能为0
  //   戳工具置1进入计数暂停模式，ctrl+k时钟自动运行到对应节拍暂停
  //   ctrl+k关闭时钟连续运行，将控制位置零，进入单步调试模式调试
  //   可计数暂停的时钟源
  //   数据存储器
endmodule

module \封装正确性测试  (
);

  wire IR1, IR2, IR3, MemW, RegW;
  wire [31:0] EX_PC, ID_PC, IF_PC, IR, LED, MDin, MDinr, MEM_PC, PC, RDin, RDinr, WB_PC;

  \单周期RISC_V  \u_单周期risc_v_1  (
    .IR1(IR1), .IR2(IR2), .IR3(IR3), .RegWrite(RegW), .MemWrite(MemW), .PC(PC), .IR(IR), .RDin(RDin),
    .MDin(MDin), .LedData(LED));
  \气泡流水线  \u_气泡流水线_1  (
    .RegWrite(RegW), .MemWrite(MemW), .IF_PC(IF_PC), .ID_PC(ID_PC), .EX_PC(EX_PC), .M_PC(MEM_PC),
    .WB_PC(WB_PC), .RDin(RDinr), .MDin(MDinr), .LedData(LED));
  \单周期_单级中断  \u_单周期_单级中断_1  (
    .IR1(IR1), .IR2(IR2), .IR3(IR3), .RegWrite(RegW), .MemWrite(MemW), .PC(PC), .IR(IR), .RDin(RDin),
    .MDin(MDin), .LedData(LED));
  \理想流水线  \u_理想流水线_1  (
    .RegWrite(RegW), .MemWrite(MemW), .IF_PC(IF_PC), .ID_PC(ID_PC), .EX_PC(EX_PC), .M_PC(MEM_PC),
    .WB_PC(WB_PC), .RDin(RDinr), .MDin(MDinr), .LedData(LED));
  \重定向流水线  \u_重定向流水线_1  (
    .RegWrite(RegW), .MemWrite(MemW), .IF_PC(IF_PC), .ID_PC(ID_PC), .EX_PC(EX_PC), .M_PC(MEM_PC),
    .WB_PC(WB_PC), .RDin(RDinr), .MDin(MDinr), .LedData(LED));
  \单周期_多级中断  \u_单周期_多级中断_1  (
    .IR1(IR1), .IR2(IR2), .IR3(IR3), .RegWrite(RegW), .MemWrite(MemW), .PC(PC), .IR(IR), .RDin(RDin),
    .MDin(MDin), .LedData(LED));

  // Notes on the sheet:
  //   单周期封装测试
  //   气泡流水封装测试
  //   单周期+单级中断封装测试
  //   请检查上面封装有无位宽不匹配，引脚标签是否和连接的标签相对应，否则无法在educoder平台上正确测试
  //   理想流水封装测试
  //   重定向流水封装测试
  //   单周期+多级中断封装测试
endmodule

module PC_selector (
  input  \中断触发 ,
  input  bne,
  input  beq,
  input  jal,
  input  jalr,
  input  uret,
  input  bltu,
  output s2,
  output s1,
  output s0
);

  or or_1 (s2, \中断触发 , uret);
  or or_2 (s1, jalr, jal);
  or or_3 (s0, \中断触发 , jalr, beq, bne, bltu);
endmodule

module PC_source (
  input  [31:0] PC,
  input  [11:0] immb,
  input  [19:0] immuj,
  input  [31:0] ALU_Res,
  input  [31:0] EPC,
  input  [1:0] in_6,
  output [31:0] out_7,
  output [31:0] out_8,
  output [31:0] out_9,
  output [31:0] out_10,
  output [31:0] URET,
  output [31:0] entrance
);

  wire comparator_1_eq, comparator_2_eq, comparator_3_eq;
  wire [1:0] priority_encoder_1_out;
  wire [11:0] shifter_1_out;
  wire [19:0] shifter_2_out;
  wire [31:0] bit_extender_1_out, bit_extender_2_out, not_1_out;

  Comparator #(.width(2), .mode("twosComplement")) comparator_1 (
    .a(in_6), .b(2'b01), .eq(comparator_1_eq));  // open: gt, lt
  Comparator #(.width(2), .mode("twosComplement")) comparator_2 (
    .a(in_6), .b(2'b10), .eq(comparator_2_eq));  // open: gt, lt
  Comparator #(.width(2), .mode("twosComplement")) comparator_3 (
    .a(in_6), .b(2'b11), .eq(comparator_3_eq));  // open: gt, lt
  assign not_1_out = ~32'h1;  // NOT_Gate not_1, 32 bits wide
  Priority_Encoder #(.select(2), .disabled("Z")) priority_encoder_1 (
    .in0(1'b0), .in1(comparator_1_eq), .in2(comparator_2_eq), .in3(comparator_3_eq),
    .out(priority_encoder_1_out));  // open: gs, en_out, en_in
  Multiplexer #(.select(2), .width(32), .disabled("Z"), .enable("false")) multiplexer_1 (
    .in1(32'h30ac), .in2(32'h3158), .in3(32'h3204), .out(entrance), .sel(priority_encoder_1_out));  // open: in0
  Shifter #(.width(12), .shift("ll")) shifter_1 (.in(immb), .\dist (4'b0001), .out(shifter_1_out));
  Shifter #(.width(20), .shift("ll")) shifter_2 (.in(immuj), .\dist (5'b00001), .out(shifter_2_out));
  assign out_10 = ALU_Res & not_1_out;  // AND_Gate and_1, 32 bits wide
  assign bit_extender_1_out = {{20{shifter_1_out[11]}}, shifter_1_out};  // Bit_Extender bit_extender_1
  assign bit_extender_2_out = {{12{shifter_2_out[19]}}, shifter_2_out};  // Bit_Extender bit_extender_2
  Adder #(.width(32)) adder_1 (.a(PC), .b(32'h4), .out(out_7));  // open: cin, cout
  Adder #(.width(32)) adder_2 (.a(PC), .b(bit_extender_1_out), .out(out_8));  // open: cin, cout
  Adder #(.width(32)) adder_3 (.a(PC), .b(bit_extender_2_out), .out(out_9));  // open: cin, cout

  assign URET = EPC;
endmodule

module Din_selector (
  input  MemToReg,
  input  CSR,
  input  jal,
  input  jalr,
  output s1,
  output s0
);

  wire and_1_out, and_2_out, not_1_out, not_2_out, not_3_out, not_4_out;

  not not_1 (not_1_out, MemToReg);
  not not_2 (not_2_out, jal);
  and and_1 (and_1_out, not_1_out, not_2_out, jalr);
  not not_3 (not_3_out, MemToReg);
  and and_2 (and_2_out, not_3_out, jal, not_4_out);
  not not_4 (not_4_out, jalr);
  or or_1 (s0, CSR, MemToReg);
  or or_2 (s1, and_1_out, and_2_out, CSR);
endmodule

module ALU_Bsource (
  input  [31:0] in_1,
  input  [11:0] in_2,
  input  [4:0] in_3,
  input  [11:0] in_4,
  output [31:0] out_5,
  output [31:0] out_6,
  output [31:0] out_7,
  output [31:0] out_8
);

  assign out_6 = {{20{in_2[11]}}, in_2};  // Bit_Extender bit_extender_1
  assign out_7 = {{27{1'b0}}, in_3};  // Bit_Extender bit_extender_2
  assign out_8 = {{20{in_4[11]}}, in_4};  // Bit_Extender bit_extender_3

  assign out_5 = in_1;
endmodule

module ALU_selector (
  input  CSR,
  input  S_Type,
  input  ALU_Src,
  output s1,
  output s0
);

  or or_1 (s1, S_Type, CSR);
  or or_2 (s0, ALU_Src, S_Type);
endmodule

module PC_in (
  input  GE,
  input  Equal,
  input  BLTU,
  input  Beq,
  input  URET,
  input  JALR,
  input  Bne,
  input  JAL,
  input  \中断触发 ,
  input  [31:0] PC,
  input  [11:0] immb,
  input  [19:0] immuj,
  input  [31:0] ALU_Res,
  input  [1:0] \中断编号 ,
  input  [31:0] EPC,
  output [31:0] PC_2
);

  wire and_1_out, and_2_out, and_3_out, not_1_out, not_2_out;
  wire [2:0] pc_selector_1_s0;
  wire [31:0] pc_source_1_entrance, pc_source_1_out_7, pc_source_1_out_8, pc_source_1_out_9,
       pc_source_1_out_10, pc_source_1_uret;

  not not_1 (not_1_out, GE);
  and and_1 (and_1_out, not_1_out, BLTU);
  PC_selector pc_selector_1 (
    .\中断触发 (\中断触发 ), .bne(and_3_out), .beq(and_2_out), .jal(JAL), .jalr(JALR), .uret(URET), .bltu(and_1_out),
    .s2(pc_selector_1_s0[2]), .s1(pc_selector_1_s0[1]), .s0(pc_selector_1_s0[0]));
  PC_source pc_source_1 (
    .PC(PC), .immb(immb), .immuj(immuj), .ALU_Res(ALU_Res), .out_7(pc_source_1_out_7),
    .out_8(pc_source_1_out_8), .out_9(pc_source_1_out_9), .out_10(pc_source_1_out_10),
    .URET(pc_source_1_uret), .entrance(pc_source_1_entrance), .in_6(\中断编号 ), .EPC(EPC));
  Multiplexer #(.select(3), .width(32), .disabled("Z"), .enable("false")) multiplexer_1 (
    .in0(pc_source_1_out_7), .in1(pc_source_1_out_8), .in2(pc_source_1_out_9), .in3(pc_source_1_out_10),
    .in4(pc_source_1_uret), .in5(pc_source_1_entrance), .out(PC_2), .sel(pc_selector_1_s0));  // open: in6, in7
  and and_2 (and_2_out, Beq, Equal);
  and and_3 (and_3_out, Bne, not_2_out);
  not not_2 (not_2_out, Equal);
endmodule

module Reg_Din (
  input  [31:0] ALU_Res,
  input  [31:0] DM_Dout,
  input  LH,
  input  MemToReg,
  input  CSR,
  input  JAL,
  input  [31:0] PC,
  input  JALR,
  input  [31:0] CSR_out,
  output [31:0] RDin
);

  wire [1:0] din_selector_1_s0;
  wire [15:0] multiplexer_1_out;
  wire [31:0] adder_1_out, bit_extender_1_out, multiplexer_2_out;

  Multiplexer #(.select(1), .width(16), .disabled("Z"), .enable("false")) multiplexer_1 (
    .in0(DM_Dout[15:0]), .in1(DM_Dout[31:16]), .out(multiplexer_1_out), .sel(ALU_Res[1]));
  assign bit_extender_1_out = {{16{multiplexer_1_out[15]}}, multiplexer_1_out};  // Bit_Extender bit_extender_1
  Adder #(.width(32)) adder_1 (.a(PC), .b(32'h4), .out(adder_1_out));  // open: cin, cout
  Multiplexer #(.select(1), .width(32), .disabled("Z"), .enable("false")) multiplexer_2 (
    .in0(DM_Dout), .in1(bit_extender_1_out), .out(multiplexer_2_out), .sel(LH));
  Multiplexer #(.select(2), .width(32), .disabled("Z"), .enable("false")) multiplexer_3 (
    .in0(ALU_Res), .in1(multiplexer_2_out), .in2(adder_1_out), .in3(CSR_out), .out(RDin),
    .sel(din_selector_1_s0));
  Din_selector din_selector_1 (
    .MemToReg(MemToReg), .CSR(CSR), .jal(JAL), .jalr(JALR), .s1(din_selector_1_s0[1]),
    .s0(din_selector_1_s0[0]));
endmodule

module ALU_Bin (
  input  [31:0] Reg_R2,
  input  [11:0] immb,
  input  [4:0] rs1,
  input  CSR,
  input  S_type,
  input  [11:0] imms,
  input  AluSrcB,
  output [31:0] ALU_Bin
);

  wire [1:0] alu_selector_1_s0;
  wire [31:0] alu_bsource_1_out_5, alu_bsource_1_out_6, alu_bsource_1_out_7, alu_bsource_1_out_8;

  ALU_Bsource alu_bsource_1 (
    .in_1(Reg_R2), .in_2(immb), .in_3(rs1), .in_4(imms), .out_5(alu_bsource_1_out_5),
    .out_6(alu_bsource_1_out_6), .out_7(alu_bsource_1_out_7), .out_8(alu_bsource_1_out_8));
  Multiplexer #(.select(2), .width(32), .disabled("Z"), .enable("false")) multiplexer_1 (
    .in0(alu_bsource_1_out_5), .in1(alu_bsource_1_out_6), .in2(alu_bsource_1_out_7),
    .in3(alu_bsource_1_out_8), .out(ALU_Bin), .sel(alu_selector_1_s0));
  ALU_selector alu_selector_1 (
    .CSR(CSR), .S_Type(S_type), .ALU_Src(AluSrcB), .s1(alu_selector_1_s0[1]), .s0(alu_selector_1_s0[0]));
endmodule

module IF_ID (
  input  [31:0] IF_PC,
  input  [31:0] IF_IR,
  input  Flush,
  input  halt,
  input  CLK,
  output [31:0] ID_PC,
  output [31:0] ID_IR
);

  wire pull_resistor_2_node;
  wire [31:0] multiplexer_1_out, multiplexer_2_out;

  Multiplexer #(.select(1), .width(32), .disabled("Z"), .enable("false")) multiplexer_1 (
    .in0(IF_PC), .in1({32{1'b0}}), .out(multiplexer_1_out), .sel(Flush));
  Multiplexer #(.select(1), .width(32), .disabled("Z"), .enable("false")) multiplexer_2 (
    .in0(IF_IR), .in1({32{1'b0}}), .out(multiplexer_2_out), .sel(Flush));
  Pull_Resistor #(.pull(0)) pull_resistor_1 (.node(Flush));
  Pull_Resistor #(.pull(0)) pull_resistor_2 (.node(pull_resistor_2_node));
  not not_1 (pull_resistor_2_node, halt);
  Register #(.width(32), .trigger("rising"), .Select("low")) register_1 (
    .D(multiplexer_1_out), .en(pull_resistor_2_node), .Q(ID_PC), .clk(CLK));  // open: clr
  Register #(.width(32), .trigger("rising"), .Select("low")) register_2 (
    .D(multiplexer_2_out), .en(pull_resistor_2_node), .Q(ID_IR), .clk(CLK));  // open: clr
endmodule

module ID_EX (
  input  [31:0] ID_PC,
  input  [31:0] ID_IR,
  input  [4:0] ID_rs1,
  input  [4:0] ID_rd,
  input  [11:0] ID_imm12,
  input  [11:0] ID_imms,
  input  [11:0] ID_immb,
  input  [19:0] ID_immuj,
  input  ID_Beq,
  input  ID_Bne,
  input  ID_MemToReg,
  input  ID_MemWrite,
  input  [3:0] ID_ALUOP,
  input  ID_ALUSrcB,
  input  ID_RegWrite,
  input  ID_S_type,
  input  ID_JAL,
  input  ID_JALR,
  input  ID_URET,
  input  ID_BLTU,
  input  ID_CSR,
  input  ID_LH,
  input  ID_ecall,
  input  [31:0] ID_Reg_R2,
  input  [31:0] ID_CSR_out,
  input  [31:0] ID_Reg_R1,
  input  Rt_MEM,
  input  Rs_MEM,
  input  Rs_WB,
  input  Rt_WB,
  input  Flush,
  input  halt,
  input  CLK,
  output [31:0] EX_PC,
  output [31:0] EX_IR,
  output [4:0] EX_rs1,
  output [4:0] EX_rd,
  output [11:0] EX_imm12,
  output [11:0] EX_imms,
  output [11:0] EX_immb,
  output [19:0] EX_immuj,
  output EX_Beq,
  output EX_Bne,
  output EX_MemToReg,
  output EX_MemWrite,
  output [3:0] EX_ALUOP,
  output EX_ALUSrcB,
  output EX_RegWrite,
  output EX_S_type,
  output EX_JAL,
  output EX_JALR,
  output EX_URET,
  output EX_BLTU,
  output EX_CSR,
  output EX_LH,
  output EX_ecall,
  output [31:0] EX_Reg_R2,
  output [31:0] EX_CSR_out,
  output [31:0] EX_Reg_R1,
  output Rt_MEM_2,
  output Rs_MEM_2,
  output Rs_WB_2,
  output Rt_WB_2
);

  wire multiplexer_9_out, multiplexer_10_out, multiplexer_11_out, multiplexer_12_out, multiplexer_14_out,
       multiplexer_15_out, multiplexer_16_out, multiplexer_17_out, multiplexer_18_out, multiplexer_19_out,
       multiplexer_20_out, multiplexer_21_out, multiplexer_22_out, multiplexer_23_out, multiplexer_25_out,
       multiplexer_26_out, multiplexer_27_out, multiplexer_28_out, pull_resistor_1_node;
  wire [3:0] multiplexer_13_out;
  wire [4:0] multiplexer_3_out, multiplexer_4_out;
  wire [11:0] multiplexer_5_out, multiplexer_6_out, multiplexer_7_out;
  wire [19:0] multiplexer_8_out;
  wire [31:0] multiplexer_1_out, multiplexer_2_out, multiplexer_24_out, multiplexer_29_out,
       multiplexer_30_out;

  Multiplexer #(.select(1), .width(32), .disabled("Z"), .enable("false")) multiplexer_1 (
    .in0(ID_PC), .in1({32{1'b0}}), .out(multiplexer_1_out), .sel(Flush));
  Multiplexer #(.select(1), .width(32), .disabled("Z"), .enable("false")) multiplexer_2 (
    .in0(ID_IR), .in1({32{1'b0}}), .out(multiplexer_2_out), .sel(Flush));
  Multiplexer #(.select(1), .width(5), .disabled("Z"), .enable("false")) multiplexer_3 (
    .in0(ID_rs1), .in1({5{1'b0}}), .out(multiplexer_3_out), .sel(Flush));
  Multiplexer #(.select(1), .width(5), .disabled("Z"), .enable("false")) multiplexer_4 (
    .in0(ID_rd), .in1({5{1'b0}}), .out(multiplexer_4_out), .sel(Flush));
  Multiplexer #(.select(1), .width(12), .disabled("Z"), .enable("false")) multiplexer_5 (
    .in0(ID_imm12), .in1({12{1'b0}}), .out(multiplexer_5_out), .sel(Flush));
  Multiplexer #(.select(1), .width(12), .disabled("Z"), .enable("false")) multiplexer_6 (
    .in0(ID_imms), .in1({12{1'b0}}), .out(multiplexer_6_out), .sel(Flush));
  Multiplexer #(.select(1), .width(12), .disabled("Z"), .enable("false")) multiplexer_7 (
    .in0(ID_immb), .in1({12{1'b0}}), .out(multiplexer_7_out), .sel(Flush));
  Multiplexer #(.select(1), .width(20), .disabled("Z"), .enable("false")) multiplexer_8 (
    .in0(ID_immuj), .in1({20{1'b0}}), .out(multiplexer_8_out), .sel(Flush));
  Multiplexer #(.select(1), .width(1), .disabled("Z"), .enable("false")) multiplexer_9 (
    .in0(ID_Beq), .in1(1'b0), .out(multiplexer_9_out), .sel(Flush));
  Multiplexer #(.select(1), .width(1), .disabled("Z"), .enable("false")) multiplexer_10 (
    .in0(ID_Bne), .in1(1'b0), .out(multiplexer_10_out), .sel(Flush));
  Multiplexer #(.select(1), .width(1), .disabled("Z"), .enable("false")) multiplexer_11 (
    .in0(ID_MemToReg), .in1(1'b0), .out(multiplexer_11_out), .sel(Flush));
  Multiplexer #(.select(1), .width(1), .disabled("Z"), .enable("false")) multiplexer_12 (
    .in0(ID_MemWrite), .in1(1'b0), .out(multiplexer_12_out), .sel(Flush));
  Multiplexer #(.select(1), .width(4), .disabled("Z"), .enable("false")) multiplexer_13 (
    .in0(ID_ALUOP), .in1(4'b0000), .out(multiplexer_13_out), .sel(Flush));
  Multiplexer #(.select(1), .width(1), .disabled("Z"), .enable("false")) multiplexer_14 (
    .in0(ID_ALUSrcB), .in1(1'b0), .out(multiplexer_14_out), .sel(Flush));
  Multiplexer #(.select(1), .width(1), .disabled("Z"), .enable("false")) multiplexer_15 (
    .in0(ID_RegWrite), .in1(1'b0), .out(multiplexer_15_out), .sel(Flush));
  Multiplexer #(.select(1), .width(1), .disabled("Z"), .enable("false")) multiplexer_16 (
    .in0(ID_S_type), .in1(1'b0), .out(multiplexer_16_out), .sel(Flush));
  Multiplexer #(.select(1), .width(1), .disabled("Z"), .enable("false")) multiplexer_17 (
    .in0(ID_JAL), .in1(1'b0), .out(multiplexer_17_out), .sel(Flush));
  Multiplexer #(.select(1), .width(1), .disabled("Z"), .enable("false")) multiplexer_18 (
    .in0(ID_JALR), .in1(1'b0), .out(multiplexer_18_out), .sel(Flush));
  Multiplexer #(.select(1), .width(1), .disabled("Z"), .enable("false")) multiplexer_19 (
    .in0(ID_URET), .in1(1'b0), .out(multiplexer_19_out), .sel(Flush));
  Multiplexer #(.select(1), .width(1), .disabled("Z"), .enable("false")) multiplexer_20 (
    .in0(ID_BLTU), .in1(1'b0), .out(multiplexer_20_out), .sel(Flush));
  Multiplexer #(.select(1), .width(1), .disabled("Z"), .enable("false")) multiplexer_21 (
    .in0(ID_CSR), .in1(1'b0), .out(multiplexer_21_out), .sel(Flush));
  Multiplexer #(.select(1), .width(1), .disabled("Z"), .enable("false")) multiplexer_22 (
    .in0(ID_LH), .in1(1'b0), .out(multiplexer_22_out), .sel(Flush));
  Multiplexer #(.select(1), .width(1), .disabled("Z"), .enable("false")) multiplexer_23 (
    .in0(ID_ecall), .in1(1'b0), .out(multiplexer_23_out), .sel(Flush));
  Multiplexer #(.select(1), .width(32), .disabled("Z"), .enable("false")) multiplexer_24 (
    .in0(ID_Reg_R2), .in1({32{1'b0}}), .out(multiplexer_24_out), .sel(Flush));
  Multiplexer #(.select(1), .width(1), .disabled("Z"), .enable("false")) multiplexer_25 (
    .in0(Rt_MEM), .in1(1'b0), .out(multiplexer_25_out), .sel(Flush));
  Multiplexer #(.select(1), .width(1), .disabled("Z"), .enable("false")) multiplexer_26 (
    .in0(Rs_MEM), .in1(1'b0), .out(multiplexer_26_out), .sel(Flush));
  Multiplexer #(.select(1), .width(1), .disabled("Z"), .enable("false")) multiplexer_27 (
    .in0(Rs_WB), .in1(1'b0), .out(multiplexer_27_out), .sel(Flush));
  Multiplexer #(.select(1), .width(1), .disabled("Z"), .enable("false")) multiplexer_28 (
    .in0(Rt_WB), .in1(1'b0), .out(multiplexer_28_out), .sel(Flush));
  Multiplexer #(.select(1), .width(32), .disabled("Z"), .enable("false")) multiplexer_29 (
    .in0(ID_CSR_out), .in1({32{1'b0}}), .out(multiplexer_29_out), .sel(Flush));
  Multiplexer #(.select(1), .width(32), .disabled("Z"), .enable("false")) multiplexer_30 (
    .in0(ID_Reg_R1), .in1({32{1'b0}}), .out(multiplexer_30_out), .sel(Flush));
  Pull_Resistor #(.pull(0)) pull_resistor_1 (.node(pull_resistor_1_node));
  Pull_Resistor #(.pull(0)) pull_resistor_2 (.node(Flush));
  not not_1 (pull_resistor_1_node, halt);
  Register #(.width(32), .trigger("rising"), .Select("low")) register_1 (
    .D(multiplexer_1_out), .en(pull_resistor_1_node), .Q(EX_PC), .clk(CLK));  // open: clr
  Register #(.width(32), .trigger("rising"), .Select("low")) register_2 (
    .D(multiplexer_2_out), .en(pull_resistor_1_node), .Q(EX_IR), .clk(CLK));  // open: clr
  Register #(.width(5), .trigger("rising"), .Select("low")) register_3 (
    .D(multiplexer_3_out), .en(pull_resistor_1_node), .Q(EX_rs1));  // open: clk, clr
  Register #(.width(5), .trigger("rising"), .Select("low")) register_4 (
    .D(multiplexer_4_out), .en(pull_resistor_1_node), .Q(EX_rd), .clk(CLK));  // open: clr
  Register #(.width(12), .trigger("rising"), .Select("low")) register_5 (
    .D(multiplexer_5_out), .en(pull_resistor_1_node), .Q(EX_imm12), .clk(CLK));  // open: clr
  Register #(.width(12), .trigger("rising"), .Select("low")) register_6 (
    .D(multiplexer_6_out), .en(pull_resistor_1_node), .Q(EX_imms), .clk(CLK));  // open: clr
  Register #(.width(12), .trigger("rising"), .Select("low")) register_7 (
    .D(multiplexer_7_out), .en(pull_resistor_1_node), .Q(EX_immb), .clk(CLK));  // open: clr
  Register #(.width(20), .trigger("rising"), .Select("low")) register_8 (
    .D(multiplexer_8_out), .en(pull_resistor_1_node), .Q(EX_immuj), .clk(CLK));  // open: clr
  Register #(.width(1), .trigger("rising"), .Select("low")) register_9 (
    .D(multiplexer_9_out), .en(pull_resistor_1_node), .Q(EX_Beq), .clk(CLK));  // open: clr
  Register #(.width(1), .trigger("rising"), .Select("low")) register_10 (
    .D(multiplexer_10_out), .en(pull_resistor_1_node), .Q(EX_Bne), .clk(CLK));  // open: clr
  Register #(.width(1), .trigger("rising"), .Select("low")) register_11 (
    .D(multiplexer_11_out), .en(pull_resistor_1_node), .Q(EX_MemToReg), .clk(CLK));  // open: clr
  Register #(.width(1), .trigger("rising"), .Select("low")) register_12 (
    .D(multiplexer_12_out), .en(pull_resistor_1_node), .Q(EX_MemWrite), .clk(CLK));  // open: clr
  Register #(.width(4), .trigger("rising"), .Select("low")) register_13 (
    .D(multiplexer_13_out), .en(pull_resistor_1_node), .Q(EX_ALUOP), .clk(CLK));  // open: clr
  Register #(.width(1), .trigger("rising"), .Select("low")) register_14 (
    .D(multiplexer_14_out), .en(pull_resistor_1_node), .Q(EX_ALUSrcB), .clk(CLK));  // open: clr
  Register #(.width(1), .trigger("rising"), .Select("low")) register_15 (
    .D(multiplexer_15_out), .en(pull_resistor_1_node), .Q(EX_RegWrite), .clk(CLK));  // open: clr
  Register #(.width(1), .trigger("rising"), .Select("low")) register_16 (
    .D(multiplexer_16_out), .en(pull_resistor_1_node), .Q(EX_S_type), .clk(CLK));  // open: clr
  Register #(.width(1), .trigger("rising"), .Select("low")) register_17 (
    .D(multiplexer_17_out), .en(pull_resistor_1_node), .Q(EX_JAL), .clk(CLK));  // open: clr
  Register #(.width(1), .trigger("rising"), .Select("low")) register_18 (
    .D(multiplexer_18_out), .en(pull_resistor_1_node), .Q(EX_JALR), .clk(CLK));  // open: clr
  Register #(.width(1), .trigger("rising"), .Select("low")) register_19 (
    .D(multiplexer_19_out), .en(pull_resistor_1_node), .Q(EX_URET), .clk(CLK));  // open: clr
  Register #(.width(1), .trigger("rising"), .Select("low")) register_20 (
    .D(multiplexer_20_out), .en(pull_resistor_1_node), .Q(EX_BLTU), .clk(CLK));  // open: clr
  Register #(.width(1), .trigger("rising"), .Select("low")) register_21 (
    .D(multiplexer_21_out), .en(pull_resistor_1_node), .Q(EX_CSR), .clk(CLK));  // open: clr
  Register #(.width(1), .trigger("rising"), .Select("low")) register_22 (
    .D(multiplexer_22_out), .en(pull_resistor_1_node), .Q(EX_LH), .clk(CLK));  // open: clr
  Register #(.width(1), .trigger("rising"), .Select("low")) register_23 (
    .D(multiplexer_23_out), .en(pull_resistor_1_node), .Q(EX_ecall), .clk(CLK));  // open: clr
  Register #(.width(32), .trigger("rising"), .Select("low")) register_24 (
    .D(multiplexer_24_out), .en(pull_resistor_1_node), .Q(EX_Reg_R2), .clk(CLK));  // open: clr
  Register #(.width(1), .trigger("rising"), .Select("low")) register_25 (
    .D(multiplexer_25_out), .en(pull_resistor_1_node), .Q(Rt_MEM_2), .clk(CLK));  // open: clr
  Register #(.width(1), .trigger("rising"), .Select("low")) register_26 (
    .D(multiplexer_26_out), .en(pull_resistor_1_node), .Q(Rs_MEM_2), .clk(CLK));  // open: clr
  Register #(.width(1), .trigger("rising"), .Select("low")) register_27 (
    .D(multiplexer_27_out), .en(pull_resistor_1_node), .Q(Rs_WB_2), .clk(CLK));  // open: clr
  Register #(.width(1), .trigger("rising"), .Select("low")) register_28 (
    .D(multiplexer_28_out), .en(pull_resistor_1_node), .Q(Rt_WB_2), .clk(CLK));  // open: clr
  Register #(.width(32), .trigger("rising"), .Select("low")) register_29 (
    .D(multiplexer_29_out), .en(pull_resistor_1_node), .Q(EX_CSR_out), .clk(CLK));  // open: clr
  Register #(.width(32), .trigger("rising"), .Select("low")) register_30 (
    .D(multiplexer_30_out), .en(pull_resistor_1_node), .Q(EX_Reg_R1), .clk(CLK));  // open: clr
endmodule

module EX_MEM (
  input  [31:0] EX_PC,
  input  [31:0] EX_IR,
  input  [4:0] EX_rd,
  input  ID_MemToReg,
  input  ID_MemWrite,
  input  ID_RegWrite,
  input  ID_JAL,
  input  ID_JALR,
  input  ID_CSR,
  input  ID_LH,
  input  [31:0] EX_Reg_R2,
  input  [31:0] EX_ALU_Res,
  input  [31:0] EX_CSR_out,
  input  EX_halt,
  input  Flush,
  input  halt,
  input  CLK,
  output [31:0] MEM_PC,
  output [31:0] MEM_IR,
  output [4:0] MEM_rd,
  output EX_MemToReg,
  output EX_MemWrite,
  output EX_RegWrite,
  output EX_JAL,
  output EX_JALR,
  output EX_CSR,
  output EX_LH,
  output [31:0] MEM_Reg_R2,
  output [31:0] MEM_ALU_Res,
  output [31:0] MEM_CSR_out,
  output MEM_halt
);

  wire multiplexer_4_out, multiplexer_5_out, multiplexer_6_out, multiplexer_7_out, multiplexer_8_out,
       multiplexer_9_out, multiplexer_10_out, multiplexer_14_out, pull_resistor_1_node;
  wire [4:0] multiplexer_3_out;
  wire [31:0] multiplexer_1_out, multiplexer_2_out, multiplexer_11_out, multiplexer_12_out,
       multiplexer_13_out;

  Multiplexer #(.select(1), .width(32), .disabled("Z"), .enable("false")) multiplexer_1 (
    .in0(EX_PC), .in1({32{1'b0}}), .out(multiplexer_1_out), .sel(Flush));
  Multiplexer #(.select(1), .width(32), .disabled("Z"), .enable("false")) multiplexer_2 (
    .in0(EX_IR), .in1({32{1'b0}}), .out(multiplexer_2_out), .sel(Flush));
  Multiplexer #(.select(1), .width(5), .disabled("Z"), .enable("false")) multiplexer_3 (
    .in0(EX_rd), .in1({5{1'b0}}), .out(multiplexer_3_out), .sel(Flush));
  Multiplexer #(.select(1), .width(1), .disabled("Z"), .enable("false")) multiplexer_4 (
    .in0(ID_MemToReg), .in1(1'b0), .out(multiplexer_4_out), .sel(Flush));
  Multiplexer #(.select(1), .width(1), .disabled("Z"), .enable("false")) multiplexer_5 (
    .in0(ID_MemWrite), .in1(1'b0), .out(multiplexer_5_out), .sel(Flush));
  Multiplexer #(.select(1), .width(1), .disabled("Z"), .enable("false")) multiplexer_6 (
    .in0(ID_RegWrite), .in1(1'b0), .out(multiplexer_6_out), .sel(Flush));
  Multiplexer #(.select(1), .width(1), .disabled("Z"), .enable("false")) multiplexer_7 (
    .in0(ID_JAL), .in1(1'b0), .out(multiplexer_7_out), .sel(Flush));
  Multiplexer #(.select(1), .width(1), .disabled("Z"), .enable("false")) multiplexer_8 (
    .in0(ID_JALR), .in1(1'b0), .out(multiplexer_8_out), .sel(Flush));
  Multiplexer #(.select(1), .width(1), .disabled("Z"), .enable("false")) multiplexer_9 (
    .in0(ID_CSR), .in1(1'b0), .out(multiplexer_9_out), .sel(Flush));
  Multiplexer #(.select(1), .width(1), .disabled("Z"), .enable("false")) multiplexer_10 (
    .in0(ID_LH), .in1(1'b0), .out(multiplexer_10_out), .sel(Flush));
  Multiplexer #(.select(1), .width(32), .disabled("Z"), .enable("false")) multiplexer_11 (
    .in0(EX_Reg_R2), .in1({32{1'b0}}), .out(multiplexer_11_out), .sel(Flush));
  Multiplexer #(.select(1), .width(32), .disabled("Z"), .enable("false")) multiplexer_12 (
    .in0(EX_ALU_Res), .in1({32{1'b0}}), .out(multiplexer_12_out), .sel(Flush));
  Multiplexer #(.select(1), .width(32), .disabled("Z"), .enable("false")) multiplexer_13 (
    .in0(EX_CSR_out), .in1({32{1'b0}}), .out(multiplexer_13_out), .sel(Flush));
  Multiplexer #(.select(1), .width(1), .disabled("Z"), .enable("false")) multiplexer_14 (
    .in0(EX_halt), .in1(1'b0), .out(multiplexer_14_out), .sel(Flush));
  Pull_Resistor #(.pull(0)) pull_resistor_1 (.node(pull_resistor_1_node));
  Pull_Resistor #(.pull(0)) pull_resistor_2 (.node(Flush));
  not not_1 (pull_resistor_1_node, halt);
  Register #(.width(32), .trigger("rising"), .Select("low")) register_1 (
    .D(multiplexer_1_out), .en(pull_resistor_1_node), .Q(MEM_PC), .clk(CLK));  // open: clr
  Register #(.width(32), .trigger("rising"), .Select("low")) register_2 (
    .D(multiplexer_2_out), .en(pull_resistor_1_node), .Q(MEM_IR), .clk(CLK));  // open: clr
  Register #(.width(5), .trigger("rising"), .Select("low")) register_3 (
    .D(multiplexer_3_out), .en(pull_resistor_1_node), .Q(MEM_rd), .clk(CLK));  // open: clr
  Register #(.width(1), .trigger("rising"), .Select("low")) register_4 (
    .D(multiplexer_4_out), .en(pull_resistor_1_node), .Q(EX_MemToReg), .clk(CLK));  // open: clr
  Register #(.width(1), .trigger("rising"), .Select("low")) register_5 (
    .D(multiplexer_5_out), .en(pull_resistor_1_node), .Q(EX_MemWrite), .clk(CLK));  // open: clr
  Register #(.width(1), .trigger("rising"), .Select("low")) register_6 (
    .D(multiplexer_6_out), .en(pull_resistor_1_node), .Q(EX_RegWrite), .clk(CLK));  // open: clr
  Register #(.width(1), .trigger("rising"), .Select("low")) register_7 (
    .D(multiplexer_7_out), .en(pull_resistor_1_node), .Q(EX_JAL), .clk(CLK));  // open: clr
  Register #(.width(1), .trigger("rising"), .Select("low")) register_8 (
    .D(multiplexer_8_out), .en(pull_resistor_1_node), .Q(EX_JALR), .clk(CLK));  // open: clr
  Register #(.width(1), .trigger("rising"), .Select("low")) register_9 (
    .D(multiplexer_9_out), .en(pull_resistor_1_node), .Q(EX_CSR), .clk(CLK));  // open: clr
  Register #(.width(1), .trigger("rising"), .Select("low")) register_10 (
    .D(multiplexer_10_out), .en(pull_resistor_1_node), .Q(EX_LH), .clk(CLK));  // open: clr
  Register #(.width(32), .trigger("rising"), .Select("low")) register_11 (
    .D(multiplexer_11_out), .en(pull_resistor_1_node), .Q(MEM_Reg_R2), .clk(CLK));  // open: clr
  Register #(.width(32), .trigger("rising"), .Select("low")) register_12 (
    .D(multiplexer_12_out), .en(pull_resistor_1_node), .Q(MEM_ALU_Res), .clk(CLK));  // open: clr
  Register #(.width(32), .trigger("rising"), .Select("low")) register_13 (
    .D(multiplexer_13_out), .en(pull_resistor_1_node), .Q(MEM_CSR_out), .clk(CLK));  // open: clr
  Register #(.width(1), .trigger("rising"), .Select("low")) register_14 (
    .D(multiplexer_14_out), .en(pull_resistor_1_node), .Q(MEM_halt), .clk(CLK));  // open: clr
endmodule

module newcontrol (
  input  in_1,
  input  [4:0] in_2,
  input  [4:0] in_3,
  output out_4,
  output out_5,
  output out_6,
  output out_7,
  output out_8,
  output out_9,
  output out_10,
  output out_11,
  output out_12,
  output [3:0] out_13,
  output out_14,
  output out_15,
  output out_16,
  output out_17,
  output out_18
);

  \单周期硬布线控制器  \u_单周期硬布线控制器_1  (
    .Funct(in_3), .OP(in_2), .ALU_OP(out_13), .MemToReg(out_9), .MemWrite(out_11), .ALU_SRC(out_15),
    .RegWrite(out_16), .ecall(out_18), .S_type(out_17), .Jalr(out_6), .Beq(out_5), .JAL(out_4), .Bne(out_7),
    .in_3(in_1), .uret(out_8), .BLTU(out_10), .CSR(out_12), .LH(out_14));  // open: LUI
endmodule

module MEM_WB (
  input  [31:0] MEM_PC,
  input  [31:0] MEM_IR,
  input  [4:0] MEM_rd,
  input  ID_MemToReg,
  input  ID_RegWrite,
  input  ID_JAL,
  input  ID_JALR,
  input  ID_CSR,
  input  ID_LH,
  input  [31:0] MEM_ALU_Res,
  input  [31:0] MEM_DM_Dput,
  input  [31:0] MEM_CSR_out,
  input  MEM_halt,
  input  Flush,
  input  in_15,
  input  in_16,
  output [31:0] WB_PC,
  output [31:0] WB_IR,
  output [4:0] WB_rd,
  output EX_MemToReg,
  output EX_RegWrite,
  output EX_JAL,
  output EX_JALR,
  output EX_CSR,
  output EX_LH,
  output [31:0] WB_ALU_Res,
  output [31:0] WB_DM_Dout,
  output [31:0] WB_CSR_out,
  output WB_halt
);

  wire multiplexer_4_out, multiplexer_5_out, multiplexer_6_out, multiplexer_7_out, multiplexer_8_out,
       multiplexer_9_out, multiplexer_13_out, pull_resistor_2_node;
  wire [4:0] multiplexer_3_out;
  wire [31:0] multiplexer_1_out, multiplexer_2_out, multiplexer_10_out, multiplexer_11_out,
       multiplexer_12_out;

  Multiplexer #(.select(1), .width(32), .disabled("Z"), .enable("false")) multiplexer_1 (
    .in0(MEM_PC), .in1({32{1'b0}}), .out(multiplexer_1_out), .sel(Flush));
  Multiplexer #(.select(1), .width(32), .disabled("Z"), .enable("false")) multiplexer_2 (
    .in0(MEM_IR), .in1({32{1'b0}}), .out(multiplexer_2_out), .sel(Flush));
  Multiplexer #(.select(1), .width(5), .disabled("Z"), .enable("false")) multiplexer_3 (
    .in0(MEM_rd), .in1({5{1'b0}}), .out(multiplexer_3_out), .sel(Flush));
  Multiplexer #(.select(1), .width(1), .disabled("Z"), .enable("false")) multiplexer_4 (
    .in0(ID_MemToReg), .in1(1'b0), .out(multiplexer_4_out), .sel(Flush));
  Multiplexer #(.select(1), .width(1), .disabled("Z"), .enable("false")) multiplexer_5 (
    .in0(ID_RegWrite), .in1(1'b0), .out(multiplexer_5_out), .sel(Flush));
  Multiplexer #(.select(1), .width(1), .disabled("Z"), .enable("false")) multiplexer_6 (
    .in0(ID_JAL), .in1(1'b0), .out(multiplexer_6_out), .sel(Flush));
  Multiplexer #(.select(1), .width(1), .disabled("Z"), .enable("false")) multiplexer_7 (
    .in0(ID_JALR), .in1(1'b0), .out(multiplexer_7_out), .sel(Flush));
  Multiplexer #(.select(1), .width(1), .disabled("Z"), .enable("false")) multiplexer_8 (
    .in0(ID_CSR), .in1(1'b0), .out(multiplexer_8_out), .sel(Flush));
  Multiplexer #(.select(1), .width(1), .disabled("Z"), .enable("false")) multiplexer_9 (
    .in0(ID_LH), .in1(1'b0), .out(multiplexer_9_out), .sel(Flush));
  Multiplexer #(.select(1), .width(32), .disabled("Z"), .enable("false")) multiplexer_10 (
    .in0(MEM_ALU_Res), .in1({32{1'b0}}), .out(multiplexer_10_out), .sel(Flush));
  Multiplexer #(.select(1), .width(32), .disabled("Z"), .enable("false")) multiplexer_11 (
    .in0(MEM_DM_Dput), .in1({32{1'b0}}), .out(multiplexer_11_out), .sel(Flush));
  Multiplexer #(.select(1), .width(32), .disabled("Z"), .enable("false")) multiplexer_12 (
    .in0(MEM_CSR_out), .in1({32{1'b0}}), .out(multiplexer_12_out), .sel(Flush));
  Multiplexer #(.select(1), .width(1), .disabled("Z"), .enable("false")) multiplexer_13 (
    .in0(MEM_halt), .in1(1'b0), .out(multiplexer_13_out), .sel(Flush));
  Pull_Resistor #(.pull(0)) pull_resistor_1 (.node(Flush));
  Pull_Resistor #(.pull(0)) pull_resistor_2 (.node(pull_resistor_2_node));
  not not_1 (pull_resistor_2_node, in_15);
  Register #(.width(32), .trigger("rising"), .Select("low")) register_1 (
    .D(multiplexer_1_out), .en(pull_resistor_2_node), .Q(WB_PC), .clk(in_16));  // open: clr
  Register #(.width(32), .trigger("rising"), .Select("low")) register_2 (
    .D(multiplexer_2_out), .en(pull_resistor_2_node), .Q(WB_IR), .clk(in_16));  // open: clr
  Register #(.width(5), .trigger("rising"), .Select("low")) register_3 (
    .D(multiplexer_3_out), .en(pull_resistor_2_node), .Q(WB_rd), .clk(in_16));  // open: clr
  Register #(.width(1), .trigger("rising"), .Select("low")) register_4 (
    .D(multiplexer_4_out), .en(pull_resistor_2_node), .Q(EX_MemToReg), .clk(in_16));  // open: clr
  Register #(.width(1), .trigger("rising"), .Select("low")) register_5 (
    .D(multiplexer_5_out), .en(pull_resistor_2_node), .Q(EX_RegWrite), .clk(in_16));  // open: clr
  Register #(.width(1), .trigger("rising"), .Select("low")) register_6 (
    .D(multiplexer_6_out), .en(pull_resistor_2_node), .Q(EX_JAL), .clk(in_16));  // open: clr
  Register #(.width(1), .trigger("rising"), .Select("low")) register_7 (
    .D(multiplexer_7_out), .en(pull_resistor_2_node), .Q(EX_JALR), .clk(in_16));  // open: clr
  Register #(.width(1), .trigger("rising"), .Select("low")) register_8 (
    .D(multiplexer_8_out), .en(pull_resistor_2_node), .Q(EX_CSR), .clk(in_16));  // open: clr
  Register #(.width(1), .trigger("rising"), .Select("low")) register_9 (
    .D(multiplexer_9_out), .en(pull_resistor_2_node), .Q(EX_LH), .clk(in_16));  // open: clr
  Register #(.width(32), .trigger("rising"), .Select("low")) register_10 (
    .D(multiplexer_10_out), .en(pull_resistor_2_node), .Q(WB_ALU_Res), .clk(in_16));  // open: clr
  Register #(.width(32), .trigger("rising"), .Select("low")) register_11 (
    .D(multiplexer_11_out), .en(pull_resistor_2_node), .Q(WB_DM_Dout), .clk(in_16));  // open: clr
  Register #(.width(1), .trigger("rising"), .Select("low")) register_12 (
    .D(multiplexer_13_out), .en(pull_resistor_2_node), .Q(WB_halt), .clk(in_16));  // open: clr
  Register #(.width(32), .trigger("rising"), .Select("low")) register_13 (
    .D(multiplexer_12_out), .en(pull_resistor_2_node), .Q(WB_CSR_out), .clk(in_16));  // open: clr
endmodule

module WhichPC (
  input  GE,
  input  Equal,
  input  BLTU,
  input  Beq,
  input  URET,
  input  JALR,
  input  Bne,
  input  JAL,
  output out_9
);

  wire and_1_out, and_2_out, and_3_out, not_1_out, not_2_out;
  wire [2:0] pc_selector_1_s0;

  not not_1 (not_1_out, GE);
  and and_1 (and_1_out, not_1_out, BLTU);
  PC_selector pc_selector_1 (
    .\中断触发 (1'b0), .bne(and_3_out), .beq(and_2_out), .jal(JAL), .jalr(JALR), .uret(URET), .bltu(and_1_out),
    .s2(pc_selector_1_s0[2]), .s1(pc_selector_1_s0[1]), .s0(pc_selector_1_s0[0]));
  and and_2 (and_2_out, Beq, Equal);
  and and_3 (and_3_out, Bne, not_2_out);
  Comparator #(.width(3), .mode("twosComplement")) comparator_1 (
    .a(pc_selector_1_s0), .b(3'b000), .eq(out_9));  // open: gt, lt
  not not_2 (not_2_out, Equal);
endmodule

module DataHazzard (
  input  ERegwrite,
  input  [4:0] IDrs1,
  input  [4:0] Erd,
  input  [4:0] IDrs2,
  input  [4:0] Mrd,
  input  MRegWrite,
  input  [4:0] OPcode,
  input  ID_ecall,
  output DataHazzard
);

  wire _2rs, and_1_out, and_2_out, and_3_out, and_4_out, and_5_out, and_6_out, and_7_out, and_8_out,
       and_9_out, and_10_out, comparator_1_eq, comparator_2_eq, comparator_3_eq, comparator_4_eq,
       comparator_5_eq, comparator_6_eq, comparator_7_eq, comparator_8_eq, comparator_9_eq, comparator_10_eq,
       comparator_11_eq, not_1_out, not_2_out, not_3_out, not_4_out;

  Comparator #(.width(5), .mode("twosComplement")) comparator_1 (
    .a(IDrs2), .b({5{1'b0}}), .eq(comparator_1_eq));  // open: gt, lt
  Comparator #(.width(5), .mode("twosComplement")) comparator_2 (
    .a(IDrs2), .b(Erd), .eq(comparator_2_eq));  // open: gt, lt
  Comparator #(.width(5), .mode("twosComplement")) comparator_3 (
    .a(IDrs1), .b({5{1'b0}}), .eq(comparator_3_eq));  // open: gt, lt
  Comparator #(.width(5), .mode("twosComplement")) comparator_4 (
    .a(IDrs1), .b(Erd), .eq(comparator_4_eq));  // open: gt, lt
  Comparator #(.width(5), .mode("twosComplement")) comparator_5 (
    .a(IDrs1), .b({5{1'b0}}), .eq(comparator_5_eq));  // open: gt, lt
  Comparator #(.width(5), .mode("twosComplement")) comparator_6 (
    .a(IDrs1), .b(Mrd), .eq(comparator_6_eq));  // open: gt, lt
  Comparator #(.width(5), .mode("twosComplement")) comparator_7 (
    .a(IDrs2), .b({5{1'b0}}), .eq(comparator_7_eq));  // open: gt, lt
  Comparator #(.width(5), .mode("twosComplement")) comparator_8 (
    .a(IDrs2), .b(Mrd), .eq(comparator_8_eq));  // open: gt, lt
  Comparator #(.width(5), .mode("twosComplement")) comparator_9 (
    .a(OPcode), .b(5'b01100), .eq(comparator_9_eq));  // open: gt, lt
  Comparator #(.width(5), .mode("twosComplement")) comparator_10 (
    .a(OPcode), .b(5'b01000), .eq(comparator_10_eq));  // open: gt, lt
  Comparator #(.width(5), .mode("twosComplement")) comparator_11 (
    .a(OPcode), .b(5'b11000), .eq(comparator_11_eq));  // open: gt, lt
  not not_1 (not_1_out, comparator_1_eq);
  and and_1 (and_1_out, ERegwrite, comparator_2_eq);
  not not_2 (not_2_out, comparator_3_eq);
  and and_2 (and_2_out, ERegwrite, comparator_4_eq);
  not not_3 (not_3_out, comparator_5_eq);
  and and_3 (and_3_out, MRegWrite, comparator_6_eq);
  not not_4 (not_4_out, comparator_7_eq);
  and and_4 (and_4_out, MRegWrite, comparator_8_eq);
  or or_1 (_2rs, comparator_9_eq, comparator_10_eq, comparator_11_eq, ID_ecall);
  and and_5 (and_5_out, not_1_out, and_1_out);
  and and_6 (and_6_out, not_2_out, and_2_out);
  and and_7 (and_7_out, not_3_out, and_3_out);
  and and_8 (and_8_out, not_4_out, and_4_out);
  and and_9 (and_9_out, _2rs, and_5_out);
  and and_10 (and_10_out, _2rs, and_8_out);
  or or_2 (DataHazzard, and_9_out, and_6_out, and_7_out, and_10_out);

  // Other names for the same wires on the sheet: ERe = ERegwrite; MRe = MRegWrite; rs1[4:0] = IDrs1; rs2[4:0] = IDrs2
endmodule

module Load_Use (
  input  ERegwrite,
  input  [4:0] IDrs1,
  input  [4:0] Erd,
  input  [4:0] IDrs2,
  input  [4:0] OPcode1,
  input  EX_MemToReg,
  output LoadUse
);

  wire _2rs, and_1_out, and_2_out, and_3_out, and_4_out, and_5_out, and_6_out, and_7_out, comparator_1_eq,
       comparator_2_eq, comparator_3_eq, comparator_4_eq, comparator_5_eq, comparator_6_eq, comparator_7_eq,
       not_1_out, not_2_out;

  Comparator #(.width(5), .mode("twosComplement")) comparator_1 (
    .a(IDrs2), .b({5{1'b0}}), .eq(comparator_1_eq));  // open: gt, lt
  not not_1 (not_1_out, comparator_1_eq);
  Comparator #(.width(5), .mode("twosComplement")) comparator_2 (
    .a(IDrs2), .b(Erd), .eq(comparator_2_eq));  // open: gt, lt
  and and_1 (and_1_out, not_1_out, and_2_out);
  and and_2 (and_2_out, ERegwrite, comparator_2_eq);
  Comparator #(.width(5), .mode("twosComplement")) comparator_3 (
    .a(IDrs1), .b({5{1'b0}}), .eq(comparator_3_eq));  // open: gt, lt
  Comparator #(.width(5), .mode("twosComplement")) comparator_4 (
    .a(IDrs1), .b(Erd), .eq(comparator_4_eq));  // open: gt, lt
  Comparator #(.width(5), .mode("twosComplement")) comparator_5 (
    .a(OPcode1), .b(5'b01100), .eq(comparator_5_eq));  // open: gt, lt
  Comparator #(.width(5), .mode("twosComplement")) comparator_6 (
    .a(OPcode1), .b(5'b01000), .eq(comparator_6_eq));  // open: gt, lt
  Comparator #(.width(5), .mode("twosComplement")) comparator_7 (
    .a(OPcode1), .b(5'b11000), .eq(comparator_7_eq));  // open: gt, lt
  not not_2 (not_2_out, comparator_3_eq);
  and and_3 (and_3_out, ERegwrite, comparator_4_eq);
  and and_4 (and_4_out, _2rs, and_1_out);
  and and_5 (and_5_out, not_2_out, and_3_out);
  or or_1 (_2rs, comparator_5_eq, comparator_6_eq, comparator_7_eq);
  and and_6 (and_6_out, and_4_out, EX_MemToReg);
  and and_7 (and_7_out, and_5_out, EX_MemToReg);
  or or_2 (LoadUse, and_6_out, and_7_out);

  // Other names for the same wires on the sheet: ERe = ERegwrite; OPcode[4:0] = OPcode1; rs1[4:0] = IDrs1;
  //   rs2[4:0] = IDrs2
endmodule

module redirect (
  input  ERegwrite,
  input  [4:0] IDrs1,
  input  [4:0] Erd,
  input  [4:0] IDrs2,
  input  [4:0] Mrd,
  input  MRegWrite,
  input  [4:0] OPcode,
  input  ID_ecall,
  output Rt_MEM,
  output Rs_MEM,
  output Rs_WB,
  output Rt_WB
);

  wire _2rs, and_1_out, and_2_out, and_4_out, and_6_out, and_7_out, and_8_out, comparator_1_eq,
       comparator_2_eq, comparator_3_eq, comparator_4_eq, comparator_5_eq, comparator_6_eq, comparator_7_eq,
       comparator_8_eq, comparator_9_eq, comparator_10_eq, comparator_11_eq, not_1_out, not_2_out, not_3_out,
       not_4_out;

  Comparator #(.width(5), .mode("twosComplement")) comparator_1 (
    .a(OPcode), .b(5'b01100), .eq(comparator_1_eq));  // open: gt, lt
  Comparator #(.width(5), .mode("twosComplement")) comparator_2 (
    .a(OPcode), .b(5'b01000), .eq(comparator_2_eq));  // open: gt, lt
  Comparator #(.width(5), .mode("twosComplement")) comparator_3 (
    .a(OPcode), .b(5'b11000), .eq(comparator_3_eq));  // open: gt, lt
  not not_1 (not_1_out, comparator_4_eq);
  Comparator #(.width(5), .mode("twosComplement")) comparator_4 (
    .a(IDrs2), .b({5{1'b0}}), .eq(comparator_4_eq));  // open: gt, lt
  Comparator #(.width(5), .mode("twosComplement")) comparator_5 (
    .a(IDrs2), .b(Erd), .eq(comparator_5_eq));  // open: gt, lt
  not not_2 (not_2_out, comparator_6_eq);
  Comparator #(.width(5), .mode("twosComplement")) comparator_6 (
    .a(IDrs1), .b({5{1'b0}}), .eq(comparator_6_eq));  // open: gt, lt
  Comparator #(.width(5), .mode("twosComplement")) comparator_7 (
    .a(IDrs1), .b(Erd), .eq(comparator_7_eq));  // open: gt, lt
  not not_3 (not_3_out, comparator_8_eq);
  Comparator #(.width(5), .mode("twosComplement")) comparator_8 (
    .a(IDrs1), .b({5{1'b0}}), .eq(comparator_8_eq));  // open: gt, lt
  Comparator #(.width(5), .mode("twosComplement")) comparator_9 (
    .a(IDrs1), .b(Mrd), .eq(comparator_9_eq));  // open: gt, lt
  Comparator #(.width(5), .mode("twosComplement")) comparator_10 (
    .a(IDrs2), .b({5{1'b0}}), .eq(comparator_10_eq));  // open: gt, lt
  not not_4 (not_4_out, comparator_10_eq);
  Comparator #(.width(5), .mode("twosComplement")) comparator_11 (
    .a(IDrs2), .b(Mrd), .eq(comparator_11_eq));  // open: gt, lt
  and and_1 (and_1_out, not_1_out, and_2_out);
  and and_2 (and_2_out, ERegwrite, comparator_5_eq);
  and and_3 (Rs_MEM, not_2_out, and_4_out);
  and and_4 (and_4_out, ERegwrite, comparator_7_eq);
  and and_5 (Rs_WB, not_3_out, and_6_out);
  and and_6 (and_6_out, MRegWrite, comparator_9_eq);
  and and_7 (and_7_out, not_4_out, and_8_out);
  and and_8 (and_8_out, MRegWrite, comparator_11_eq);
  or or_1 (_2rs, comparator_1_eq, comparator_2_eq, comparator_3_eq, ID_ecall);
  and and_9 (Rt_MEM, _2rs, and_1_out);
  and and_10 (Rt_WB, _2rs, and_7_out);

  // Other names for the same wires on the sheet: ERe = ERegwrite; MRe = MRegWrite; rs1[4:0] = IDrs1; rs2[4:0] = IDrs2
endmodule

module ICS (
  input  \_1号中断 ,
  input  \_2号中断 ,
  input  [5:0] in_3,
  input  \_3号中断 ,
  input  \_4号中断 ,
  input  \_5号中断 ,
  input  \同步清零信号 ,
  input  CLK,
  output new_w1,
  output \_1号中断指示灯 ,
  output new_w2,
  output [2:0] \中断号 ,
  output \中断请求 ,
  output \_2号中断指示灯 ,
  output new_w3,
  output \_3号中断指示灯 ,
  output new_w4,
  output \_4号中断指示灯 ,
  output new_w5,
  output \_5号中断指示灯 
);

  wire and_1_out, and_2_out, and_3_out, and_4_out, and_5_out, and_6_out, and_7_out, and_8_out, and_9_out,
       and_10_out, comparator_2_eq, comparator_3_eq, comparator_4_eq, d_ff_1_q, d_ff_2_q, d_ff_3_q, d_ff_4_q,
       d_ff_5_q, empty, or_6_out, or_7_out, or_8_out, or_9_out, or_10_out, or_11_out, register_1_q, rst1,
       rst2, rst3, rst4, rst5;
  wire [2:0] multiplexer_1_out, multiplexer_2_out, register_2_q;

  or or_1 (\_1号中断指示灯 , new_w1, d_ff_1_q);
  or or_2 (\_2号中断指示灯 , new_w2, d_ff_2_q);
  or or_3 (\_3号中断指示灯 , new_w3, d_ff_3_q);
  or or_4 (\_4号中断指示灯 , new_w4, d_ff_4_q);
  or or_5 (\_5号中断指示灯 , new_w5, d_ff_5_q);
  D_Flip_Flop #(.trigger("rising"), .Pre_Clr_Positions("LEGACY"), .NegatePresetClear("false"), .enable("true"), .NewFFLayout("false")) d_ff_1 (
    .clk(\_1号中断 ), .D(1'b1), .Q(d_ff_1_q), .reset(new_w1));  // open: Qn, preset, en
  D_Flip_Flop #(.trigger("rising"), .Pre_Clr_Positions("LEGACY"), .NegatePresetClear("false"), .enable("true"), .NewFFLayout("false")) d_ff_2 (
    .clk(\_2号中断 ), .D(1'b1), .Q(d_ff_2_q), .reset(new_w2));  // open: Qn, preset, en
  D_Flip_Flop #(.trigger("rising"), .Pre_Clr_Positions("LEGACY"), .NegatePresetClear("false"), .enable("true"), .NewFFLayout("false")) d_ff_3 (
    .clk(\_3号中断 ), .D(1'b1), .Q(d_ff_3_q), .reset(new_w3));  // open: Qn, preset, en
  D_Flip_Flop #(.trigger("rising"), .Pre_Clr_Positions("LEGACY"), .NegatePresetClear("false"), .enable("true"), .NewFFLayout("false")) d_ff_4 (
    .clk(\_4号中断 ), .D(1'b1), .Q(d_ff_4_q), .reset(new_w4));  // open: Qn, preset, en
  D_Flip_Flop #(.trigger("rising"), .Pre_Clr_Positions("LEGACY"), .NegatePresetClear("false"), .enable("true"), .NewFFLayout("false")) d_ff_5 (
    .clk(\_5号中断 ), .D(1'b1), .Q(d_ff_5_q), .reset(new_w5));  // open: Qn, preset, en
  or or_6 (or_6_out, d_ff_1_q, new_w1);
  or or_7 (or_7_out, d_ff_2_q, new_w2);
  or or_8 (or_8_out, d_ff_3_q, new_w3);
  or or_9 (or_9_out, d_ff_4_q, new_w4);
  or or_10 (or_10_out, d_ff_5_q, new_w5);
  and and_1 (and_1_out, or_6_out, ~rst1);  // AND_Gate
  and and_2 (and_2_out, or_7_out, ~rst2);  // AND_Gate
  and and_3 (and_3_out, or_8_out, ~rst3);  // AND_Gate
  and and_4 (and_4_out, or_9_out, ~rst4);  // AND_Gate
  and and_5 (and_5_out, or_10_out, ~rst5);  // AND_Gate
  D_Flip_Flop #(.trigger("rising"), .Pre_Clr_Positions("LEGACY"), .NegatePresetClear("false"), .enable("true"), .NewFFLayout("false")) IR1 (
    .clk(CLK), .D(and_1_out), .Q(new_w1));  // open: Qn, preset, en, reset
  D_Flip_Flop #(.trigger("rising"), .Pre_Clr_Positions("LEGACY"), .NegatePresetClear("false"), .enable("true"), .NewFFLayout("false")) IR2 (
    .clk(CLK), .D(and_2_out), .Q(new_w2));  // open: Qn, preset, en, reset
  D_Flip_Flop #(.trigger("rising"), .Pre_Clr_Positions("LEGACY"), .NegatePresetClear("false"), .enable("true"), .NewFFLayout("false")) IR3 (
    .clk(CLK), .D(and_3_out), .Q(new_w3));  // open: Qn, preset, en, reset
  D_Flip_Flop #(.trigger("rising"), .Pre_Clr_Positions("LEGACY"), .NegatePresetClear("false"), .enable("true"), .NewFFLayout("false")) IR4 (
    .clk(CLK), .D(and_4_out), .Q(new_w4));  // open: Qn, preset, en, reset
  D_Flip_Flop #(.trigger("rising"), .Pre_Clr_Positions("LEGACY"), .NegatePresetClear("false"), .enable("true"), .NewFFLayout("false")) IR5 (
    .clk(CLK), .D(and_5_out), .Q(new_w5));  // open: Qn, preset, en, reset
  and and_6 (and_6_out, new_w1, in_3[1]);
  and and_7 (and_7_out, new_w2, in_3[2]);
  and and_8 (and_8_out, new_w3, in_3[3]);
  and and_9 (and_9_out, new_w4, in_3[4]);
  and and_10 (and_10_out, new_w5, in_3[5]);
  Multiplexer #(.select(1), .width(3), .disabled("Z"), .enable("false")) multiplexer_1 (
    .in0(3'b000), .in1(\中断号 ), .out(multiplexer_1_out), .sel(\中断请求 ));
  Priority_Encoder #(.select(3), .disabled("Z")) priority_encoder_1 (
    .in0(1'b0), .in1(and_6_out), .in2(and_7_out), .in3(and_8_out), .in4(and_9_out), .in5(and_10_out),
    .out(\中断号 ), .gs(\中断请求 ));  // open: in6, in7, en_out, en_in
  or or_11 (or_11_out, rst1, rst2, rst3, empty);
  Register #(.width(1), .trigger("rising"), .Select("low")) register_1 (
    .D(or_11_out), .Q(register_1_q), .clk(CLK));  // open: en, clr
  Multiplexer #(.select(1), .width(3), .disabled("Z"), .enable("false")) multiplexer_2 (
    .in0(register_2_q), .in1(multiplexer_1_out), .out(multiplexer_2_out), .sel(register_1_q));
  Register #(.width(3), .trigger("falling"), .Select("low")) register_2 (
    .D(multiplexer_2_out), .Q(register_2_q), .clk(CLK));  // open: en, clr
  Comparator #(.width(3), .mode("twosComplement")) comparator_1 (
    .a(register_2_q), .b(3'b000), .eq(empty));  // open: gt, lt
  Comparator #(.width(3), .mode("twosComplement")) comparator_2 (
    .a(register_2_q), .b(3'b001), .eq(comparator_2_eq));  // open: gt, lt
  Comparator #(.width(3), .mode("twosComplement")) comparator_3 (
    .a(register_2_q), .b(3'b010), .eq(comparator_3_eq));  // open: gt, lt
  Comparator #(.width(3), .mode("twosComplement")) comparator_4 (
    .a(register_2_q), .b(3'b011), .eq(comparator_4_eq));  // open: gt, lt
  and and_11 (rst1, comparator_2_eq, \同步清零信号 );
  and and_12 (rst2, comparator_3_eq, \同步清零信号 );
  and and_13 (rst3, comparator_4_eq, \同步清零信号 );
  // also tied to GND on the sheet: in_3[0]

  // Other names for the same wires on the sheet: uret = \同步清零信号 

  // Notes on the sheet:
  //   Reset 
  //   Reset 
  //   Reset 
  //   Reset 
  //   Reset 
endmodule

module ICM (
  input  \_1号中断 ,
  input  \_2号中断 ,
  input  [3:0] in_3,
  input  \_3号中断 ,
  input  \同步清零信号 ,
  input  CLK,
  output new_w1,
  output \_1号中断指示灯 ,
  output new_w2,
  output [1:0] \中断号 ,
  output \中断请求 ,
  output \_2号中断指示灯 ,
  output new_w3,
  output \_3号中断指示灯 
);

  wire and_1_out, and_2_out, and_3_out, and_4_out, and_5_out, and_6_out, comparator_2_eq, comparator_3_eq,
       comparator_4_eq, d_ff_1_q, d_ff_2_q, d_ff_3_q, empty, or_4_out, or_5_out, or_6_out, rst1, rst2, rst3;
  wire [1:0] multiplexer_1_out, register_1_q;

  or or_1 (\_1号中断指示灯 , new_w1, d_ff_1_q);
  or or_2 (\_2号中断指示灯 , new_w2, d_ff_2_q);
  or or_3 (\_3号中断指示灯 , new_w3, d_ff_3_q);
  D_Flip_Flop #(.trigger("rising"), .Pre_Clr_Positions("LEGACY"), .NegatePresetClear("false"), .enable("true"), .NewFFLayout("false")) d_ff_1 (
    .clk(\_1号中断 ), .D(1'b1), .Q(d_ff_1_q), .reset(new_w1));  // open: Qn, preset, en
  D_Flip_Flop #(.trigger("rising"), .Pre_Clr_Positions("LEGACY"), .NegatePresetClear("false"), .enable("true"), .NewFFLayout("false")) d_ff_2 (
    .clk(\_2号中断 ), .D(1'b1), .Q(d_ff_2_q), .reset(new_w2));  // open: Qn, preset, en
  D_Flip_Flop #(.trigger("rising"), .Pre_Clr_Positions("LEGACY"), .NegatePresetClear("false"), .enable("true"), .NewFFLayout("false")) d_ff_3 (
    .clk(\_3号中断 ), .D(1'b1), .Q(d_ff_3_q), .reset(new_w3));  // open: Qn, preset, en
  or or_4 (or_4_out, d_ff_1_q, new_w1);
  or or_5 (or_5_out, d_ff_2_q, new_w2);
  or or_6 (or_6_out, d_ff_3_q, new_w3);
  and and_1 (and_1_out, or_4_out, ~rst1);  // AND_Gate
  and and_2 (and_2_out, or_5_out, ~rst2);  // AND_Gate
  and and_3 (and_3_out, or_6_out, ~rst3);  // AND_Gate
  D_Flip_Flop #(.trigger("rising"), .Pre_Clr_Positions("LEGACY"), .NegatePresetClear("false"), .enable("true"), .NewFFLayout("false")) IR1 (
    .clk(CLK), .D(and_1_out), .Q(new_w1));  // open: Qn, preset, en, reset
  D_Flip_Flop #(.trigger("rising"), .Pre_Clr_Positions("LEGACY"), .NegatePresetClear("false"), .enable("true"), .NewFFLayout("false")) IR2 (
    .clk(CLK), .D(and_2_out), .Q(new_w2));  // open: Qn, preset, en, reset
  D_Flip_Flop #(.trigger("rising"), .Pre_Clr_Positions("LEGACY"), .NegatePresetClear("false"), .enable("true"), .NewFFLayout("false")) IR3 (
    .clk(CLK), .D(and_3_out), .Q(new_w3));  // open: Qn, preset, en, reset
  and and_4 (and_4_out, new_w1, in_3[1]);
  and and_5 (and_5_out, new_w2, in_3[2]);
  and and_6 (and_6_out, new_w3, in_3[3]);
  Multiplexer #(.select(1), .width(2), .disabled("Z"), .enable("false")) multiplexer_1 (
    .in0(2'b00), .in1(\中断号 ), .out(multiplexer_1_out), .sel(\中断请求 ));
  Priority_Encoder #(.select(2), .disabled("Z")) priority_encoder_1 (
    .in0(1'b0), .in1(and_4_out), .in2(and_5_out), .in3(and_6_out), .out(\中断号 ), .gs(\中断请求 ));  // open: en_out, en_in
  Register #(.width(2), .trigger("falling"), .Select("low")) register_1 (
    .D(multiplexer_1_out), .Q(register_1_q), .clk(CLK));  // open: en, clr
  Comparator #(.width(2), .mode("twosComplement")) comparator_1 (
    .a(register_1_q), .b(2'b00), .eq(empty));  // open: gt, lt
  Comparator #(.width(2), .mode("twosComplement")) comparator_2 (
    .a(register_1_q), .b(2'b01), .eq(comparator_2_eq));  // open: gt, lt
  Comparator #(.width(2), .mode("twosComplement")) comparator_3 (
    .a(register_1_q), .b(2'b10), .eq(comparator_3_eq));  // open: gt, lt
  Comparator #(.width(2), .mode("twosComplement")) comparator_4 (
    .a(register_1_q), .b(2'b11), .eq(comparator_4_eq));  // open: gt, lt
  and and_7 (rst1, comparator_2_eq, \同步清零信号 );
  and and_8 (rst2, comparator_3_eq, \同步清零信号 );
  and and_9 (rst3, comparator_4_eq, \同步清零信号 );

  // Other names for the same wires on the sheet: uret = \同步清零信号 

  // Notes on the sheet:
  //   Reset 
  //   Reset 
  //   Reset 
endmodule

module Interrupt_Block (
  input  In3,
  input  In2,
  input  In1,
  input  s1,
  input  s0,
  output pass
);

  wire and_1_out, and_2_out, and_3_out, and_4_out, not_1_out, not_2_out, not_3_out, not_4_out, not_5_out;

  not not_1 (not_1_out, s1);
  not not_2 (not_2_out, s0);
  not not_3 (not_3_out, s1);
  not not_4 (not_4_out, s1);
  not not_5 (not_5_out, s0);
  and and_1 (and_1_out, In1, not_1_out, not_2_out);
  and and_2 (and_2_out, In2, not_3_out);
  and and_3 (and_3_out, In3, not_4_out);
  and and_4 (and_4_out, In3, not_5_out);
  or or_1 (pass, and_1_out, and_2_out, and_3_out, and_4_out);
endmodule

module multi_Interrupt_jump (
  input  URET,
  input  [1:0] \中断程序号 ,
  input  CLK,
  input  [31:0] nextPC,
  input  [1:0] \中断号 ,
  input  \中断触发 ,
  output [31:0] EPC,
  output clear1
);

  wire comparator_1_eq, comparator_2_eq, comparator_3_eq, d_ff_1_q, d_ff_2_q, d_ff_3_q, d_ff_5_q, d_ff_6_q,
       demultiplexer_1_out1, demultiplexer_1_out2, demultiplexer_1_out3;
  wire [1:0] register_1_q;
  wire [31:0] register_2_q, register_3_q, register_4_q;

  Comparator #(.width(2), .mode("twosComplement")) comparator_1 (
    .a(2'b01), .b(\中断号 ), .eq(comparator_1_eq));  // open: gt, lt
  Register #(.width(2), .trigger("rising"), .Select("low")) register_1 (
    .D(\中断程序号 ), .Q(register_1_q), .clk(CLK));  // open: en, clr
  Register #(.width(32), .trigger("rising"), .Select("low")) register_2 (
    .D(nextPC), .en(comparator_1_eq), .Q(register_2_q), .clk(\中断触发 ), .clr(clear1));
  Demultiplexer #(.select(2), .width(1), .tristate("false"), .disabled("Z"), .enable("false")) demultiplexer_1 (
    .out1(demultiplexer_1_out1), .out2(demultiplexer_1_out2), .out3(demultiplexer_1_out3), .in(URET),
    .sel(register_1_q));  // open: out0
  Comparator #(.width(2), .mode("twosComplement")) comparator_2 (
    .a(2'b10), .b(\中断号 ), .eq(comparator_2_eq));  // open: gt, lt
  D_Flip_Flop #(.trigger("rising"), .Pre_Clr_Positions("LEGACY"), .NegatePresetClear("false"), .enable("true"), .NewFFLayout("false")) d_ff_1 (
    .clk(CLK), .D(demultiplexer_1_out1), .Q(d_ff_1_q));  // open: Qn, preset, en, reset
  D_Flip_Flop #(.trigger("rising"), .Pre_Clr_Positions("LEGACY"), .NegatePresetClear("false"), .enable("true"), .NewFFLayout("false")) d_ff_2 (
    .clk(CLK), .D(demultiplexer_1_out2), .Q(d_ff_2_q));  // open: Qn, preset, en, reset
  D_Flip_Flop #(.trigger("rising"), .Pre_Clr_Positions("LEGACY"), .NegatePresetClear("false"), .enable("true"), .NewFFLayout("false")) d_ff_3 (
    .clk(CLK), .D(demultiplexer_1_out3), .Q(d_ff_3_q));  // open: Qn, preset, en, reset
  Multiplexer #(.select(2), .width(32), .disabled("Z"), .enable("false")) multiplexer_1 (
    .in0({32{1'b0}}), .in1(register_2_q), .in2(register_3_q), .in3(register_4_q), .out(EPC),
    .sel(register_1_q));
  Register #(.width(32), .trigger("rising"), .Select("low")) register_3 (
    .D(nextPC), .en(comparator_2_eq), .Q(register_3_q), .clk(\中断触发 ), .clr(d_ff_5_q));
  D_Flip_Flop #(.trigger("rising"), .Pre_Clr_Positions("LEGACY"), .NegatePresetClear("false"), .enable("true"), .NewFFLayout("false")) d_ff_4 (
    .clk(CLK), .D(d_ff_1_q), .Q(clear1));  // open: Qn, preset, en, reset
  D_Flip_Flop #(.trigger("rising"), .Pre_Clr_Positions("LEGACY"), .NegatePresetClear("false"), .enable("true"), .NewFFLayout("false")) d_ff_5 (
    .clk(CLK), .D(d_ff_2_q), .Q(d_ff_5_q));  // open: Qn, preset, en, reset
  D_Flip_Flop #(.trigger("rising"), .Pre_Clr_Positions("LEGACY"), .NegatePresetClear("false"), .enable("true"), .NewFFLayout("false")) d_ff_6 (
    .clk(CLK), .D(d_ff_3_q), .Q(d_ff_6_q));  // open: Qn, preset, en, reset
  Comparator #(.width(2), .mode("twosComplement")) comparator_3 (
    .a(2'b11), .b(\中断号 ), .eq(comparator_3_eq));  // open: gt, lt
  Register #(.width(32), .trigger("rising"), .Select("low")) register_4 (
    .D(nextPC), .en(comparator_3_eq), .Q(register_4_q), .clk(\中断触发 ), .clr(d_ff_6_q));
endmodule

module BTB (
  input  CLK,
  input  [31:0] PC,
  input  EX_Branch,
  input  EX_BranchTaken,
  input  [31:0] EX_PC,
  input  [31:0] EX_BranchAddr,
  output PredictJump,
  output [31:0] Jumpaddr
);

  \全相联Cache  \u_全相联cache_1  (
    .CLK(CLK), .in_2(PC), .PredictJump(PredictJump), .JumpAddr(Jumpaddr), .Branch(EX_Branch),
    .EX_BranchTaken(EX_BranchTaken), .EX_PC(EX_PC), .EX_DPC(EX_BranchAddr));
endmodule
module \重定向流水线_单级中断  (
  output RegWrite,
  output MemWrite,
  output [31:0] IF_PC,
  output [31:0] ID_PC,
  output [31:0] EX_PC,
  output [31:0] M_PC,
  output [31:0] WB_PC,
  output [31:0] RDin,
  output [31:0] MDin,
  output [31:0] LedData
);

  wire and_1_out, and_2_out, and_3_out, and_4_out, and_5_out, and_6_out, and_7_out, and_8_out, and_9_out,
       and_10_out, Beq, BLTU, Bne, CLK, clock_1_out, comparator_1_eq, comparator_2_eq, comparator_3_eq,
       comparator_4_eq, comparator_5_eq, comparator_5_lt, comparator_6_eq, controlled_inverter_1_out,
       controlled_inverter_2_out, controlled_inverter_3_out, d_ff_2_q, Equal, EX_CSR, EX_ecall,
       ex_mem_1_ex_csr, ex_mem_1_ex_jal, ex_mem_1_ex_jalr, ex_mem_1_ex_lh, ex_mem_1_ex_memtoreg,
       ex_mem_1_mem_halt, EX_MemToReg, EX_RegWrite, Flush, GE, Go, halt, ID_ecall, id_ex_1_ex_alusrcb,
       id_ex_1_ex_lh, id_ex_1_ex_memwrite, id_ex_1_ex_s_type, IE, IR1, IR2, IR3, JAL, JALR, Load_Use,
       MEM_RegWrite, multiplexer_2_out, multiplexer_4_out, nand_1_out, newcontrol_1_out_4,
       newcontrol_1_out_5, newcontrol_1_out_6, newcontrol_1_out_7, newcontrol_1_out_8, newcontrol_1_out_9,
       newcontrol_1_out_10, newcontrol_1_out_11, newcontrol_1_out_12, newcontrol_1_out_14,
       newcontrol_1_out_15, newcontrol_1_out_16, newcontrol_1_out_17, not_1_out, not_3_out, not_4_out,
       not_5_out, not_6_out, not_7_out, not_8_out, not_9_out, not_10_out, not_11_out, not_12_out, not_13_out,
       not_14_out, not_15_out, not_16_out, nW1, nW2, nW3, or_1_out, or_2_out, or_3_out, or_4_out, or_5_out,
       redirect_1_rs_mem, redirect_1_rs_wb, redirect_1_rt_mem, redirect_1_rt_wb, register_2_q, register_4_q,
       Rs_MEM, Rs_WB, RST, Rt_MEM, Rt_WB, URET, W1, W2, W3, WB_CSR, WB_JAL, WB_JALR, WB_LH, WB_MemToReg,
       whichpc_1_out_9, \中断响应 , \中断触发 , \中断请求 ;
  wire [1:0] \中断号 ;
  wire [3:0] id_ex_1_ex_aluop, newcontrol_1_out_13;
  wire [4:0] EX_rd, EX_rs1, MEM_rd, rrs1, rrs2, WB_rd;
  wire [11:0] EX_imm12, EX_imms, immb;
  wire [12:0] CNT_num;
  wire [15:0] \LoadUse次数 , \总周期数 , \插入气泡数 , \无条件分支数 , \条件分支成功数 ;
  wire [19:0] immuj;
  wire [31:0] alu_bin_1_alu_bin, CSR_out, DM_Dout, EPC, EX_ALU_Res, EX_CSR_out, EX_IR, ex_mem_1_mem_csr_out,
       EX_Reg_R1, EX_Reg_R2, ID_CSR_out, ID_IR, ID_Reg_R1, IF_IR, MEM_ALU_Res, MEM_IR, multiplexer_1_out,
       multiplexer_7_out, multiplexer_8_out, multiplexer_9_out, pc_in_1_pc_2, ram_1_data, redirect_Reg_R1,
       redirect_Reg_R2, regifile_1_r2, WB_ALU_Res, WB_IR;

  Button \u_总复位  (.out(RST));
  Button _1 (.out(IR1));
  Button _2 (.out(IR2));
  Button _3 (.out(IR3));
  // Probe on \总周期数 
  // Probe on \总周期数 
  Button \u_继续运行  (.out(Go));
  LED #(.active("true")) led_1 (.in(W1));
  LED #(.active("true")) led_2 (.in(W2));
  LED #(.active("true")) led_3 (.in(W3));
  not not_1 (not_1_out, halt);
  Hex_Digit_Display hex_digit_display_1 (.value(LedData[31:28]));  // open: dp
  // Probe on IF_PC[19:0]
  // RiscV_Probe riscv_probe_1: pin names not known; wires that end beside it: IF_IR
  not not_2 (Flush, whichpc_1_out_9);
  Counter #(.width(16), .max('hffff), .ongoal("wrap"), .trigger("rising"), .behavior("new")) counter_1 (
    .count(not_1_out), .Q(\总周期数 ), .clk(CLK), .clr(RST));  // open: load, D, carry, preset, down
  not not_3 (not_3_out, \中断响应 );
  Comparator #(.width(16), .mode("twosComplement")) comparator_1 (
    .a(16'h23b), .b(\总周期数 ), .eq(comparator_1_eq));  // open: gt, lt
  Comparator #(.width(16), .mode("twosComplement")) comparator_2 (
    .a(\总周期数 ), .b(16'h1), .eq(comparator_2_eq));  // open: gt, lt
  Comparator #(.width(16), .mode("twosComplement")) comparator_3 (
    .a(\总周期数 ), .b(16'h4), .eq(comparator_3_eq));  // open: gt, lt
  Comparator #(.width(16), .mode("twosComplement")) comparator_4 (
    .a(\总周期数 ), .b(16'h7), .eq(comparator_4_eq));  // open: gt, lt
  Hex_Digit_Display hex_digit_display_2 (.value(LedData[23:20]));  // open: dp
  Hex_Digit_Display hex_digit_display_3 (.value(LedData[27:24]));  // open: dp
  // Probe on ID_PC[19:0]
  // RiscV_Probe riscv_probe_2: pin names not known; wires that end beside it: ID_IR
  WhichPC whichpc_1 (
    .out_9(whichpc_1_out_9), .GE(GE), .BLTU(BLTU), .URET(URET), .JALR(JALR), .JAL(JAL), .Beq(Beq), .Bne(Bne),
    .Equal(Equal));
  Multiplexer #(.select(1), .width(32), .disabled("Z"), .enable("false")) multiplexer_1 (
    .in0(EX_PC), .in1(IF_PC), .out(multiplexer_1_out), .sel(whichpc_1_out_9));
  Register #(.width(32), .trigger("rising"), .Select("low")) register_1 (
    .D(EX_PC), .en(and_1_out), .Q(EPC), .clk(CLK), .clr(RST));
  and and_1 (and_1_out, not_3_out, \中断触发 );
  or or_1 (or_1_out, comparator_1_eq, comparator_2_eq);
  assign controlled_inverter_1_out = or_1_out ? ~CLK : 1'bz;  // Controlled_Inverter controlled_inverter_1
  assign controlled_inverter_2_out = comparator_3_eq ? ~CLK : 1'bz;  // Controlled_Inverter controlled_inverter_2
  assign controlled_inverter_3_out = comparator_4_eq ? ~CLK : 1'bz;  // Controlled_Inverter controlled_inverter_3
  Hex_Digit_Display hex_digit_display_4 (.value(LedData[19:16]));  // open: dp
  Hex_Digit_Display hex_digit_display_5 (.value(LedData[15:12]));  // open: dp
  or or_2 (or_2_out, nW1, nW2, nW3);
  Pull_Resistor #(.pull(0)) pull_resistor_1 (.node(controlled_inverter_1_out));
  Pull_Resistor #(.pull(0)) pull_resistor_2 (.node(controlled_inverter_2_out));
  Pull_Resistor #(.pull(0)) pull_resistor_3 (.node(controlled_inverter_3_out));
  Hex_Digit_Display hex_digit_display_6 (.value(LedData[7:4]));  // open: dp
  Hex_Digit_Display hex_digit_display_7 (.value(LedData[11:8]));  // open: dp
  // Probe on EX_PC[19:0]
  // RiscV_Probe riscv_probe_3: pin names not known; wires that end beside it: EX_IR
  and and_2 (and_2_out, or_2_out, IE);
  Hex_Digit_Display hex_digit_display_8 (.value(LedData[3:0]));  // open: dp
  D_Flip_Flop #(.trigger("falling"), .Pre_Clr_Positions("LEGACY"), .NegatePresetClear("false"), .enable("true"), .NewFFLayout("false")) d_ff_1 (
    .clk(CLK), .D(and_2_out), .Q(\中断触发 ));  // open: Qn, preset, en, reset
  PC_in pc_in_1 (
    .PC(multiplexer_1_out), .immb(immb), .immuj(immuj), .ALU_Res(EX_ALU_Res), .\中断编号 (\中断号 ), .EPC(EPC),
    .GE(GE), .BLTU(BLTU), .URET(URET), .JALR(JALR), .JAL(JAL), .Beq(Beq), .Bne(Bne), .Equal(Equal),
    .\中断触发 (\中断触发 ), .PC_2(pc_in_1_pc_2));
  not not_4 (not_4_out, multiplexer_2_out);
  Multiplexer #(.select(1), .width(1), .disabled("Z"), .enable("false")) multiplexer_2 (
    .in0(and_3_out), .in1(and_4_out), .out(multiplexer_2_out), .sel(halt));
  and and_3 (and_3_out, not_5_out, Load_Use);
  not not_5 (not_5_out, Flush);
  not not_6 (not_6_out, Go);
  // Probe on \总周期数 
  // Probe on M_PC[19:0]
  // RiscV_Probe riscv_probe_4: pin names not known; wires that end beside it: MEM_IR
  Register #(.width(32), .trigger("rising"), .Select("low")) PC (
    .D(pc_in_1_pc_2), .en(not_4_out), .Q(IF_PC), .clk(CLK), .clr(RST));
  and and_4 (and_4_out, not_6_out, halt);
  // ICS ics_1: pin names not known; wires that end beside it: IR1, IR2, IR3, 4'b1110, URET, CLK, \中断请求 , \中断号 , W1, W2, W3, nW1, nW2, nW3, nW3, nW3
  // Probe on \总周期数 
  // Probe on \无条件分支数 
  // Probe on \条件分支成功数 
  // Probe on \插入气泡数 
  // Probe on \LoadUse次数 
  not not_7 (not_7_out, \中断触发 );
  not not_8 (not_8_out, \中断响应 );
  // Probe on IF_PC[11:0]
  // Probe on WB_PC[19:0]
  // RiscV_Probe riscv_probe_5: pin names not known; wires that end beside it: WB_IR
  and and_5 (and_5_out, \中断触发 , IE);
  Register #(.width(1), .trigger("rising"), .Select("low")) u_IE (
    .D(not_7_out), .en(not_8_out), .Q(IE), .clk(CLK), .clr(RST));
  // Probe on EX_PC[11:0]
  // Probe on ID_PC[11:0]
  Register #(.width(1), .trigger("rising"), .Select("low")) register_2 (
    .D(and_5_out), .en(not_9_out), .Q(register_2_q), .clk(CLK));  // open: clr
  not not_9 (not_9_out, and_6_out);
  and and_6 (and_6_out, not_10_out, \中断响应 );
  not not_10 (not_10_out, URET);
  ROM #(.addrWidth(10), .dataWidth(32), .Select("high")) rom_1 (.addr(IF_PC[11:2]), .data(IF_IR));
  or or_3 (or_3_out, \中断触发 , Flush);
  // Probe on M_PC[11:0]
  D_Flip_Flop #(.trigger("high"), .Pre_Clr_Positions("LEGACY"), .NegatePresetClear("false"), .enable("true"), .NewFFLayout("false")) d_ff_2 (.Q(d_ff_2_q));  // open: clk, D, Qn, preset, en, reset
  // Probe on 13'h78
  Multiplexer #(.select(1), .width(1), .disabled("Z"), .enable("false")) multiplexer_3 (
    .in0(register_2_q), .in1(1'b0), .out(\中断响应 ), .sel(URET));
  IF_ID if_id_1 (
    .IF_PC(IF_PC), .IF_IR(IF_IR), .ID_PC(ID_PC), .ID_IR(ID_IR), .CLK(CLK), .halt(multiplexer_4_out),
    .Flush(or_3_out));
  Multiplexer #(.select(1), .width(1), .disabled("Z"), .enable("false")) multiplexer_4 (
    .in0(Load_Use), .in1(and_7_out), .out(multiplexer_4_out), .sel(halt));
  and and_7 (and_7_out, not_11_out, halt);
  not not_11 (not_11_out, Go);
  Multiplexer #(.select(1), .width(5), .disabled("Z"), .enable("false")) multiplexer_5 (
    .in0(ID_IR[19:15]), .in1(5'b10001), .out(rrs1), .sel(ID_ecall));
  Multiplexer #(.select(1), .width(5), .disabled("Z"), .enable("false")) multiplexer_6 (
    .in0(ID_IR[24:20]), .in1(5'b01010), .out(rrs2), .sel(ID_ecall));
  // Probe on WB_PC[11:0]
  Comparator #(.width(13), .mode("twosComplement")) comparator_5 (
    .a(CNT_num), .b(13'h78), .eq(comparator_5_eq), .lt(comparator_5_lt));  // open: gt
  Clock #(.highDuration(1), .lowDuration(1)) clock_1 (.out(clock_1_out));
  // RiscV_Probe riscv_probe_6: pin names not known; wires that end beside it: ID_IR
  Reg_Din reg_din_1 (
    .DM_Dout(DM_Dout), .PC(WB_PC), .CSR_out(CSR_out), .ALU_Res(WB_ALU_Res), .LH(WB_LH),
    .MemToReg(WB_MemToReg), .CSR(WB_CSR), .JAL(WB_JAL), .JALR(WB_JALR), .RDin(RDin));
  nand nand_1 (nand_1_out, d_ff_2_q, comparator_5_eq);
  Counter #(.width(13), .max('h1fff), .ongoal("stay"), .trigger("rising"), .behavior("old")) counter_2 (
    .count(comparator_5_lt), .Q(CNT_num), .clk(clock_1_out));  // open: load, D, carry, clr, preset
  Regifile regifile_1 (
    .Din(RDin), .Clk(CLK), .R1(ID_Reg_R1), .R2(regifile_1_r2), .WE(RegWrite), .W_num(WB_rd), .R1_num(rrs1),
    .R2_num(rrs2));
  assign CLK = nand_1_out ? clock_1_out : 1'bz;  // Controlled_Buffer controlled_buffer_1
  Register #(.width(32), .trigger("rising"), .Select("low")) register_3 (
    .D(WB_ALU_Res), .en(WB_CSR), .Q(ID_CSR_out), .clk(CLK), .clr(RST));
  Pull_Resistor #(.pull(1)) pull_resistor_4 (.node(CLK));
  newcontrol newcontrol_1 (
    .out_4(newcontrol_1_out_4), .out_6(newcontrol_1_out_6), .out_8(newcontrol_1_out_8),
    .out_10(newcontrol_1_out_10), .out_12(newcontrol_1_out_12), .out_14(newcontrol_1_out_14),
    .in_1(ID_IR[21]), .in_2(ID_IR[6:2]), .in_3({ID_IR[30], ID_IR[25], ID_IR[14:12]}),
    .out_5(newcontrol_1_out_5), .out_7(newcontrol_1_out_7), .out_9(newcontrol_1_out_9),
    .out_11(newcontrol_1_out_11), .out_13(newcontrol_1_out_13), .out_15(newcontrol_1_out_15),
    .out_16(newcontrol_1_out_16), .out_17(newcontrol_1_out_17), .out_18(ID_ecall));
  redirect redirect_1 (
    .ERegwrite(EX_RegWrite), .IDrs1(rrs1), .Erd(EX_rd), .IDrs2(rrs2), .Mrd(MEM_rd), .MRegWrite(MEM_RegWrite),
    .OPcode(ID_IR[6:2]), .Rt_MEM(redirect_1_rt_mem), .Rs_MEM(redirect_1_rs_mem), .Rs_WB(redirect_1_rs_wb),
    .Rt_WB(redirect_1_rt_wb), .ID_ecall(ID_ecall));
  Load_Use load_use_1 (
    .ERegwrite(EX_RegWrite), .IDrs1(rrs1), .Erd(EX_rd), .IDrs2(rrs2), .OPcode1(ID_IR[6:2]),
    .LoadUse(Load_Use), .EX_MemToReg(EX_MemToReg));
  or or_4 (or_4_out, Load_Use, \中断触发 , Flush);
  ID_EX id_ex_1 (
    .ID_PC(ID_PC), .ID_IR(ID_IR), .ID_rs1(ID_IR[19:15]), .ID_rd(ID_IR[11:7]), .ID_imm12(ID_IR[31:20]),
    .ID_imms({ID_IR[31:25], ID_IR[11:7]}), .ID_immb({ID_IR[31], ID_IR[7], ID_IR[30:25], ID_IR[11:8]}),
    .ID_immuj({ID_IR[31], ID_IR[19:12], ID_IR[20], ID_IR[30:21]}), .ID_Beq(newcontrol_1_out_5),
    .ID_Bne(newcontrol_1_out_7), .ID_MemToReg(newcontrol_1_out_9), .ID_MemWrite(newcontrol_1_out_11),
    .ID_ALUOP(newcontrol_1_out_13), .ID_ALUSrcB(newcontrol_1_out_15), .ID_RegWrite(newcontrol_1_out_16),
    .ID_S_type(newcontrol_1_out_17), .ID_JAL(newcontrol_1_out_4), .ID_JALR(newcontrol_1_out_6),
    .ID_URET(newcontrol_1_out_8), .ID_BLTU(newcontrol_1_out_10), .ID_CSR(newcontrol_1_out_12),
    .ID_LH(newcontrol_1_out_14), .ID_ecall(ID_ecall), .ID_Reg_R2(regifile_1_r2), .ID_CSR_out(ID_CSR_out),
    .EX_PC(EX_PC), .EX_IR(EX_IR), .EX_rs1(EX_rs1), .EX_rd(EX_rd), .EX_imm12(EX_imm12), .EX_imms(EX_imms),
    .EX_immb(immb), .EX_immuj(immuj), .EX_Beq(Beq), .EX_Bne(Bne), .EX_MemToReg(EX_MemToReg),
    .EX_MemWrite(id_ex_1_ex_memwrite), .EX_ALUOP(id_ex_1_ex_aluop), .EX_ALUSrcB(id_ex_1_ex_alusrcb),
    .EX_RegWrite(EX_RegWrite), .EX_S_type(id_ex_1_ex_s_type), .EX_JAL(JAL), .EX_JALR(JALR), .EX_URET(URET),
    .EX_BLTU(BLTU), .EX_CSR(EX_CSR), .EX_LH(id_ex_1_ex_lh), .EX_ecall(EX_ecall), .EX_Reg_R2(EX_Reg_R2),
    .EX_CSR_out(EX_CSR_out), .CLK(CLK), .ID_Reg_R1(ID_Reg_R1), .EX_Reg_R1(EX_Reg_R1), .halt(and_8_out),
    .Flush(or_4_out), .Rt_MEM_2(Rt_MEM), .Rs_MEM_2(Rs_MEM), .Rs_WB_2(Rs_WB), .Rt_WB_2(Rt_WB),
    .Rt_MEM(redirect_1_rt_mem), .Rs_MEM(redirect_1_rs_mem), .Rs_WB(redirect_1_rs_wb), .Rt_WB(redirect_1_rt_wb));
  and and_8 (and_8_out, not_12_out, halt);
  not not_12 (not_12_out, Go);
  Multiplexer #(.select(1), .width(32), .disabled("Z"), .enable("false")) multiplexer_7 (
    .in0(EX_Reg_R1), .in1(RDin), .out(multiplexer_7_out), .sel(Rs_WB));
  Multiplexer #(.select(1), .width(32), .disabled("Z"), .enable("false")) multiplexer_8 (
    .in0(EX_Reg_R2), .in1(RDin), .out(multiplexer_8_out), .sel(Rt_WB));
  Multiplexer #(.select(1), .width(32), .disabled("Z"), .enable("false")) multiplexer_9 (
    .in0(redirect_Reg_R1), .in1(EX_CSR_out), .out(multiplexer_9_out), .sel(EX_CSR));
  ALU_Bin alu_bin_1 (
    .Reg_R2(redirect_Reg_R2), .immb(EX_imm12), .rs1(EX_rs1), .imms(EX_imms), .CSR(EX_CSR),
    .S_type(id_ex_1_ex_s_type), .AluSrcB(id_ex_1_ex_alusrcb), .ALU_Bin(alu_bin_1_alu_bin));
  Multiplexer #(.select(1), .width(32), .disabled("Z"), .enable("false")) multiplexer_10 (
    .in0(multiplexer_7_out), .in1(MEM_ALU_Res), .out(redirect_Reg_R1), .sel(Rs_MEM));
  Multiplexer #(.select(1), .width(32), .disabled("Z"), .enable("false")) multiplexer_11 (
    .in0(multiplexer_8_out), .in1(MEM_ALU_Res), .out(redirect_Reg_R2), .sel(Rt_MEM));
  ALU alu_1 (
    .X(multiplexer_9_out), .Y(alu_bin_1_alu_bin), .AluOP(id_ex_1_ex_aluop), .Equal(Equal),
    .Result(EX_ALU_Res), .out_4(GE));  // open: Result_2, out_6
  not not_13 (not_13_out, comparator_6_eq);
  Comparator #(.width(32), .mode("twosComplement")) comparator_6 (
    .a(32'h22), .b(redirect_Reg_R1), .eq(comparator_6_eq));  // open: gt, lt
  Register #(.width(1), .trigger("rising"), .Select("low")) register_4 (
    .D(not_13_out), .en(EX_ecall), .Q(register_4_q), .clk(CLK), .clr(Go));
  Register #(.width(32), .trigger("rising"), .Select("low")) register_5 (
    .D(redirect_Reg_R2), .en(comparator_6_eq), .Q(LedData), .clk(CLK), .clr(RST));
  EX_MEM ex_mem_1 (
    .EX_PC(EX_PC), .EX_IR(EX_IR), .EX_rd(EX_rd), .ID_MemToReg(EX_MemToReg),
    .ID_MemWrite(id_ex_1_ex_memwrite), .ID_RegWrite(EX_RegWrite), .ID_CSR(EX_CSR), .ID_LH(id_ex_1_ex_lh),
    .EX_Reg_R2(redirect_Reg_R2), .EX_ALU_Res(EX_ALU_Res), .MEM_PC(M_PC), .MEM_IR(MEM_IR), .MEM_rd(MEM_rd),
    .EX_MemToReg(ex_mem_1_ex_memtoreg), .EX_MemWrite(MemWrite), .EX_RegWrite(MEM_RegWrite),
    .EX_CSR(ex_mem_1_ex_csr), .EX_LH(ex_mem_1_ex_lh), .MEM_Reg_R2(MDin), .MEM_ALU_Res(MEM_ALU_Res),
    .CLK(CLK), .halt(or_5_out), .ID_JALR(JALR), .EX_JALR(ex_mem_1_ex_jalr), .ID_JAL(JAL),
    .EX_JAL(ex_mem_1_ex_jal), .EX_CSR_out(EX_CSR_out), .MEM_CSR_out(ex_mem_1_mem_csr_out),
    .EX_halt(register_4_q), .MEM_halt(ex_mem_1_mem_halt));  // open: Flush
  or or_5 (or_5_out, \中断触发 , and_9_out);
  and and_9 (and_9_out, not_14_out, halt);
  not not_14 (not_14_out, Go);
  not not_15 (not_15_out, MemWrite);
  RAM #(.addrWidth(10), .dataWidth(32), .bus("separate"), .Select("high")) ram_1 (
    .addr(MEM_ALU_Res[11:2]), .din(MDin), .data(ram_1_data), .str(MemWrite), .clk(CLK), .ld(not_15_out),
    .clr(RST));  // open: sel
  MEM_WB mem_wb_1 (
    .MEM_PC(M_PC), .MEM_IR(MEM_IR), .MEM_rd(MEM_rd), .ID_MemToReg(ex_mem_1_ex_memtoreg),
    .ID_RegWrite(MEM_RegWrite), .ID_JAL(ex_mem_1_ex_jal), .ID_JALR(ex_mem_1_ex_jalr),
    .ID_CSR(ex_mem_1_ex_csr), .ID_LH(ex_mem_1_ex_lh), .MEM_ALU_Res(MEM_ALU_Res), .WB_PC(WB_PC),
    .WB_IR(WB_IR), .WB_rd(WB_rd), .EX_MemToReg(WB_MemToReg), .EX_RegWrite(RegWrite), .EX_JAL(WB_JAL),
    .EX_JALR(WB_JALR), .EX_CSR(WB_CSR), .EX_LH(WB_LH), .WB_ALU_Res(WB_ALU_Res), .in_15(and_10_out),
    .in_16(CLK), .MEM_DM_Dput(ram_1_data), .WB_DM_Dout(DM_Dout), .MEM_CSR_out(ex_mem_1_mem_csr_out),
    .WB_CSR_out(CSR_out), .MEM_halt(ex_mem_1_mem_halt), .WB_halt(halt));  // open: Flush
  and and_10 (and_10_out, not_16_out, halt);
  not not_16 (not_16_out, Go);

  // Other names for the same wires on the sheet: rd[4:0] = ID_IR[11:7]; ID_rs2[4:0] = ID_IR[24:20];
  //   ID_rs1[4:0] = ID_IR[19:15]; ID_OPcode[4:0] = ID_IR[6:2]; MEM_PC[31:0] = M_PC

  // Notes on the sheet:
  //   中断源
  //   时空图监测，可删除
  //   中断等待指示
  //   单级中断测试信号模拟器
  //   数码管输出
  //   指令存储器
  //   控制位
  //   指令字
  //   contents of rom_1 (hex, n*v repeats v):
  //   7d000113 100413 1f41993 41f9d993 433 c00913 800b13 140413 f47413 800293 100313 499993 89e9b3 1300533
  //   2200893 73 406282b3 fe0294e3 140413 f00f93 1f47433 1c41413 800293 100313 49d993 89e9b3 1300533
  //   2200893 73 406282b3 fe0294e3 1c45413 406b0b33 b0463 f95ff06f 2b3 fff2c293 1029293 fff2e293 500533
  //   2200893 73 f5dff06f 1112023 410113 a12023 410113 812023 410113 1312023 410113 1412023 410113 1512023
  //   410113 1612023 410113 100b13 300a13 100a93 1600433 441413 14469b3 1300533 2200893 73 fe0416e3
  //   415a0a33 fe0a10e3 ffc10113 12b03 ffc10113 12a83 ffc10113 12a03 ffc10113 12983 ffc10113 12403
  //   ffc10113 12503 ffc10113 12883 200073 1112023 410113 a12023 410113 812023 410113 1312023 410113
  //   1412023 410113 1512023 410113 1612023 410113 200b13 300a13 100a93 1600433 441413 14469b3 1300533
  //   2200893 73 fe0416e3 415a0a33 fe0a10e3 ffc10113 12b03 ffc10113 12a83 ffc10113 12a03 ffc10113 12983
  //   ffc10113 12403 ffc10113 12503 ffc10113 12883 200073 1112023 410113 a12023 410113 812023 410113
  //   1312023 410113 1412023 410113 1512023 410113 1612023 410113 300b13 300a13 100a93 1600433 441413
  //   14469b3 1300533 2200893 73 fe0416e3 415a0a33 fe0a10e3 ffc10113 12b03 ffc10113 12a83 ffc10113 12a03
  //   ffc10113 12983 ffc10113 12403 ffc10113 12503 ffc10113 12883 200073
  //   流水调试日志用
  //   暂停节拍，不能为0
  //   指令探针
  //   可计数暂停的时钟源
  //   为方便自动评测，需要输出流水线各段保存的PC值，注意是PC不是PC+4，另外ID段寄存器写入信息，Mem段内存写入信息也要输出
  //   数据存储器
endmodule

module \全相联Cache  (
  input  CLK,
  input  [31:0] in_2,
  input  Branch,
  input  [31:0] EX_PC,
  input  [31:0] EX_DPC,
  input  EX_BranchTaken,
  output PredictJump,
  output [31:0] JumpAddr
);

  wire _404, comparator_1_eq, comparator_2_eq, comparator_3_eq, comparator_4_eq, comparator_5_eq,
       comparator_6_eq, comparator_7_eq, comparator_8_eq, comparator_9_eq, comparator_10_eq,
       comparator_11_eq, comparator_12_eq, comparator_13_eq, comparator_14_eq, comparator_15_eq,
       comparator_16_eq, comparator_17_gt, decoder_1_out0, decoder_1_out1, decoder_1_out2, decoder_1_out3,
       decoder_1_out4, decoder_1_out5, decoder_1_out6, decoder_1_out7, decoder_2_out0, decoder_2_out1,
       decoder_2_out2, decoder_2_out3, decoder_2_out4, decoder_2_out5, decoder_2_out6, decoder_2_out7, empty,
       Find, Hit, L0, L00, L1, L2, L3, L4, L5, L6, L7, L11, L22, L33, L44, L55, L66, L77, Miss,
       multiplexer_1_out, multiplexer_2_out, multiplexer_3_out, multiplexer_4_out, multiplexer_5_out,
       multiplexer_6_out, multiplexer_7_out, multiplexer_8_out, multiplexer_9_out, multiplexer_10_out,
       multiplexer_11_out, multiplexer_12_out, multiplexer_13_out, multiplexer_14_out, multiplexer_15_out,
       multiplexer_16_out, not_1_out, not_2_out, not_3_out, not_4_out, not_5_out, not_6_out, not_7_out,
       not_8_out, not_11_out, not_12_out, not_13_out, not_14_out, not_15_out, not_16_out, not_17_out,
       not_18_out, V0, V1, V2, V3, V4, V5, V6, V7, WriteL0, WriteL1, WriteL2, WriteL3, WriteL4, WriteL5,
       WriteL6, WriteL7;
  wire [1:0] controlled_buffer_1_out, controlled_buffer_9_out, Pre, Pre0, Pre1, Pre2, Pre3, Pre4, Pre5, Pre6,
       Pre7;
  wire [2:0] empty_num, MAX_num, \归并比较电路_max3_1_max_num , \归并比较电路_max3_2_max_num , \归并比较电路_max3_3_max_num ,
       \归并比较电路_max3_4_max_num , \归并比较电路_max3_5_max_num , \归并比较电路_max3_6_max_num ;
  wire [15:0] MAX, Out0, Out1, Out2, Out3, Out4, Out5, Out6, Out7, \归并比较电路_max3_1_max , \归并比较电路_max3_2_max ,
       \归并比较电路_max3_3_max , \归并比较电路_max3_4_max , \归并比较电路_max3_5_max , \归并比较电路_max3_6_max ;
  wire [31:0] BPC0, BPC1, BPC2, BPC3, BPC4, BPC5, BPC6, BPC7, controlled_buffer_17_out, DPC0, DPC1, DPC2,
       DPC3, DPC4, DPC5, DPC6, DPC7;

  Register #(.width(1), .trigger("rising"), .Select("low")) register_1 (
    .D(1'b1), .en(WriteL0), .Q(V0), .clk(CLK));  // open: clr
  Register #(.width(1), .trigger("rising"), .Select("low")) register_2 (
    .D(1'b1), .en(WriteL1), .Q(V1), .clk(CLK));  // open: clr
  Register #(.width(1), .trigger("rising"), .Select("low")) register_3 (
    .D(1'b1), .en(WriteL2), .Q(V2), .clk(CLK));  // open: clr
  Register #(.width(1), .trigger("rising"), .Select("low")) register_4 (
    .D(1'b1), .en(WriteL3), .Q(V3), .clk(CLK));  // open: clr
  Register #(.width(1), .trigger("rising"), .Select("low")) register_5 (
    .D(1'b1), .en(WriteL4), .Q(V4), .clk(CLK));  // open: clr
  Register #(.width(1), .trigger("rising"), .Select("low")) register_6 (
    .D(1'b1), .en(WriteL5), .Q(V5), .clk(CLK));  // open: clr
  Register #(.width(1), .trigger("rising"), .Select("low")) register_7 (
    .D(1'b1), .en(WriteL6), .Q(V6), .clk(CLK));  // open: clr
  Register #(.width(1), .trigger("rising"), .Select("low")) register_8 (
    .D(1'b1), .en(WriteL7), .Q(V7), .clk(CLK));  // open: clr
  Register #(.width(32), .trigger("rising"), .Select("low")) register_9 (
    .D(EX_PC), .en(WriteL0), .Q(BPC0), .clk(CLK));  // open: clr
  Register #(.width(32), .trigger("rising"), .Select("low")) register_10 (
    .D(EX_PC), .en(WriteL1), .Q(BPC1), .clk(CLK));  // open: clr
  Register #(.width(32), .trigger("rising"), .Select("low")) register_11 (
    .D(EX_PC), .en(WriteL2), .Q(BPC2), .clk(CLK));  // open: clr
  Register #(.width(32), .trigger("rising"), .Select("low")) register_12 (
    .D(EX_PC), .en(WriteL3), .Q(BPC3), .clk(CLK));  // open: clr
  Register #(.width(32), .trigger("rising"), .Select("low")) register_13 (
    .D(EX_PC), .en(WriteL4), .Q(BPC4), .clk(CLK));  // open: clr
  Register #(.width(32), .trigger("rising"), .Select("low")) register_14 (
    .D(EX_PC), .en(WriteL5), .Q(BPC5), .clk(CLK));  // open: clr
  Register #(.width(32), .trigger("rising"), .Select("low")) register_15 (
    .D(EX_PC), .en(WriteL6), .Q(BPC6), .clk(CLK));  // open: clr
  Register #(.width(32), .trigger("rising"), .Select("low")) register_16 (
    .D(EX_PC), .en(WriteL7), .Q(BPC7), .clk(CLK));  // open: clr
  Register #(.width(32), .trigger("rising"), .Select("low")) register_17 (
    .D(EX_DPC), .en(WriteL0), .Q(DPC0), .clk(CLK));  // open: clr
  Register #(.width(32), .trigger("rising"), .Select("low")) register_18 (
    .D(EX_DPC), .en(WriteL1), .Q(DPC1), .clk(CLK));  // open: clr
  Register #(.width(32), .trigger("rising"), .Select("low")) register_19 (
    .D(EX_DPC), .en(WriteL2), .Q(DPC2), .clk(CLK));  // open: clr
  Register #(.width(32), .trigger("rising"), .Select("low")) register_20 (
    .D(EX_DPC), .en(WriteL3), .Q(DPC3), .clk(CLK));  // open: clr
  Register #(.width(32), .trigger("rising"), .Select("low")) register_21 (
    .D(EX_DPC), .en(WriteL4), .Q(DPC4), .clk(CLK));  // open: clr
  Register #(.width(32), .trigger("rising"), .Select("low")) register_22 (
    .D(EX_DPC), .en(WriteL5), .Q(DPC5), .clk(CLK));  // open: clr
  Register #(.width(32), .trigger("rising"), .Select("low")) register_23 (
    .D(EX_DPC), .en(WriteL6), .Q(DPC6), .clk(CLK));  // open: clr
  Register #(.width(32), .trigger("rising"), .Select("low")) register_24 (
    .D(EX_DPC), .en(WriteL7), .Q(DPC7), .clk(CLK));  // open: clr
  Register #(.width(2), .trigger("rising"), .Select("low")) register_25 (
    .D(Pre), .en(WriteL0), .Q(Pre0), .clk(CLK), .clr(not_1_out));
  not not_1 (not_1_out, V0);
  Register #(.width(2), .trigger("rising"), .Select("low")) register_26 (
    .D(Pre), .en(WriteL1), .Q(Pre1), .clk(CLK), .clr(not_2_out));
  not not_2 (not_2_out, V1);
  Register #(.width(2), .trigger("rising"), .Select("low")) register_27 (
    .D(Pre), .en(WriteL2), .Q(Pre2), .clk(CLK), .clr(not_3_out));
  not not_3 (not_3_out, V2);
  Register #(.width(2), .trigger("rising"), .Select("low")) register_28 (
    .D(Pre), .en(WriteL3), .Q(Pre3), .clk(CLK), .clr(not_4_out));
  not not_4 (not_4_out, V3);
  Register #(.width(2), .trigger("rising"), .Select("low")) register_29 (
    .D(Pre), .en(WriteL4), .Q(Pre4), .clk(CLK), .clr(not_5_out));
  not not_5 (not_5_out, V4);
  Register #(.width(2), .trigger("rising"), .Select("low")) register_30 (
    .D(Pre), .en(WriteL5), .Q(Pre5), .clk(CLK), .clr(not_6_out));
  not not_6 (not_6_out, V5);
  Register #(.width(2), .trigger("rising"), .Select("low")) register_31 (
    .D(Pre), .en(WriteL6), .Q(Pre6), .clk(CLK), .clr(not_7_out));
  not not_7 (not_7_out, V6);
  Register #(.width(2), .trigger("rising"), .Select("low")) register_32 (
    .D(Pre), .en(WriteL7), .Q(Pre7), .clk(CLK), .clr(not_8_out));
  not not_8 (not_8_out, V7);
  Counter #(.width(16), .max('hffff), .ongoal("stay"), .trigger("rising"), .behavior("new")) out_cnt0 (
    .load(WriteL0), .D({16{1'b0}}), .Q(Out0), .clk(CLK));  // open: count, carry, clr, preset, down
  Counter #(.width(16), .max('hffff), .ongoal("stay"), .trigger("rising"), .behavior("new")) out_cnt1 (
    .load(WriteL1), .D({16{1'b0}}), .Q(Out1), .clk(CLK));  // open: count, carry, clr, preset, down
  Counter #(.width(16), .max('hffff), .ongoal("stay"), .trigger("rising"), .behavior("new")) out_cnt2 (
    .load(WriteL2), .D({16{1'b0}}), .Q(Out2), .clk(CLK));  // open: count, carry, clr, preset, down
  Counter #(.width(16), .max('hffff), .ongoal("stay"), .trigger("rising"), .behavior("new")) out_cnt3 (
    .load(WriteL3), .D({16{1'b0}}), .Q(Out3), .clk(CLK));  // open: count, carry, clr, preset, down
  Counter #(.width(16), .max('hffff), .ongoal("stay"), .trigger("rising"), .behavior("new")) out_cnt4 (
    .load(WriteL4), .D({16{1'b0}}), .Q(Out4), .clk(CLK));  // open: count, carry, clr, preset, down
  Counter #(.width(16), .max('hffff), .ongoal("stay"), .trigger("rising"), .behavior("new")) out_cnt5 (
    .load(WriteL5), .D({16{1'b0}}), .Q(Out5), .clk(CLK));  // open: count, carry, clr, preset, down
  Counter #(.width(16), .max('hffff), .ongoal("stay"), .trigger("rising"), .behavior("new")) out_cnt6 (
    .load(WriteL6), .D({16{1'b0}}), .Q(Out6), .clk(CLK));  // open: count, carry, clr, preset, down
  Counter #(.width(16), .max('hffff), .ongoal("stay"), .trigger("rising"), .behavior("new")) out_cnt7 (
    .load(WriteL7), .D({16{1'b0}}), .Q(Out7), .clk(CLK));  // open: count, carry, clr, preset, down
  Decoder #(.select(3), .tristate("false"), .disabled("Z"), .enable("false")) decoder_1 (
    .out0(decoder_1_out0), .out1(decoder_1_out1), .out2(decoder_1_out2), .out3(decoder_1_out3),
    .out4(decoder_1_out4), .out5(decoder_1_out5), .out6(decoder_1_out6), .out7(decoder_1_out7), .sel(MAX_num));
  Comparator #(.width(32), .mode("twosComplement")) comparator_1 (
    .a(BPC0), .b(in_2), .eq(comparator_1_eq));  // open: gt, lt
  Comparator #(.width(32), .mode("twosComplement")) comparator_2 (
    .a(BPC1), .b(in_2), .eq(comparator_2_eq));  // open: gt, lt
  Comparator #(.width(32), .mode("twosComplement")) comparator_3 (
    .a(BPC2), .b(in_2), .eq(comparator_3_eq));  // open: gt, lt
  Comparator #(.width(32), .mode("twosComplement")) comparator_4 (
    .a(BPC3), .b(in_2), .eq(comparator_4_eq));  // open: gt, lt
  Comparator #(.width(32), .mode("twosComplement")) comparator_5 (
    .a(BPC4), .b(in_2), .eq(comparator_5_eq));  // open: gt, lt
  Comparator #(.width(32), .mode("twosComplement")) comparator_6 (
    .a(BPC5), .b(in_2), .eq(comparator_6_eq));  // open: gt, lt
  Comparator #(.width(32), .mode("twosComplement")) comparator_7 (
    .a(BPC6), .b(in_2), .eq(comparator_7_eq));  // open: gt, lt
  Comparator #(.width(32), .mode("twosComplement")) comparator_8 (
    .a(BPC7), .b(in_2), .eq(comparator_8_eq));  // open: gt, lt
  Comparator #(.width(32), .mode("twosComplement")) comparator_9 (
    .a(BPC0), .b(EX_PC), .eq(comparator_9_eq));  // open: gt, lt
  Comparator #(.width(32), .mode("twosComplement")) comparator_10 (
    .a(BPC1), .b(EX_PC), .eq(comparator_10_eq));  // open: gt, lt
  Comparator #(.width(32), .mode("twosComplement")) comparator_11 (
    .a(BPC2), .b(EX_PC), .eq(comparator_11_eq));  // open: gt, lt
  Comparator #(.width(32), .mode("twosComplement")) comparator_12 (
    .a(BPC3), .b(EX_PC), .eq(comparator_12_eq));  // open: gt, lt
  Comparator #(.width(32), .mode("twosComplement")) comparator_13 (
    .a(BPC4), .b(EX_PC), .eq(comparator_13_eq));  // open: gt, lt
  Comparator #(.width(32), .mode("twosComplement")) comparator_14 (
    .a(BPC5), .b(EX_PC), .eq(comparator_14_eq));  // open: gt, lt
  Comparator #(.width(32), .mode("twosComplement")) comparator_15 (
    .a(BPC6), .b(EX_PC), .eq(comparator_15_eq));  // open: gt, lt
  Comparator #(.width(32), .mode("twosComplement")) comparator_16 (
    .a(BPC7), .b(EX_PC), .eq(comparator_16_eq));  // open: gt, lt
  Decoder #(.select(3), .tristate("false"), .disabled("Z"), .enable("false")) decoder_2 (
    .out0(decoder_2_out0), .out1(decoder_2_out1), .out2(decoder_2_out2), .out3(decoder_2_out3),
    .out4(decoder_2_out4), .out5(decoder_2_out5), .out6(decoder_2_out6), .out7(decoder_2_out7),
    .sel(empty_num));
  and and_1 (L00, comparator_1_eq, V0);
  and and_2 (L11, comparator_2_eq, V1);
  and and_3 (L22, comparator_3_eq, V2);
  and and_4 (L33, comparator_4_eq, V3);
  and and_5 (L44, comparator_5_eq, V4);
  and and_6 (L55, comparator_6_eq, V5);
  and and_7 (L66, comparator_7_eq, V6);
  and and_8 (L77, comparator_8_eq, V7);
  and and_9 (L0, comparator_9_eq, V0);
  and and_10 (L1, comparator_10_eq, V1);
  and and_11 (L2, comparator_11_eq, V2);
  and and_12 (L3, comparator_12_eq, V3);
  and and_13 (L4, comparator_13_eq, V4);
  and and_14 (L5, comparator_14_eq, V5);
  and and_15 (L6, comparator_15_eq, V6);
  and and_16 (L7, comparator_16_eq, V7);
  Multiplexer #(.select(1), .width(1), .disabled("Z"), .enable("false")) multiplexer_1 (
    .in0(decoder_1_out0), .in1(decoder_2_out0), .out(multiplexer_1_out), .sel(empty));
  Multiplexer #(.select(1), .width(1), .disabled("Z"), .enable("false")) multiplexer_2 (
    .in0(decoder_1_out1), .in1(decoder_2_out1), .out(multiplexer_2_out), .sel(empty));
  Multiplexer #(.select(1), .width(1), .disabled("Z"), .enable("false")) multiplexer_3 (
    .in0(decoder_1_out2), .in1(decoder_2_out2), .out(multiplexer_3_out), .sel(empty));
  Multiplexer #(.select(1), .width(1), .disabled("Z"), .enable("false")) multiplexer_4 (
    .in0(decoder_1_out3), .in1(decoder_2_out3), .out(multiplexer_4_out), .sel(empty));
  Multiplexer #(.select(1), .width(1), .disabled("Z"), .enable("false")) multiplexer_5 (
    .in0(decoder_1_out4), .in1(decoder_2_out4), .out(multiplexer_5_out), .sel(empty));
  Multiplexer #(.select(1), .width(1), .disabled("Z"), .enable("false")) multiplexer_6 (
    .in0(decoder_1_out5), .in1(decoder_2_out5), .out(multiplexer_6_out), .sel(empty));
  Multiplexer #(.select(1), .width(1), .disabled("Z"), .enable("false")) multiplexer_7 (
    .in0(decoder_1_out6), .in1(decoder_2_out6), .out(multiplexer_7_out), .sel(empty));
  Multiplexer #(.select(1), .width(1), .disabled("Z"), .enable("false")) multiplexer_8 (
    .in0(decoder_1_out7), .in1(decoder_2_out7), .out(multiplexer_8_out), .sel(empty));
  or or_1 (Find, L00, L11, L22, L33, L44, L55, L66, L77);
  or or_2 (Hit, L0, L1, L2, L3, L4, L5, L6, L7);
  not not_9 (_404, Find);
  not not_10 (Miss, Hit);
  Multiplexer #(.select(1), .width(1), .disabled("Z"), .enable("false")) multiplexer_9 (
    .in0(multiplexer_1_out), .in1(L0), .out(multiplexer_9_out), .sel(Hit));
  Multiplexer #(.select(1), .width(1), .disabled("Z"), .enable("false")) multiplexer_10 (
    .in0(multiplexer_2_out), .in1(L1), .out(multiplexer_10_out), .sel(Hit));
  Multiplexer #(.select(1), .width(1), .disabled("Z"), .enable("false")) multiplexer_11 (
    .in0(multiplexer_3_out), .in1(L2), .out(multiplexer_11_out), .sel(Hit));
  Multiplexer #(.select(1), .width(1), .disabled("Z"), .enable("false")) multiplexer_12 (
    .in0(multiplexer_4_out), .in1(L3), .out(multiplexer_12_out), .sel(Hit));
  Multiplexer #(.select(1), .width(1), .disabled("Z"), .enable("false")) multiplexer_13 (
    .in0(multiplexer_5_out), .in1(L4), .out(multiplexer_13_out), .sel(Hit));
  Multiplexer #(.select(1), .width(1), .disabled("Z"), .enable("false")) multiplexer_14 (
    .in0(multiplexer_6_out), .in1(L5), .out(multiplexer_14_out), .sel(Hit));
  Multiplexer #(.select(1), .width(1), .disabled("Z"), .enable("false")) multiplexer_15 (
    .in0(multiplexer_7_out), .in1(L6), .out(multiplexer_15_out), .sel(Hit));
  Multiplexer #(.select(1), .width(1), .disabled("Z"), .enable("false")) multiplexer_16 (
    .in0(multiplexer_8_out), .in1(L7), .out(multiplexer_16_out), .sel(Hit));
  and and_17 (WriteL0, multiplexer_9_out, Branch);
  and and_18 (WriteL1, multiplexer_10_out, Branch);
  and and_19 (WriteL2, multiplexer_11_out, Branch);
  and and_20 (WriteL3, multiplexer_12_out, Branch);
  and and_21 (WriteL4, multiplexer_13_out, Branch);
  and and_22 (WriteL5, multiplexer_14_out, Branch);
  and and_23 (WriteL6, multiplexer_15_out, Branch);
  and and_24 (WriteL7, multiplexer_16_out, Branch);
  assign controlled_buffer_1_out = L00 ? Pre0 : 2'bz;  // Controlled_Buffer controlled_buffer_1
  assign controlled_buffer_1_out = L11 ? Pre1 : 2'bz;  // Controlled_Buffer controlled_buffer_2
  assign controlled_buffer_1_out = L22 ? Pre2 : 2'bz;  // Controlled_Buffer controlled_buffer_3
  assign controlled_buffer_1_out = L33 ? Pre3 : 2'bz;  // Controlled_Buffer controlled_buffer_4
  assign controlled_buffer_1_out = L44 ? Pre4 : 2'bz;  // Controlled_Buffer controlled_buffer_5
  assign controlled_buffer_1_out = L55 ? Pre5 : 2'bz;  // Controlled_Buffer controlled_buffer_6
  assign controlled_buffer_1_out = L66 ? Pre6 : 2'bz;  // Controlled_Buffer controlled_buffer_7
  assign controlled_buffer_1_out = L77 ? Pre7 : 2'bz;  // Controlled_Buffer controlled_buffer_8
  assign controlled_buffer_9_out = L0 ? Pre0 : 2'bz;  // Controlled_Buffer controlled_buffer_9
  assign controlled_buffer_9_out = L1 ? Pre1 : 2'bz;  // Controlled_Buffer controlled_buffer_10
  assign controlled_buffer_9_out = L2 ? Pre2 : 2'bz;  // Controlled_Buffer controlled_buffer_11
  assign controlled_buffer_9_out = L3 ? Pre3 : 2'bz;  // Controlled_Buffer controlled_buffer_12
  assign controlled_buffer_9_out = L4 ? Pre4 : 2'bz;  // Controlled_Buffer controlled_buffer_13
  assign controlled_buffer_9_out = L5 ? Pre5 : 2'bz;  // Controlled_Buffer controlled_buffer_14
  assign controlled_buffer_9_out = L6 ? Pre6 : 2'bz;  // Controlled_Buffer controlled_buffer_15
  assign controlled_buffer_9_out = L7 ? Pre7 : 2'bz;  // Controlled_Buffer controlled_buffer_16
  Comparator #(.width(2), .mode("unsigned")) comparator_17 (
    .a(controlled_buffer_1_out), .b(2'b01), .gt(comparator_17_gt));  // open: eq, lt
  Multiplexer #(.select(1), .width(1), .disabled("Z"), .enable("false")) multiplexer_17 (
    .in0(1'b0), .in1(comparator_17_gt), .out(PredictJump), .sel(Find));
  \双位预测状态机  \u_双位预测状态机_1  (
    .S1(controlled_buffer_9_out[1]), .S0(controlled_buffer_9_out[0]), .jump(EX_BranchTaken), .N1(Pre[1]),
    .N0(Pre[0]));
  \归并比较电路_MAX3  \u_归并比较电路_max3_1  (
    .Y(Out0), .MAX(\归并比较电路_max3_1_max ), .X(Out1), .Y_num(3'b000), .Max_num(\归并比较电路_max3_1_max_num ),
    .X_num(3'b001));
  \归并比较电路_MAX3  \u_归并比较电路_max3_2  (
    .Y(Out2), .MAX(\归并比较电路_max3_2_max ), .X(Out3), .Y_num(3'b010), .Max_num(\归并比较电路_max3_2_max_num ),
    .X_num(3'b011));
  \归并比较电路_MAX3  \u_归并比较电路_max3_3  (
    .Y(Out4), .MAX(\归并比较电路_max3_3_max ), .X(Out5), .Y_num(3'b100), .Max_num(\归并比较电路_max3_3_max_num ),
    .X_num(3'b101));
  \归并比较电路_MAX3  \u_归并比较电路_max3_4  (
    .Y(Out6), .MAX(\归并比较电路_max3_4_max ), .X(Out7), .Y_num(3'b110), .Max_num(\归并比较电路_max3_4_max_num ),
    .X_num(3'b111));
  assign controlled_buffer_17_out = L00 ? DPC0 : 32'bz;  // Controlled_Buffer controlled_buffer_17
  assign controlled_buffer_17_out = L11 ? DPC1 : 32'bz;  // Controlled_Buffer controlled_buffer_18
  assign controlled_buffer_17_out = L22 ? DPC2 : 32'bz;  // Controlled_Buffer controlled_buffer_19
  assign controlled_buffer_17_out = L33 ? DPC3 : 32'bz;  // Controlled_Buffer controlled_buffer_20
  assign controlled_buffer_17_out = L44 ? DPC4 : 32'bz;  // Controlled_Buffer controlled_buffer_21
  assign controlled_buffer_17_out = L55 ? DPC5 : 32'bz;  // Controlled_Buffer controlled_buffer_22
  assign controlled_buffer_17_out = L66 ? DPC6 : 32'bz;  // Controlled_Buffer controlled_buffer_23
  assign controlled_buffer_17_out = L77 ? DPC7 : 32'bz;  // Controlled_Buffer controlled_buffer_24
  not not_11 (not_11_out, V0);
  not not_12 (not_12_out, V1);
  not not_13 (not_13_out, V2);
  not not_14 (not_14_out, V3);
  not not_15 (not_15_out, V4);
  not not_16 (not_16_out, V5);
  not not_17 (not_17_out, V6);
  not not_18 (not_18_out, V7);
  \归并比较电路_MAX3  \u_归并比较电路_max3_5  (
    .Y(\归并比较电路_max3_1_max ), .MAX(\归并比较电路_max3_5_max ), .X(\归并比较电路_max3_2_max ),
    .Y_num(\归并比较电路_max3_1_max_num ), .Max_num(\归并比较电路_max3_5_max_num ), .X_num(\归并比较电路_max3_2_max_num ));
  \归并比较电路_MAX3  \u_归并比较电路_max3_6  (
    .Y(\归并比较电路_max3_3_max ), .MAX(\归并比较电路_max3_6_max ), .X(\归并比较电路_max3_4_max ),
    .Y_num(\归并比较电路_max3_3_max_num ), .Max_num(\归并比较电路_max3_6_max_num ), .X_num(\归并比较电路_max3_4_max_num ));
  Multiplexer #(.select(1), .width(32), .disabled("Z"), .enable("false")) multiplexer_18 (
    .in0({32{1'b0}}), .in1(controlled_buffer_17_out), .out(JumpAddr), .sel(Find));
  \归并比较电路_MAX3  \u_归并比较电路_max3_7  (
    .Y(\归并比较电路_max3_5_max ), .MAX(MAX), .X(\归并比较电路_max3_6_max ), .Y_num(\归并比较电路_max3_5_max_num ),
    .Max_num(MAX_num), .X_num(\归并比较电路_max3_6_max_num ));
  Priority_Encoder #(.select(3), .disabled("Z")) priority_encoder_1 (
    .in0(not_11_out), .in1(not_12_out), .in2(not_13_out), .in3(not_14_out), .in4(not_15_out),
    .in5(not_16_out), .in6(not_17_out), .in7(not_18_out), .out(empty_num), .gs(empty));  // open: en_out, en_in

  // Other names for the same wires on the sheet: BPC[31:0] = EX_PC; DPC[31:0] = EX_DPC; PC[31:0] = in_2
endmodule

module \双位预测状态机  (
  input  S1,
  input  S0,
  input  jump,
  output N1,
  output N0
);

  wire and_1_out, and_2_out, and_3_out, and_4_out, not_1_out, not_2_out, not_3_out, not_4_out, not_5_out;

  not not_1 (not_1_out, S0);
  not not_2 (not_2_out, S1);
  not not_3 (not_3_out, S0);
  not not_4 (not_4_out, S0);
  not not_5 (not_5_out, jump);
  and and_1 (and_1_out, S0, jump);
  and and_2 (and_2_out, S1, not_1_out);
  and and_3 (and_3_out, not_2_out, not_3_out, jump);
  and and_4 (and_4_out, S1, not_4_out, not_5_out);
  or or_1 (N1, and_1_out, and_2_out);
  or or_2 (N0, and_3_out, and_4_out);
endmodule

module \归并比较电路_MAX3  (
  input  [15:0] Y,
  input  [15:0] X,
  input  [2:0] Y_num,
  input  [2:0] X_num,
  output [15:0] MAX,
  output [2:0] Max_num
);

  wire comparator_1_eq, comparator_1_gt, or_1_out;

  Multiplexer #(.select(1), .width(16), .disabled("Z"), .enable("false")) multiplexer_1 (
    .in0(Y), .in1(X), .out(MAX), .sel(or_1_out));
  Comparator #(.width(16), .mode("unsigned")) comparator_1 (
    .a(X), .b(Y), .gt(comparator_1_gt), .eq(comparator_1_eq));  // open: lt
  or or_1 (or_1_out, comparator_1_gt, comparator_1_eq);
  Multiplexer #(.select(1), .width(3), .disabled("Z"), .enable("false")) multiplexer_2 (
    .in0(Y_num), .in1(X_num), .out(Max_num), .sel(or_1_out));

  // Notes on the sheet:
  //   输出两个输入中的较大值，并输出较大值的3位编号
endmodule

module \重定向流水线_动态分支预测  (
  output RegWrite,
  output MemWrite,
  output [31:0] IF_PC,
  output [31:0] ID_PC,
  output [31:0] EX_PC,
  output [31:0] M_PC,
  output [31:0] WB_PC,
  output [31:0] RDin,
  output [31:0] MDin,
  output [31:0] LedData
);

  wire and_2_out, and_3_out, and_4_out, and_5_out, and_6_out, and_7_out, and_8_out, Beq, BLTU, Bne, CLK,
       clock_1_out, comparator_1_eq, comparator_1_lt, comparator_2_eq, d_ff_1_q, Equal, EX_Branch,
       EX_BranchTaken, EX_CSR, EX_ecall, ex_mem_1_ex_csr, ex_mem_1_ex_jal, ex_mem_1_ex_jalr, ex_mem_1_ex_lh,
       ex_mem_1_ex_memtoreg, ex_mem_1_mem_halt, EX_MemToReg, EX_RegWrite, Flush, GE, Go, halt, ID_ecall,
       id_ex_1_ex_alusrcb, id_ex_1_ex_lh, id_ex_1_ex_memwrite, id_ex_1_ex_s_type, IF_predictJump, IR1, IR2,
       IR3, JAL, JALR, Load_Use, MEM_RegWrite, multiplexer_3_out, multiplexer_5_out, multiplexer_6_out,
       multiplexer_9_out, nand_1_out, newcontrol_1_out_4, newcontrol_1_out_5, newcontrol_1_out_6,
       newcontrol_1_out_7, newcontrol_1_out_8, newcontrol_1_out_9, newcontrol_1_out_10, newcontrol_1_out_11,
       newcontrol_1_out_12, newcontrol_1_out_14, newcontrol_1_out_15, newcontrol_1_out_16,
       newcontrol_1_out_17, not_2_out, not_3_out, not_4_out, not_5_out, not_6_out, not_7_out, not_8_out,
       not_9_out, not_10_out, not_11_out, not_12_out, not_13_out, or_2_out, or_3_out, or_4_out, or_5_out,
       or_6_out, PredictErr, redirect_1_rs_mem, redirect_1_rs_wb, redirect_1_rt_mem, redirect_1_rt_wb,
       register_1_q, register_3_q, register_4_q, Rs_MEM, Rs_WB, RST, Rt_MEM, Rt_WB, URET, W1, W2, W3, WB_CSR,
       WB_JAL, WB_JALR, WB_LH, WB_MemToReg, whichpc_1_out_9;
  wire [1:0] undriven, undriven_2;
  wire [3:0] id_ex_1_ex_aluop, newcontrol_1_out_13;
  wire [4:0] EX_rd, EX_rs1, MEM_rd, rrs1, rrs2, WB_rd;
  wire [11:0] EX_imm12, EX_imms, immb;
  wire [12:0] CNT_num;
  wire [15:0] \LoadUse次数 , \总周期数 , \插入气泡数 , \无条件分支数 , \条件分支成功数 ;
  wire [19:0] immuj;
  wire [31:0] adder_1_out, alu_bin_1_alu_bin, CSR_out, DM_Dout, EX_ALU_Res, EX_CSR_out, EX_IR,
       ex_mem_1_mem_csr_out, EX_Reg_R1, EX_Reg_R2, ID_CSR_out, ID_IR, ID_Reg_R1, IF_IR, MEM_ALU_Res, MEM_IR,
       multiplexer_1_out, multiplexer_2_out, multiplexer_10_out, multiplexer_11_out, multiplexer_12_out,
       pc_in_1_pc_2, pc_in_2_pc_2, PredictAddr, ram_1_data, redirect_Reg_R1, redirect_Reg_R2, regifile_1_r2,
       WB_ALU_Res, WB_IR, \全相联cache_1_jumpaddr ;

  Button \u_总复位  (.out(RST));
  Button _1 (.out(IR1));
  Button _2 (.out(IR2));
  Button _3 (.out(IR3));
  // Probe on \总周期数 
  // Probe on \总周期数 
  Button \u_继续运行  (.out(Go));
  LED #(.active("true")) led_1 (.in(W1));
  LED #(.active("true")) led_2 (.in(W2));
  LED #(.active("true")) led_3 (.in(W3));
  not not_1 (EX_BranchTaken, whichpc_1_out_9);
  Hex_Digit_Display hex_digit_display_1 (.value(LedData[31:28]));  // open: dp
  // Probe on IF_PC[19:0]
  // RiscV_Probe riscv_probe_1: pin names not known; wires that end beside it: IF_IR
  WhichPC whichpc_1 (
    .out_9(whichpc_1_out_9), .GE(GE), .BLTU(BLTU), .URET(URET), .JALR(JALR), .JAL(JAL), .Beq(Beq), .Bne(Bne),
    .Equal(Equal));
  Multiplexer #(.select(1), .width(32), .disabled("Z"), .enable("false")) multiplexer_1 (
    .in0(EX_PC), .in1(EX_PC), .out(multiplexer_1_out), .sel(whichpc_1_out_9));
  not not_2 (not_2_out, halt);
  Counter #(.width(16), .max('hffff), .ongoal("wrap"), .trigger("rising"), .behavior("new")) counter_1 (
    .count(not_2_out), .Q(\总周期数 ), .clk(CLK), .clr(RST));  // open: load, D, carry, preset, down
  Hex_Digit_Display hex_digit_display_2 (.value(LedData[27:24]));  // open: dp
  Hex_Digit_Display hex_digit_display_3 (.value(LedData[23:20]));  // open: dp
  // Probe on ID_PC[19:0]
  // RiscV_Probe riscv_probe_2: pin names not known; wires that end beside it: ID_IR
  Hex_Digit_Display hex_digit_display_4 (.value(LedData[15:12]));  // open: dp
  Hex_Digit_Display hex_digit_display_5 (.value(LedData[19:16]));  // open: dp
  or or_1 (EX_Branch, Bne, Beq, BLTU, JALR, JAL, URET);
  Hex_Digit_Display hex_digit_display_6 (.value(LedData[11:8]));  // open: dp
  Hex_Digit_Display hex_digit_display_7 (.value(LedData[7:4]));  // open: dp
  // Probe on EX_PC[19:0]
  // RiscV_Probe riscv_probe_3: pin names not known; wires that end beside it: EX_IR
  PC_in pc_in_1 (
    .PC(multiplexer_1_out), .immb(immb), .immuj(immuj), .ALU_Res(EX_ALU_Res), .\中断编号 (undriven), .GE(GE),
    .BLTU(BLTU), .URET(URET), .JALR(JALR), .JAL(JAL), .Beq(Beq), .Bne(Bne), .Equal(Equal), .\中断触发 (1'b0),
    .PC_2(pc_in_1_pc_2));  // open: EPC
  PC_in pc_in_2 (
    .PC(EX_PC), .immb(immb), .immuj(immuj), .ALU_Res(EX_ALU_Res), .\中断编号 (undriven_2), .GE(1'b0),
    .BLTU(BLTU), .URET(URET), .JALR(JALR), .JAL(JAL), .Beq(Beq), .Bne(Bne), .Equal(Beq), .\中断触发 (1'b0),
    .PC_2(pc_in_2_pc_2));  // open: EPC
  Counter #(.width(16), .max('hffff), .ongoal("wrap"), .trigger("rising"), .behavior("new")) counter_2 (
    .count(Load_Use), .Q(\LoadUse次数 ), .clk(CLK), .clr(RST));  // open: load, D, carry, preset, down
  Hex_Digit_Display hex_digit_display_8 (.value(LedData[3:0]));  // open: dp
  // Probe on \总周期数 
  // Probe on M_PC[19:0]
  // RiscV_Probe riscv_probe_4: pin names not known; wires that end beside it: MEM_IR
  and and_1 (Flush, EX_Branch, PredictErr);
  Multiplexer #(.select(1), .width(32), .disabled("Z"), .enable("false")) multiplexer_2 (
    .in0(PredictAddr), .in1(pc_in_1_pc_2), .out(multiplexer_2_out), .sel(PredictErr));
  not not_3 (not_3_out, multiplexer_3_out);
  Multiplexer #(.select(1), .width(1), .disabled("Z"), .enable("false")) multiplexer_3 (
    .in0(and_2_out), .in1(and_3_out), .out(multiplexer_3_out), .sel(halt));
  and and_2 (and_2_out, not_4_out, Load_Use);
  not not_4 (not_4_out, Flush);
  and and_3 (and_3_out, not_5_out, halt);
  not not_5 (not_5_out, Go);
  \全相联Cache  \u_全相联cache_1  (
    .CLK(CLK), .in_2(IF_PC), .PredictJump(IF_predictJump), .JumpAddr(\全相联cache_1_jumpaddr ),
    .Branch(EX_Branch), .EX_BranchTaken(EX_BranchTaken), .EX_PC(EX_PC), .EX_DPC(pc_in_2_pc_2));
  // Probe on \总周期数 
  // Probe on \无条件分支数 
  // Probe on \条件分支成功数 
  // Probe on \插入气泡数 
  // Probe on \LoadUse次数 
  Register #(.width(32), .trigger("rising"), .Select("low")) PC (
    .D(multiplexer_2_out), .en(not_3_out), .Q(IF_PC), .clk(CLK), .clr(RST));
  or or_2 (or_2_out, JALR, JAL);
  // Probe on IF_PC[11:0]
  // Probe on WB_PC[19:0]
  // RiscV_Probe riscv_probe_5: pin names not known; wires that end beside it: WB_IR
  Adder #(.width(32)) adder_1 (.a(IF_PC), .b(32'h4), .out(adder_1_out));  // open: cin, cout
  Multiplexer #(.select(1), .width(32), .disabled("Z"), .enable("false")) multiplexer_4 (
    .in0(adder_1_out), .in1(\全相联cache_1_jumpaddr ), .out(PredictAddr), .sel(IF_predictJump));
  Counter #(.width(16), .max('hffff), .ongoal("wrap"), .trigger("rising"), .behavior("new")) counter_3 (
    .count(or_2_out), .Q(\无条件分支数 ), .clk(CLK), .clr(RST));  // open: load, D, carry, preset, down
  // Probe on EX_PC[11:0]
  // Probe on ID_PC[11:0]
  Multiplexer #(.select(1), .width(1), .disabled("Z"), .enable("false")) multiplexer_5 (
    .in0(IF_predictJump), .in1(1'b0), .out(multiplexer_5_out), .sel(Flush));
  // Probe on M_PC[11:0]
  D_Flip_Flop #(.trigger("high"), .Pre_Clr_Positions("LEGACY"), .NegatePresetClear("false"), .enable("true"), .NewFFLayout("false")) d_ff_1 (.Q(d_ff_1_q));  // open: clk, D, Qn, preset, en, reset
  // Probe on 13'h9e
  IF_ID if_id_1 (
    .IF_PC(IF_PC), .IF_IR(IF_IR), .ID_PC(ID_PC), .ID_IR(ID_IR), .CLK(CLK), .halt(multiplexer_6_out),
    .Flush(Flush));
  ROM #(.addrWidth(10), .dataWidth(32), .Select("high")) rom_1 (.addr(IF_PC[11:2]), .data(IF_IR));
  Register #(.width(1), .trigger("rising"), .Select("low")) register_1 (
    .D(multiplexer_5_out), .en(not_6_out), .Q(register_1_q), .clk(CLK));  // open: clr
  not not_6 (not_6_out, Load_Use);
  // Probe on WB_PC[11:0]
  Comparator #(.width(13), .mode("twosComplement")) comparator_1 (
    .a(CNT_num), .b(13'h9e), .eq(comparator_1_eq), .lt(comparator_1_lt));  // open: gt
  Clock #(.highDuration(1), .lowDuration(1)) clock_1 (.out(clock_1_out));
  Multiplexer #(.select(1), .width(1), .disabled("Z"), .enable("false")) multiplexer_6 (
    .in0(Load_Use), .in1(and_4_out), .out(multiplexer_6_out), .sel(halt));
  and and_4 (and_4_out, not_7_out, halt);
  not not_7 (not_7_out, Go);
  Multiplexer #(.select(1), .width(5), .disabled("Z"), .enable("false")) multiplexer_7 (
    .in0(ID_IR[19:15]), .in1(5'b10001), .out(rrs1), .sel(ID_ecall));
  Multiplexer #(.select(1), .width(5), .disabled("Z"), .enable("false")) multiplexer_8 (
    .in0(ID_IR[24:20]), .in1(5'b01010), .out(rrs2), .sel(ID_ecall));
  not not_8 (not_8_out, or_3_out);
  or or_3 (or_3_out, JALR, JAL);
  nand nand_1 (nand_1_out, d_ff_1_q, comparator_1_eq);
  Counter #(.width(13), .max('h1fff), .ongoal("stay"), .trigger("rising"), .behavior("old")) counter_4 (
    .count(comparator_1_lt), .Q(CNT_num), .clk(clock_1_out));  // open: load, D, carry, clr, preset
  // RiscV_Probe riscv_probe_6: pin names not known; wires that end beside it: ID_IR
  Reg_Din reg_din_1 (
    .DM_Dout(DM_Dout), .PC(WB_PC), .CSR_out(CSR_out), .ALU_Res(WB_ALU_Res), .LH(WB_LH),
    .MemToReg(WB_MemToReg), .CSR(WB_CSR), .JAL(WB_JAL), .JALR(WB_JALR), .RDin(RDin));
  and and_5 (and_5_out, EX_BranchTaken, not_8_out);
  Counter #(.width(16), .max('hffff), .ongoal("wrap"), .trigger("rising"), .behavior("new")) counter_5 (
    .count(and_5_out), .Q(\条件分支成功数 ), .clk(CLK), .clr(RST));  // open: load, D, carry, preset, down
  assign CLK = nand_1_out ? clock_1_out : 1'bz;  // Controlled_Buffer controlled_buffer_1
  Register #(.width(32), .trigger("rising"), .Select("low")) register_2 (
    .D(WB_ALU_Res), .en(WB_CSR), .Q(ID_CSR_out), .clk(CLK), .clr(RST));
  Regifile regifile_1 (
    .Din(RDin), .Clk(CLK), .R1(ID_Reg_R1), .R2(regifile_1_r2), .WE(RegWrite), .W_num(WB_rd), .R1_num(rrs1),
    .R2_num(rrs2));
  Pull_Resistor #(.pull(1)) pull_resistor_1 (.node(CLK));
  newcontrol newcontrol_1 (
    .out_4(newcontrol_1_out_4), .out_6(newcontrol_1_out_6), .out_8(newcontrol_1_out_8),
    .out_10(newcontrol_1_out_10), .out_12(newcontrol_1_out_12), .out_14(newcontrol_1_out_14),
    .in_1(ID_IR[21]), .in_2(ID_IR[6:2]), .in_3({ID_IR[30], ID_IR[25], ID_IR[14:12]}),
    .out_5(newcontrol_1_out_5), .out_7(newcontrol_1_out_7), .out_9(newcontrol_1_out_9),
    .out_11(newcontrol_1_out_11), .out_13(newcontrol_1_out_13), .out_15(newcontrol_1_out_15),
    .out_16(newcontrol_1_out_16), .out_17(newcontrol_1_out_17), .out_18(ID_ecall));
  or or_4 (or_4_out, Flush, Load_Use);
  Counter #(.width(16), .max('hffff), .ongoal("wrap"), .trigger("rising"), .behavior("new")) counter_6 (
    .count(or_4_out), .Q(\插入气泡数 ), .clk(CLK), .clr(RST));  // open: load, D, carry, preset, down
  redirect redirect_1 (
    .ERegwrite(EX_RegWrite), .IDrs1(rrs1), .Erd(EX_rd), .IDrs2(rrs2), .Mrd(MEM_rd), .MRegWrite(MEM_RegWrite),
    .OPcode(ID_IR[6:2]), .Rt_MEM(redirect_1_rt_mem), .Rs_MEM(redirect_1_rs_mem), .Rs_WB(redirect_1_rs_wb),
    .Rt_WB(redirect_1_rt_wb), .ID_ecall(ID_ecall));
  Load_Use load_use_1 (
    .ERegwrite(EX_RegWrite), .IDrs1(rrs1), .Erd(EX_rd), .IDrs2(rrs2), .OPcode1(ID_IR[6:2]),
    .LoadUse(Load_Use), .EX_MemToReg(EX_MemToReg));
  or or_5 (or_5_out, Load_Use, Flush);
  Multiplexer #(.select(1), .width(1), .disabled("Z"), .enable("false")) multiplexer_9 (
    .in0(register_1_q), .in1(1'b0), .out(multiplexer_9_out), .sel(or_6_out));
  or or_6 (or_6_out, Load_Use, Flush);
  ID_EX id_ex_1 (
    .ID_PC(ID_PC), .ID_IR(ID_IR), .ID_rs1(ID_IR[19:15]), .ID_rd(ID_IR[11:7]), .ID_imm12(ID_IR[31:20]),
    .ID_imms({ID_IR[31:25], ID_IR[11:7]}), .ID_immb({ID_IR[31], ID_IR[7], ID_IR[30:25], ID_IR[11:8]}),
    .ID_immuj({ID_IR[31], ID_IR[19:12], ID_IR[20], ID_IR[30:21]}), .ID_Beq(newcontrol_1_out_5),
    .ID_Bne(newcontrol_1_out_7), .ID_MemToReg(newcontrol_1_out_9), .ID_MemWrite(newcontrol_1_out_11),
    .ID_ALUOP(newcontrol_1_out_13), .ID_ALUSrcB(newcontrol_1_out_15), .ID_RegWrite(newcontrol_1_out_16),
    .ID_S_type(newcontrol_1_out_17), .ID_JAL(newcontrol_1_out_4), .ID_JALR(newcontrol_1_out_6),
    .ID_URET(newcontrol_1_out_8), .ID_BLTU(newcontrol_1_out_10), .ID_CSR(newcontrol_1_out_12),
    .ID_LH(newcontrol_1_out_14), .ID_ecall(ID_ecall), .ID_Reg_R2(regifile_1_r2), .ID_CSR_out(ID_CSR_out),
    .EX_PC(EX_PC), .EX_IR(EX_IR), .EX_rs1(EX_rs1), .EX_rd(EX_rd), .EX_imm12(EX_imm12), .EX_imms(EX_imms),
    .EX_immb(immb), .EX_immuj(immuj), .EX_Beq(Beq), .EX_Bne(Bne), .EX_MemToReg(EX_MemToReg),
    .EX_MemWrite(id_ex_1_ex_memwrite), .EX_ALUOP(id_ex_1_ex_aluop), .EX_ALUSrcB(id_ex_1_ex_alusrcb),
    .EX_RegWrite(EX_RegWrite), .EX_S_type(id_ex_1_ex_s_type), .EX_JAL(JAL), .EX_JALR(JALR), .EX_URET(URET),
    .EX_BLTU(BLTU), .EX_CSR(EX_CSR), .EX_LH(id_ex_1_ex_lh), .EX_ecall(EX_ecall), .EX_Reg_R2(EX_Reg_R2),
    .EX_CSR_out(EX_CSR_out), .CLK(CLK), .ID_Reg_R1(ID_Reg_R1), .EX_Reg_R1(EX_Reg_R1), .halt(and_6_out),
    .Flush(or_5_out), .Rt_MEM_2(Rt_MEM), .Rs_MEM_2(Rs_MEM), .Rs_WB_2(Rs_WB), .Rt_WB_2(Rt_WB),
    .Rt_MEM(redirect_1_rt_mem), .Rs_MEM(redirect_1_rs_mem), .Rs_WB(redirect_1_rs_wb), .Rt_WB(redirect_1_rt_wb));
  and and_6 (and_6_out, not_9_out, halt);
  not not_9 (not_9_out, Go);
  Register #(.width(1), .trigger("rising"), .Select("low")) register_3 (
    .D(multiplexer_9_out), .Q(register_3_q), .clk(CLK));  // open: en, clr
  xor xor_1 (PredictErr, EX_BranchTaken, register_3_q);
  Multiplexer #(.select(1), .width(32), .disabled("Z"), .enable("false")) multiplexer_10 (
    .in0(EX_Reg_R1), .in1(RDin), .out(multiplexer_10_out), .sel(Rs_WB));
  Multiplexer #(.select(1), .width(32), .disabled("Z"), .enable("false")) multiplexer_11 (
    .in0(EX_Reg_R2), .in1(RDin), .out(multiplexer_11_out), .sel(Rt_WB));
  Multiplexer #(.select(1), .width(32), .disabled("Z"), .enable("false")) multiplexer_12 (
    .in0(redirect_Reg_R1), .in1(EX_CSR_out), .out(multiplexer_12_out), .sel(EX_CSR));
  ALU_Bin alu_bin_1 (
    .Reg_R2(redirect_Reg_R2), .immb(EX_imm12), .rs1(EX_rs1), .imms(EX_imms), .CSR(EX_CSR),
    .S_type(id_ex_1_ex_s_type), .AluSrcB(id_ex_1_ex_alusrcb), .ALU_Bin(alu_bin_1_alu_bin));
  ALU alu_1 (
    .X(multiplexer_12_out), .Y(alu_bin_1_alu_bin), .AluOP(id_ex_1_ex_aluop), .Equal(Equal),
    .Result(EX_ALU_Res), .out_4(GE));  // open: Result_2, out_6
  Comparator #(.width(32), .mode("twosComplement")) comparator_2 (
    .a(32'h22), .b(redirect_Reg_R1), .eq(comparator_2_eq));  // open: gt, lt
  Multiplexer #(.select(1), .width(32), .disabled("Z"), .enable("false")) multiplexer_13 (
    .in0(multiplexer_10_out), .in1(MEM_ALU_Res), .out(redirect_Reg_R1), .sel(Rs_MEM));
  Multiplexer #(.select(1), .width(32), .disabled("Z"), .enable("false")) multiplexer_14 (
    .in0(multiplexer_11_out), .in1(MEM_ALU_Res), .out(redirect_Reg_R2), .sel(Rt_MEM));
  not not_10 (not_10_out, comparator_2_eq);
  Register #(.width(1), .trigger("rising"), .Select("low")) register_4 (
    .D(not_10_out), .en(EX_ecall), .Q(register_4_q), .clk(CLK), .clr(Go));
  Register #(.width(32), .trigger("rising"), .Select("low")) register_5 (
    .D(redirect_Reg_R2), .en(comparator_2_eq), .Q(LedData), .clk(CLK), .clr(RST));
  EX_MEM ex_mem_1 (
    .EX_PC(EX_PC), .EX_IR(EX_IR), .EX_rd(EX_rd), .ID_MemToReg(EX_MemToReg),
    .ID_MemWrite(id_ex_1_ex_memwrite), .ID_RegWrite(EX_RegWrite), .ID_CSR(EX_CSR), .ID_LH(id_ex_1_ex_lh),
    .EX_Reg_R2(redirect_Reg_R2), .EX_ALU_Res(EX_ALU_Res), .MEM_PC(M_PC), .MEM_IR(MEM_IR), .MEM_rd(MEM_rd),
    .EX_MemToReg(ex_mem_1_ex_memtoreg), .EX_MemWrite(MemWrite), .EX_RegWrite(MEM_RegWrite),
    .EX_CSR(ex_mem_1_ex_csr), .EX_LH(ex_mem_1_ex_lh), .MEM_Reg_R2(MDin), .MEM_ALU_Res(MEM_ALU_Res),
    .CLK(CLK), .halt(and_7_out), .ID_JALR(JALR), .EX_JALR(ex_mem_1_ex_jalr), .ID_JAL(JAL),
    .EX_JAL(ex_mem_1_ex_jal), .EX_CSR_out(EX_CSR_out), .MEM_CSR_out(ex_mem_1_mem_csr_out),
    .EX_halt(register_4_q), .MEM_halt(ex_mem_1_mem_halt));  // open: Flush
  and and_7 (and_7_out, not_11_out, halt);
  not not_11 (not_11_out, Go);
  not not_12 (not_12_out, MemWrite);
  RAM #(.addrWidth(10), .dataWidth(32), .bus("separate"), .Select("high")) ram_1 (
    .addr(MEM_ALU_Res[11:2]), .din(MDin), .data(ram_1_data), .str(MemWrite), .clk(CLK), .ld(not_12_out),
    .clr(RST));  // open: sel
  MEM_WB mem_wb_1 (
    .MEM_PC(M_PC), .MEM_IR(MEM_IR), .MEM_rd(MEM_rd), .ID_MemToReg(ex_mem_1_ex_memtoreg),
    .ID_RegWrite(MEM_RegWrite), .ID_JAL(ex_mem_1_ex_jal), .ID_JALR(ex_mem_1_ex_jalr),
    .ID_CSR(ex_mem_1_ex_csr), .ID_LH(ex_mem_1_ex_lh), .MEM_ALU_Res(MEM_ALU_Res), .WB_PC(WB_PC),
    .WB_IR(WB_IR), .WB_rd(WB_rd), .EX_MemToReg(WB_MemToReg), .EX_RegWrite(RegWrite), .EX_JAL(WB_JAL),
    .EX_JALR(WB_JALR), .EX_CSR(WB_CSR), .EX_LH(WB_LH), .WB_ALU_Res(WB_ALU_Res), .in_15(and_8_out),
    .in_16(CLK), .MEM_DM_Dput(ram_1_data), .WB_DM_Dout(DM_Dout), .MEM_CSR_out(ex_mem_1_mem_csr_out),
    .WB_CSR_out(CSR_out), .MEM_halt(ex_mem_1_mem_halt), .WB_halt(halt));  // open: Flush
  and and_8 (and_8_out, not_13_out, halt);
  not not_13 (not_13_out, Go);

  // Other names for the same wires on the sheet: rd[4:0] = ID_IR[11:7]; ID_rs2[4:0] = ID_IR[24:20];
  //   ID_rs1[4:0] = ID_IR[19:15]; ID_OPcode[4:0] = ID_IR[6:2]; MEM_PC[31:0] = M_PC

  // Notes on the sheet:
  //   中断源
  //   时空图监测，可删除
  //   中断等待指示
  //   数码管输出
  //   指令存储器
  //   控制位
  //   流水调试日志用
  //   暂停节拍，不能为0
  //   指令字
  //   contents of rom_1 (hex, n*v repeats v):
  //   100493 100006f 100493 200913 300993 100006f 100493 200913 300993 100006f 100493 200913 300993
  //   100006f 100493 200913 300993 3d8000ef 100413 100493 1f49493 900533 2200893 73 24d493 48463 fedff06f
  //   900533 2200893 73 100493 249493 900533 2200893 73 48463 fedff06f 100493 1f49493 900533 2200893 73
  //   4034d493 900533 2200893 73 4044d493 900533 2200893 73 4044d493 900533 2200893 73 4044d493 900533
  //   2200893 73 4044d493 900533 2200893 73 4044d493 900533 2200893 73 4044d493 900533 2200893 73 4044d493
  //   900533 2200893 73 100413 1f41993 41f9d993 433 c00913 300b13 140413 f47413 800293 100313 499993
  //   89e9b3 1300533 2200893 73 406282b3 fe0294e3 140413 f00f93 1f47433 1c41413 800293 100313 49d993
  //   89e9b3 1300533 2200893 73 406282b3 fe0294e3 1c45413 406b0b33 b0463 f95ff06f 2b3 fff2c293 829293
  //   ff2e293 500533 2200893 73 fff00413 493 84a023 140413 448493 84a023 140413 448493 84a023 140413
  //   448493 84a023 140413 448493 84a023 140413 448493 84a023 140413 448493 84a023 140413 448493 84a023
  //   140413 448493 84a023 140413 448493 84a023 140413 448493 84a023 140413 448493 84a023 140413 448493
  //   84a023 140413 448493 84a023 140413 448493 84a023 140413 448493 84a023 140413 448493 140413 433
  //   3c00493 42983 4aa03 149a2b3 28663 134a023 1442023 ffc48493 fe9412e3 800533 2200893 73 440413 3c00493
  //   fc9416e3 3200893 73 100293 300313 800493 849493 7648493 900533 2200893 73 800e13 5494b3 6494b3
  //   900533 2200893 73 fffe0e13 fe0e14e3 a00893 73 fff00293 7700493 849493 7748493 900533 2200893 73
  //   1000e13 54c4b3 900533 2200893 73 fffe0e13 fe0e16e3 a00893 73 313 1000e13 8400493 849493 8348493
  //   400913 891913 490913 849493 8248493 849493 8148493 891913 490913 891913 490913 932023 12484b3 430313
  //   fffe0e13 fe0e18e3 2000e13 313 31483 900533 2200893 73 230313 fffe0e13 fe0e14e3 a00893 73 ff100493
  //   900533 2200893 73 148493 fe9068e3 900533 2200893 73 a00893 73 a00893 73 413 140413 800533 2200893 73
  //   240413 800533 2200893 73 340413 800533 2200893 73 440413 800533 2200893 73 540413 800533 2200893 73
  //   640413 800533 2200893 73 740413 800533 2200893 73 840413 800533 2200893 2200893 73 8067
  //   戳工具置1进入计数暂停模式，ctrl+k时钟自动运行到对应节拍暂停
  //   ctrl+k关闭时钟连续运行，将控制位置零，进入单步调试模式调试
  //   指令探针
  //   可计数暂停的时钟源
  //   为方便自动评测，需要输出流水线各段保存的PC值，注意是PC不是PC+4，另外ID段寄存器写入信息，Mem段内存写入信息也要输出
  //   数据存储器
endmodule

module \全相联Cache改  (
  input  CLK,
  input  [31:0] in_2,
  input  Branch,
  input  [31:0] EX_PC,
  input  [31:0] EX_DPC,
  input  EX_BranchTaken,
  output PredictJump,
  output [31:0] JumpAddr
);

  wire _404, comparator_1_eq, comparator_2_eq, comparator_3_eq, comparator_4_eq, comparator_5_eq,
       comparator_6_eq, comparator_7_eq, comparator_8_eq, comparator_9_eq, comparator_10_eq,
       comparator_11_eq, comparator_12_eq, comparator_13_eq, comparator_14_eq, comparator_15_eq,
       comparator_16_eq, comparator_17_gt, decoder_1_out0, decoder_1_out1, decoder_1_out2, decoder_1_out3,
       decoder_1_out4, decoder_1_out5, decoder_1_out6, decoder_1_out7, decoder_2_out0, decoder_2_out1,
       decoder_2_out2, decoder_2_out3, decoder_2_out4, decoder_2_out5, decoder_2_out6, decoder_2_out7, empty,
       Find, Hit, L0, L00, L1, L2, L3, L4, L5, L6, L7, L11, L22, L33, L44, L55, L66, L77, Miss,
       multiplexer_1_out, multiplexer_2_out, multiplexer_3_out, multiplexer_4_out, multiplexer_5_out,
       multiplexer_6_out, multiplexer_7_out, multiplexer_8_out, multiplexer_9_out, multiplexer_10_out,
       multiplexer_11_out, multiplexer_12_out, multiplexer_13_out, multiplexer_14_out, multiplexer_15_out,
       multiplexer_16_out, not_1_out, not_2_out, not_3_out, not_4_out, not_5_out, not_6_out, not_7_out,
       not_8_out, not_9_out, not_10_out, not_11_out, not_12_out, not_13_out, not_14_out, not_15_out,
       not_16_out, not_19_out, not_20_out, not_21_out, not_22_out, not_23_out, not_24_out, not_25_out,
       not_26_out, Pre_0, Pre_1, V0, V1, V2, V3, V4, V5, V6, V7, WriteL0, WriteL1, WriteL2, WriteL3, WriteL4,
       WriteL5, WriteL6, WriteL7;
  wire [1:0] controlled_buffer_1_out, controlled_buffer_9_out, Pre0, Pre1, Pre2, Pre3, Pre4, Pre5, Pre6, Pre7;
  wire [2:0] empty_num, MAX_num, \归并比较电路_max3_1_max_num , \归并比较电路_max3_2_max_num , \归并比较电路_max3_3_max_num ,
       \归并比较电路_max3_4_max_num , \归并比较电路_max3_5_max_num , \归并比较电路_max3_6_max_num ;
  wire [15:0] MAX, Out0, Out1, Out2, Out3, Out4, Out5, Out6, Out7, \归并比较电路_max3_1_max , \归并比较电路_max3_2_max ,
       \归并比较电路_max3_3_max , \归并比较电路_max3_4_max , \归并比较电路_max3_5_max , \归并比较电路_max3_6_max ;
  wire [31:0] BPC0, BPC1, BPC2, BPC3, BPC4, BPC5, BPC6, BPC7, controlled_buffer_17_out, DPC0, DPC1, DPC2,
       DPC3, DPC4, DPC5, DPC6, DPC7;

  Register #(.width(1), .trigger("rising"), .Select("low")) register_1 (
    .D(1'b1), .en(WriteL0), .Q(V0), .clk(CLK));  // open: clr
  Register #(.width(1), .trigger("rising"), .Select("low")) register_2 (
    .D(1'b1), .en(WriteL1), .Q(V1), .clk(CLK));  // open: clr
  Register #(.width(1), .trigger("rising"), .Select("low")) register_3 (
    .D(1'b1), .en(WriteL2), .Q(V2), .clk(CLK));  // open: clr
  Register #(.width(1), .trigger("rising"), .Select("low")) register_4 (
    .D(1'b1), .en(WriteL3), .Q(V3), .clk(CLK));  // open: clr
  Register #(.width(1), .trigger("rising"), .Select("low")) register_5 (
    .D(1'b1), .en(WriteL4), .Q(V4), .clk(CLK));  // open: clr
  Register #(.width(1), .trigger("rising"), .Select("low")) register_6 (
    .D(1'b1), .en(WriteL5), .Q(V5), .clk(CLK));  // open: clr
  Register #(.width(1), .trigger("rising"), .Select("low")) register_7 (
    .D(1'b1), .en(WriteL6), .Q(V6), .clk(CLK));  // open: clr
  Register #(.width(1), .trigger("rising"), .Select("low")) register_8 (
    .D(1'b1), .en(WriteL7), .Q(V7), .clk(CLK));  // open: clr
  Register #(.width(32), .trigger("rising"), .Select("low")) register_9 (
    .D(EX_PC), .en(WriteL0), .Q(BPC0), .clk(CLK));  // open: clr
  Register #(.width(32), .trigger("rising"), .Select("low")) register_10 (
    .D(EX_PC), .en(WriteL1), .Q(BPC1), .clk(CLK));  // open: clr
  Register #(.width(32), .trigger("rising"), .Select("low")) register_11 (
    .D(EX_PC), .en(WriteL2), .Q(BPC2), .clk(CLK));  // open: clr
  Register #(.width(32), .trigger("rising"), .Select("low")) register_12 (
    .D(EX_PC), .en(WriteL3), .Q(BPC3), .clk(CLK));  // open: clr
  Register #(.width(32), .trigger("rising"), .Select("low")) register_13 (
    .D(EX_PC), .en(WriteL4), .Q(BPC4), .clk(CLK));  // open: clr
  Register #(.width(32), .trigger("rising"), .Select("low")) register_14 (
    .D(EX_PC), .en(WriteL5), .Q(BPC5), .clk(CLK));  // open: clr
  Register #(.width(32), .trigger("rising"), .Select("low")) register_15 (
    .D(EX_PC), .en(WriteL6), .Q(BPC6), .clk(CLK));  // open: clr
  Register #(.width(32), .trigger("rising"), .Select("low")) register_16 (
    .D(EX_PC), .en(WriteL7), .Q(BPC7), .clk(CLK));  // open: clr
  Register #(.width(32), .trigger("rising"), .Select("low")) register_17 (
    .D(EX_DPC), .en(WriteL0), .Q(DPC0), .clk(CLK));  // open: clr
  Register #(.width(32), .trigger("rising"), .Select("low")) register_18 (
    .D(EX_DPC), .en(WriteL1), .Q(DPC1), .clk(CLK));  // open: clr
  Register #(.width(32), .trigger("rising"), .Select("low")) register_19 (
    .D(EX_DPC), .en(WriteL2), .Q(DPC2), .clk(CLK));  // open: clr
  Register #(.width(32), .trigger("rising"), .Select("low")) register_20 (
    .D(EX_DPC), .en(WriteL3), .Q(DPC3), .clk(CLK));  // open: clr
  Register #(.width(32), .trigger("rising"), .Select("low")) register_21 (
    .D(EX_DPC), .en(WriteL4), .Q(DPC4), .clk(CLK));  // open: clr
  Register #(.width(32), .trigger("rising"), .Select("low")) register_22 (
    .D(EX_DPC), .en(WriteL5), .Q(DPC5), .clk(CLK));  // open: clr
  Register #(.width(32), .trigger("rising"), .Select("low")) register_23 (
    .D(EX_DPC), .en(WriteL6), .Q(DPC6), .clk(CLK));  // open: clr
  Register #(.width(32), .trigger("rising"), .Select("low")) register_24 (
    .D(EX_DPC), .en(WriteL7), .Q(DPC7), .clk(CLK));  // open: clr
  not not_1 (not_1_out, V0);
  Register #(.width(1), .trigger("rising"), .Select("low")) register_25 (
    .D(Pre_1), .en(WriteL0), .Q(Pre0[1]), .clk(CLK), .preset(not_1_out));  // open: clr, cs
  Register #(.width(1), .trigger("rising"), .Select("low")) register_26 (
    .D(Pre_1), .en(WriteL1), .Q(Pre1[1]), .clk(CLK), .preset(not_2_out));  // open: clr, cs
  not not_2 (not_2_out, V1);
  Register #(.width(1), .trigger("rising"), .Select("low")) register_27 (
    .D(Pre_1), .en(WriteL2), .Q(Pre2[1]), .clk(CLK), .preset(not_3_out));  // open: clr, cs
  not not_3 (not_3_out, V2);
  Register #(.width(1), .trigger("rising"), .Select("low")) register_28 (
    .D(Pre_1), .en(WriteL3), .Q(Pre3[1]), .clk(CLK), .preset(not_4_out));  // open: clr, cs
  not not_4 (not_4_out, V3);
  Register #(.width(1), .trigger("rising"), .Select("low")) register_29 (
    .D(Pre_1), .en(WriteL4), .Q(Pre4[1]), .clk(CLK), .preset(not_5_out));  // open: clr, cs
  not not_5 (not_5_out, V4);
  Register #(.width(1), .trigger("rising"), .Select("low")) register_30 (
    .D(Pre_1), .en(WriteL5), .Q(Pre5[1]), .clk(CLK), .preset(not_6_out));  // open: clr, cs
  not not_6 (not_6_out, V5);
  Register #(.width(1), .trigger("rising"), .Select("low")) register_31 (
    .D(Pre_1), .en(WriteL6), .Q(Pre6[1]), .clk(CLK), .preset(not_7_out));  // open: clr, cs
  not not_7 (not_7_out, V6);
  Register #(.width(1), .trigger("rising"), .Select("low")) register_32 (
    .D(Pre_1), .en(WriteL7), .Q(Pre7[1]), .clk(CLK), .preset(not_8_out));  // open: clr, cs
  not not_8 (not_8_out, V7);
  Register #(.width(1), .trigger("rising"), .Select("low")) register_33 (
    .D(Pre_0), .en(WriteL1), .Q(Pre1[0]), .clk(CLK), .preset(not_10_out));  // open: clr, cs
  Register #(.width(1), .trigger("rising"), .Select("low")) register_34 (
    .D(Pre_0), .en(WriteL2), .Q(Pre2[0]), .clk(CLK), .preset(not_11_out));  // open: clr, cs
  Register #(.width(1), .trigger("rising"), .Select("low")) register_35 (
    .D(Pre_0), .en(WriteL3), .Q(Pre3[0]), .clk(CLK), .preset(not_12_out));  // open: clr, cs
  Register #(.width(1), .trigger("rising"), .Select("low")) register_36 (
    .D(Pre_0), .en(WriteL4), .Q(Pre4[0]), .clk(CLK), .preset(not_13_out));  // open: clr, cs
  Register #(.width(1), .trigger("rising"), .Select("low")) register_37 (
    .D(Pre_0), .en(WriteL5), .Q(Pre5[0]), .clk(CLK), .preset(not_14_out));  // open: clr, cs
  Register #(.width(1), .trigger("rising"), .Select("low")) register_38 (
    .D(Pre_0), .en(WriteL6), .Q(Pre6[0]), .clk(CLK), .preset(not_15_out));  // open: clr, cs
  Register #(.width(1), .trigger("rising"), .Select("low")) register_39 (
    .D(Pre_0), .en(WriteL7), .Q(Pre7[0]), .clk(CLK), .preset(not_16_out));  // open: clr, cs
  Register #(.width(1), .trigger("rising"), .Select("low")) register_40 (
    .D(Pre_0), .en(WriteL0), .Q(Pre0[0]), .clk(CLK), .preset(not_9_out));  // open: clr, cs
  not not_9 (not_9_out, V0);
  not not_10 (not_10_out, V1);
  not not_11 (not_11_out, V2);
  not not_12 (not_12_out, V3);
  not not_13 (not_13_out, V4);
  not not_14 (not_14_out, V5);
  not not_15 (not_15_out, V6);
  not not_16 (not_16_out, V7);
  Counter #(.width(16), .max('hffff), .ongoal("stay"), .trigger("rising"), .behavior("new")) out_cnt0 (
    .load(WriteL0), .D({16{1'b0}}), .Q(Out0), .clk(CLK));  // open: count, carry, clr, preset, down
  Counter #(.width(16), .max('hffff), .ongoal("stay"), .trigger("rising"), .behavior("new")) out_cnt1 (
    .load(WriteL1), .D({16{1'b0}}), .Q(Out1), .clk(CLK));  // open: count, carry, clr, preset, down
  Counter #(.width(16), .max('hffff), .ongoal("stay"), .trigger("rising"), .behavior("new")) out_cnt2 (
    .load(WriteL2), .D({16{1'b0}}), .Q(Out2), .clk(CLK));  // open: count, carry, clr, preset, down
  Counter #(.width(16), .max('hffff), .ongoal("stay"), .trigger("rising"), .behavior("new")) out_cnt3 (
    .load(WriteL3), .D({16{1'b0}}), .Q(Out3), .clk(CLK));  // open: count, carry, clr, preset, down
  Counter #(.width(16), .max('hffff), .ongoal("stay"), .trigger("rising"), .behavior("new")) out_cnt4 (
    .load(WriteL4), .D({16{1'b0}}), .Q(Out4), .clk(CLK));  // open: count, carry, clr, preset, down
  Counter #(.width(16), .max('hffff), .ongoal("stay"), .trigger("rising"), .behavior("new")) out_cnt5 (
    .load(WriteL5), .D({16{1'b0}}), .Q(Out5), .clk(CLK));  // open: count, carry, clr, preset, down
  Counter #(.width(16), .max('hffff), .ongoal("stay"), .trigger("rising"), .behavior("new")) out_cnt6 (
    .load(WriteL6), .D({16{1'b0}}), .Q(Out6), .clk(CLK));  // open: count, carry, clr, preset, down
  Counter #(.width(16), .max('hffff), .ongoal("stay"), .trigger("rising"), .behavior("new")) out_cnt7 (
    .load(WriteL7), .D({16{1'b0}}), .Q(Out7), .clk(CLK));  // open: count, carry, clr, preset, down
  Decoder #(.select(3), .tristate("false"), .disabled("Z"), .enable("false")) decoder_1 (
    .out0(decoder_1_out0), .out1(decoder_1_out1), .out2(decoder_1_out2), .out3(decoder_1_out3),
    .out4(decoder_1_out4), .out5(decoder_1_out5), .out6(decoder_1_out6), .out7(decoder_1_out7), .sel(MAX_num));
  Comparator #(.width(32), .mode("twosComplement")) comparator_1 (
    .a(BPC0), .b(in_2), .eq(comparator_1_eq));  // open: gt, lt
  Comparator #(.width(32), .mode("twosComplement")) comparator_2 (
    .a(BPC1), .b(in_2), .eq(comparator_2_eq));  // open: gt, lt
  Comparator #(.width(32), .mode("twosComplement")) comparator_3 (
    .a(BPC2), .b(in_2), .eq(comparator_3_eq));  // open: gt, lt
  Comparator #(.width(32), .mode("twosComplement")) comparator_4 (
    .a(BPC3), .b(in_2), .eq(comparator_4_eq));  // open: gt, lt
  Comparator #(.width(32), .mode("twosComplement")) comparator_5 (
    .a(BPC4), .b(in_2), .eq(comparator_5_eq));  // open: gt, lt
  Comparator #(.width(32), .mode("twosComplement")) comparator_6 (
    .a(BPC5), .b(in_2), .eq(comparator_6_eq));  // open: gt, lt
  Comparator #(.width(32), .mode("twosComplement")) comparator_7 (
    .a(BPC6), .b(in_2), .eq(comparator_7_eq));  // open: gt, lt
  Comparator #(.width(32), .mode("twosComplement")) comparator_8 (
    .a(BPC7), .b(in_2), .eq(comparator_8_eq));  // open: gt, lt
  Comparator #(.width(32), .mode("twosComplement")) comparator_9 (
    .a(BPC0), .b(EX_PC), .eq(comparator_9_eq));  // open: gt, lt
  Comparator #(.width(32), .mode("twosComplement")) comparator_10 (
    .a(BPC1), .b(EX_PC), .eq(comparator_10_eq));  // open: gt, lt
  Comparator #(.width(32), .mode("twosComplement")) comparator_11 (
    .a(BPC2), .b(EX_PC), .eq(comparator_11_eq));  // open: gt, lt
  Comparator #(.width(32), .mode("twosComplement")) comparator_12 (
    .a(BPC3), .b(EX_PC), .eq(comparator_12_eq));  // open: gt, lt
  Comparator #(.width(32), .mode("twosComplement")) comparator_13 (
    .a(BPC4), .b(EX_PC), .eq(comparator_13_eq));  // open: gt, lt
  Comparator #(.width(32), .mode("twosComplement")) comparator_14 (
    .a(BPC5), .b(EX_PC), .eq(comparator_14_eq));  // open: gt, lt
  Comparator #(.width(32), .mode("twosComplement")) comparator_15 (
    .a(BPC6), .b(EX_PC), .eq(comparator_15_eq));  // open: gt, lt
  Comparator #(.width(32), .mode("twosComplement")) comparator_16 (
    .a(BPC7), .b(EX_PC), .eq(comparator_16_eq));  // open: gt, lt
  Decoder #(.select(3), .tristate("false"), .disabled("Z"), .enable("false")) decoder_2 (
    .out0(decoder_2_out0), .out1(decoder_2_out1), .out2(decoder_2_out2), .out3(decoder_2_out3),
    .out4(decoder_2_out4), .out5(decoder_2_out5), .out6(decoder_2_out6), .out7(decoder_2_out7),
    .sel(empty_num));
  and and_1 (L00, comparator_1_eq, V0);
  and and_2 (L11, comparator_2_eq, V1);
  and and_3 (L22, comparator_3_eq, V2);
  and and_4 (L33, comparator_4_eq, V3);
  and and_5 (L44, comparator_5_eq, V4);
  and and_6 (L55, comparator_6_eq, V5);
  and and_7 (L66, comparator_7_eq, V6);
  and and_8 (L77, comparator_8_eq, V7);
  and and_9 (L0, comparator_9_eq, V0);
  and and_10 (L1, comparator_10_eq, V1);
  and and_11 (L2, comparator_11_eq, V2);
  and and_12 (L3, comparator_12_eq, V3);
  and and_13 (L4, comparator_13_eq, V4);
  and and_14 (L5, comparator_14_eq, V5);
  and and_15 (L6, comparator_15_eq, V6);
  and and_16 (L7, comparator_16_eq, V7);
  Multiplexer #(.select(1), .width(1), .disabled("Z"), .enable("false")) multiplexer_1 (
    .in0(decoder_1_out0), .in1(decoder_2_out0), .out(multiplexer_1_out), .sel(empty));
  Multiplexer #(.select(1), .width(1), .disabled("Z"), .enable("false")) multiplexer_2 (
    .in0(decoder_1_out1), .in1(decoder_2_out1), .out(multiplexer_2_out), .sel(empty));
  Multiplexer #(.select(1), .width(1), .disabled("Z"), .enable("false")) multiplexer_3 (
    .in0(decoder_1_out2), .in1(decoder_2_out2), .out(multiplexer_3_out), .sel(empty));
  Multiplexer #(.select(1), .width(1), .disabled("Z"), .enable("false")) multiplexer_4 (
    .in0(decoder_1_out3), .in1(decoder_2_out3), .out(multiplexer_4_out), .sel(empty));
  Multiplexer #(.select(1), .width(1), .disabled("Z"), .enable("false")) multiplexer_5 (
    .in0(decoder_1_out4), .in1(decoder_2_out4), .out(multiplexer_5_out), .sel(empty));
  Multiplexer #(.select(1), .width(1), .disabled("Z"), .enable("false")) multiplexer_6 (
    .in0(decoder_1_out5), .in1(decoder_2_out5), .out(multiplexer_6_out), .sel(empty));
  Multiplexer #(.select(1), .width(1), .disabled("Z"), .enable("false")) multiplexer_7 (
    .in0(decoder_1_out6), .in1(decoder_2_out6), .out(multiplexer_7_out), .sel(empty));
  Multiplexer #(.select(1), .width(1), .disabled("Z"), .enable("false")) multiplexer_8 (
    .in0(decoder_1_out7), .in1(decoder_2_out7), .out(multiplexer_8_out), .sel(empty));
  or or_1 (Find, L00, L11, L22, L33, L44, L55, L66, L77);
  or or_2 (Hit, L0, L1, L2, L3, L4, L5, L6, L7);
  not not_17 (_404, Find);
  not not_18 (Miss, Hit);
  Multiplexer #(.select(1), .width(1), .disabled("Z"), .enable("false")) multiplexer_9 (
    .in0(multiplexer_1_out), .in1(L0), .out(multiplexer_9_out), .sel(Hit));
  Multiplexer #(.select(1), .width(1), .disabled("Z"), .enable("false")) multiplexer_10 (
    .in0(multiplexer_2_out), .in1(L1), .out(multiplexer_10_out), .sel(Hit));
  Multiplexer #(.select(1), .width(1), .disabled("Z"), .enable("false")) multiplexer_11 (
    .in0(multiplexer_3_out), .in1(L2), .out(multiplexer_11_out), .sel(Hit));
  Multiplexer #(.select(1), .width(1), .disabled("Z"), .enable("false")) multiplexer_12 (
    .in0(multiplexer_4_out), .in1(L3), .out(multiplexer_12_out), .sel(Hit));
  Multiplexer #(.select(1), .width(1), .disabled("Z"), .enable("false")) multiplexer_13 (
    .in0(multiplexer_5_out), .in1(L4), .out(multiplexer_13_out), .sel(Hit));
  Multiplexer #(.select(1), .width(1), .disabled("Z"), .enable("false")) multiplexer_14 (
    .in0(multiplexer_6_out), .in1(L5), .out(multiplexer_14_out), .sel(Hit));
  Multiplexer #(.select(1), .width(1), .disabled("Z"), .enable("false")) multiplexer_15 (
    .in0(multiplexer_7_out), .in1(L6), .out(multiplexer_15_out), .sel(Hit));
  Multiplexer #(.select(1), .width(1), .disabled("Z"), .enable("false")) multiplexer_16 (
    .in0(multiplexer_8_out), .in1(L7), .out(multiplexer_16_out), .sel(Hit));
  and and_17 (WriteL0, multiplexer_9_out, Branch);
  and and_18 (WriteL1, multiplexer_10_out, Branch);
  and and_19 (WriteL2, multiplexer_11_out, Branch);
  and and_20 (WriteL3, multiplexer_12_out, Branch);
  and and_21 (WriteL4, multiplexer_13_out, Branch);
  and and_22 (WriteL5, multiplexer_14_out, Branch);
  and and_23 (WriteL6, multiplexer_15_out, Branch);
  and and_24 (WriteL7, multiplexer_16_out, Branch);
  assign controlled_buffer_1_out = L00 ? Pre0 : 2'bz;  // Controlled_Buffer controlled_buffer_1
  assign controlled_buffer_1_out = L11 ? Pre1 : 2'bz;  // Controlled_Buffer controlled_buffer_2
  assign controlled_buffer_1_out = L22 ? Pre2 : 2'bz;  // Controlled_Buffer controlled_buffer_3
  assign controlled_buffer_1_out = L33 ? Pre3 : 2'bz;  // Controlled_Buffer controlled_buffer_4
  assign controlled_buffer_1_out = L44 ? Pre4 : 2'bz;  // Controlled_Buffer controlled_buffer_5
  assign controlled_buffer_1_out = L55 ? Pre5 : 2'bz;  // Controlled_Buffer controlled_buffer_6
  assign controlled_buffer_1_out = L66 ? Pre6 : 2'bz;  // Controlled_Buffer controlled_buffer_7
  assign controlled_buffer_1_out = L77 ? Pre7 : 2'bz;  // Controlled_Buffer controlled_buffer_8
  assign controlled_buffer_9_out = L0 ? Pre0 : 2'bz;  // Controlled_Buffer controlled_buffer_9
  assign controlled_buffer_9_out = L1 ? Pre1 : 2'bz;  // Controlled_Buffer controlled_buffer_10
  assign controlled_buffer_9_out = L2 ? Pre2 : 2'bz;  // Controlled_Buffer controlled_buffer_11
  assign controlled_buffer_9_out = L3 ? Pre3 : 2'bz;  // Controlled_Buffer controlled_buffer_12
  assign controlled_buffer_9_out = L4 ? Pre4 : 2'bz;  // Controlled_Buffer controlled_buffer_13
  assign controlled_buffer_9_out = L5 ? Pre5 : 2'bz;  // Controlled_Buffer controlled_buffer_14
  assign controlled_buffer_9_out = L6 ? Pre6 : 2'bz;  // Controlled_Buffer controlled_buffer_15
  assign controlled_buffer_9_out = L7 ? Pre7 : 2'bz;  // Controlled_Buffer controlled_buffer_16
  Comparator #(.width(2), .mode("unsigned")) comparator_17 (
    .a(controlled_buffer_1_out), .b(2'b01), .gt(comparator_17_gt));  // open: eq, lt
  Multiplexer #(.select(1), .width(1), .disabled("Z"), .enable("false")) multiplexer_17 (
    .in0(1'b0), .in1(comparator_17_gt), .out(PredictJump), .sel(Find));
  \双位预测状态机  \u_双位预测状态机_1  (
    .S1(controlled_buffer_9_out[1]), .S0(controlled_buffer_9_out[0]), .jump(EX_BranchTaken), .N1(Pre_1),
    .N0(Pre_0));
  \归并比较电路_MAX3  \u_归并比较电路_max3_1  (
    .Y(Out0), .MAX(\归并比较电路_max3_1_max ), .X(Out1), .Y_num(3'b000), .Max_num(\归并比较电路_max3_1_max_num ),
    .X_num(3'b001));
  \归并比较电路_MAX3  \u_归并比较电路_max3_2  (
    .Y(Out2), .MAX(\归并比较电路_max3_2_max ), .X(Out3), .Y_num(3'b010), .Max_num(\归并比较电路_max3_2_max_num ),
    .X_num(3'b011));
  \归并比较电路_MAX3  \u_归并比较电路_max3_3  (
    .Y(Out4), .MAX(\归并比较电路_max3_3_max ), .X(Out5), .Y_num(3'b100), .Max_num(\归并比较电路_max3_3_max_num ),
    .X_num(3'b101));
  \归并比较电路_MAX3  \u_归并比较电路_max3_4  (
    .Y(Out6), .MAX(\归并比较电路_max3_4_max ), .X(Out7), .Y_num(3'b110), .Max_num(\归并比较电路_max3_4_max_num ),
    .X_num(3'b111));
  assign controlled_buffer_17_out = L00 ? DPC0 : 32'bz;  // Controlled_Buffer controlled_buffer_17
  assign controlled_buffer_17_out = L11 ? DPC1 : 32'bz;  // Controlled_Buffer controlled_buffer_18
  assign controlled_buffer_17_out = L22 ? DPC2 : 32'bz;  // Controlled_Buffer controlled_buffer_19
  assign controlled_buffer_17_out = L33 ? DPC3 : 32'bz;  // Controlled_Buffer controlled_buffer_20
  assign controlled_buffer_17_out = L44 ? DPC4 : 32'bz;  // Controlled_Buffer controlled_buffer_21
  assign controlled_buffer_17_out = L55 ? DPC5 : 32'bz;  // Controlled_Buffer controlled_buffer_22
  assign controlled_buffer_17_out = L66 ? DPC6 : 32'bz;  // Controlled_Buffer controlled_buffer_23
  assign controlled_buffer_17_out = L77 ? DPC7 : 32'bz;  // Controlled_Buffer controlled_buffer_24
  not not_19 (not_19_out, V0);
  not not_20 (not_20_out, V1);
  not not_21 (not_21_out, V2);
  not not_22 (not_22_out, V3);
  not not_23 (not_23_out, V4);
  not not_24 (not_24_out, V5);
  not not_25 (not_25_out, V6);
  not not_26 (not_26_out, V7);
  \归并比较电路_MAX3  \u_归并比较电路_max3_5  (
    .Y(\归并比较电路_max3_1_max ), .MAX(\归并比较电路_max3_5_max ), .X(\归并比较电路_max3_2_max ),
    .Y_num(\归并比较电路_max3_1_max_num ), .Max_num(\归并比较电路_max3_5_max_num ), .X_num(\归并比较电路_max3_2_max_num ));
  \归并比较电路_MAX3  \u_归并比较电路_max3_6  (
    .Y(\归并比较电路_max3_3_max ), .MAX(\归并比较电路_max3_6_max ), .X(\归并比较电路_max3_4_max ),
    .Y_num(\归并比较电路_max3_3_max_num ), .Max_num(\归并比较电路_max3_6_max_num ), .X_num(\归并比较电路_max3_4_max_num ));
  Multiplexer #(.select(1), .width(32), .disabled("Z"), .enable("false")) multiplexer_18 (
    .in0({32{1'b0}}), .in1(controlled_buffer_17_out), .out(JumpAddr), .sel(Find));
  \归并比较电路_MAX3  \u_归并比较电路_max3_7  (
    .Y(\归并比较电路_max3_5_max ), .MAX(MAX), .X(\归并比较电路_max3_6_max ), .Y_num(\归并比较电路_max3_5_max_num ),
    .Max_num(MAX_num), .X_num(\归并比较电路_max3_6_max_num ));
  Priority_Encoder #(.select(3), .disabled("Z")) priority_encoder_1 (
    .in0(not_19_out), .in1(not_20_out), .in2(not_21_out), .in3(not_22_out), .in4(not_23_out),
    .in5(not_24_out), .in6(not_25_out), .in7(not_26_out), .out(empty_num), .gs(empty));  // open: en_out, en_in

  // Other names for the same wires on the sheet: BPC[31:0] = EX_PC; DPC[31:0] = EX_DPC; PC[31:0] = in_2
endmodule
module \重定向流水见_动态分支预测改  (
  output RegWrite,
  output MemWrite,
  output [31:0] IF_PC,
  output [31:0] ID_PC,
  output [31:0] EX_PC,
  output [31:0] M_PC,
  output [31:0] WB_PC,
  output [31:0] RDin,
  output [31:0] MDin,
  output [31:0] LedData
);

  wire and_2_out, and_3_out, and_4_out, and_5_out, and_6_out, and_7_out, and_8_out, Beq, BLTU, Bne, CLK,
       clock_1_out, comparator_1_eq, comparator_1_lt, comparator_2_eq, d_ff_1_q, Equal, EX_Branch,
       EX_BranchTaken, EX_CSR, EX_ecall, ex_mem_1_ex_csr, ex_mem_1_ex_jal, ex_mem_1_ex_jalr, ex_mem_1_ex_lh,
       ex_mem_1_ex_memtoreg, ex_mem_1_mem_halt, EX_MemToReg, EX_RegWrite, Flush, GE, Go, halt, ID_ecall,
       id_ex_1_ex_alusrcb, id_ex_1_ex_lh, id_ex_1_ex_memwrite, id_ex_1_ex_s_type, IF_predictJump, IR1, IR2,
       IR3, JAL, JALR, Load_Use, MEM_RegWrite, multiplexer_3_out, multiplexer_5_out, multiplexer_6_out,
       multiplexer_9_out, nand_1_out, newcontrol_1_out_4, newcontrol_1_out_5, newcontrol_1_out_6,
       newcontrol_1_out_7, newcontrol_1_out_8, newcontrol_1_out_9, newcontrol_1_out_10, newcontrol_1_out_11,
       newcontrol_1_out_12, newcontrol_1_out_14, newcontrol_1_out_15, newcontrol_1_out_16,
       newcontrol_1_out_17, not_2_out, not_3_out, not_4_out, not_5_out, not_6_out, not_7_out, not_8_out,
       not_9_out, not_10_out, not_11_out, not_12_out, not_13_out, or_2_out, or_3_out, or_4_out, or_5_out,
       or_6_out, PredictErr, redirect_1_rs_mem, redirect_1_rs_wb, redirect_1_rt_mem, redirect_1_rt_wb,
       register_1_q, register_3_q, register_4_q, Rs_MEM, Rs_WB, RST, Rt_MEM, Rt_WB, URET, W1, W2, W3, WB_CSR,
       WB_JAL, WB_JALR, WB_LH, WB_MemToReg, whichpc_1_out_9;
  wire [1:0] undriven, undriven_2;
  wire [3:0] id_ex_1_ex_aluop, newcontrol_1_out_13;
  wire [4:0] EX_rd, EX_rs1, MEM_rd, rrs1, rrs2, WB_rd;
  wire [11:0] EX_imm12, EX_imms, immb;
  wire [12:0] CNT_num;
  wire [15:0] \LoadUse次数 , \总周期数 , \插入气泡数 , \无条件分支数 , \条件分支成功数 ;
  wire [19:0] immuj;
  wire [31:0] adder_1_out, alu_bin_1_alu_bin, CSR_out, DM_Dout, EX_ALU_Res, EX_CSR_out, EX_IR,
       ex_mem_1_mem_csr_out, EX_Reg_R1, EX_Reg_R2, ID_CSR_out, ID_IR, ID_Reg_R1, IF_IR, MEM_ALU_Res, MEM_IR,
       multiplexer_1_out, multiplexer_2_out, multiplexer_10_out, multiplexer_11_out, multiplexer_12_out,
       pc_in_1_pc_2, pc_in_2_pc_2, PredictAddr, ram_1_data, redirect_Reg_R1, redirect_Reg_R2, regifile_1_r2,
       WB_ALU_Res, WB_IR, \全相联cache改_1_jumpaddr ;

  Button \u_总复位  (.out(RST));
  Button _1 (.out(IR1));
  Button _2 (.out(IR2));
  Button _3 (.out(IR3));
  // Probe on \总周期数 
  // Probe on \总周期数 
  Button \u_继续运行  (.out(Go));
  LED #(.active("true")) led_1 (.in(W1));
  LED #(.active("true")) led_2 (.in(W2));
  LED #(.active("true")) led_3 (.in(W3));
  not not_1 (EX_BranchTaken, whichpc_1_out_9);
  Hex_Digit_Display hex_digit_display_1 (.value(LedData[31:28]));  // open: dp
  // Probe on IF_PC[19:0]
  // RiscV_Probe riscv_probe_1: pin names not known; wires that end beside it: IF_IR
  WhichPC whichpc_1 (
    .out_9(whichpc_1_out_9), .GE(GE), .BLTU(BLTU), .URET(URET), .JALR(JALR), .JAL(JAL), .Beq(Beq), .Bne(Bne),
    .Equal(Equal));
  Multiplexer #(.select(1), .width(32), .disabled("Z"), .enable("false")) multiplexer_1 (
    .in0(EX_PC), .in1(EX_PC), .out(multiplexer_1_out), .sel(whichpc_1_out_9));
  not not_2 (not_2_out, halt);
  Counter #(.width(16), .max('hffff), .ongoal("wrap"), .trigger("rising"), .behavior("new")) counter_1 (
    .count(not_2_out), .Q(\总周期数 ), .clk(CLK), .clr(RST));  // open: load, D, carry, preset, down
  Hex_Digit_Display hex_digit_display_2 (.value(LedData[23:20]));  // open: dp
  Hex_Digit_Display hex_digit_display_3 (.value(LedData[27:24]));  // open: dp
  // Probe on ID_PC[19:0]
  // RiscV_Probe riscv_probe_2: pin names not known; wires that end beside it: ID_IR
  Hex_Digit_Display hex_digit_display_4 (.value(LedData[19:16]));  // open: dp
  Hex_Digit_Display hex_digit_display_5 (.value(LedData[15:12]));  // open: dp
  or or_1 (EX_Branch, Bne, Beq, BLTU, JALR, JAL, URET);
  Hex_Digit_Display hex_digit_display_6 (.value(LedData[7:4]));  // open: dp
  Hex_Digit_Display hex_digit_display_7 (.value(LedData[11:8]));  // open: dp
  // Probe on EX_PC[19:0]
  // RiscV_Probe riscv_probe_3: pin names not known; wires that end beside it: EX_IR
  PC_in pc_in_1 (
    .PC(multiplexer_1_out), .immb(immb), .immuj(immuj), .ALU_Res(EX_ALU_Res), .\中断编号 (undriven), .GE(GE),
    .BLTU(BLTU), .URET(URET), .JALR(JALR), .JAL(JAL), .Beq(Beq), .Bne(Bne), .Equal(Equal), .\中断触发 (1'b0),
    .PC_2(pc_in_1_pc_2));  // open: EPC
  PC_in pc_in_2 (
    .PC(EX_PC), .immb(immb), .immuj(immuj), .ALU_Res(EX_ALU_Res), .\中断编号 (undriven_2), .GE(1'b0),
    .BLTU(BLTU), .URET(URET), .JALR(JALR), .JAL(JAL), .Beq(Beq), .Bne(Bne), .Equal(Beq), .\中断触发 (1'b0),
    .PC_2(pc_in_2_pc_2));  // open: EPC
  Counter #(.width(16), .max('hffff), .ongoal("wrap"), .trigger("rising"), .behavior("new")) counter_2 (
    .count(Load_Use), .Q(\LoadUse次数 ), .clk(CLK), .clr(RST));  // open: load, D, carry, preset, down
  Hex_Digit_Display hex_digit_display_8 (.value(LedData[3:0]));  // open: dp
  // Probe on \总周期数 
  // Probe on M_PC[19:0]
  // RiscV_Probe riscv_probe_4: pin names not known; wires that end beside it: MEM_IR
  and and_1 (Flush, EX_Branch, PredictErr);
  Multiplexer #(.select(1), .width(32), .disabled("Z"), .enable("false")) multiplexer_2 (
    .in0(PredictAddr), .in1(pc_in_1_pc_2), .out(multiplexer_2_out), .sel(PredictErr));
  not not_3 (not_3_out, multiplexer_3_out);
  Multiplexer #(.select(1), .width(1), .disabled("Z"), .enable("false")) multiplexer_3 (
    .in0(and_2_out), .in1(and_3_out), .out(multiplexer_3_out), .sel(halt));
  and and_2 (and_2_out, not_4_out, Load_Use);
  not not_4 (not_4_out, Flush);
  and and_3 (and_3_out, not_5_out, halt);
  not not_5 (not_5_out, Go);
  \全相联Cache改  \u_全相联cache改_1  (
    .CLK(CLK), .in_2(IF_PC), .Branch(EX_Branch), .EX_PC(EX_PC), .EX_DPC(pc_in_2_pc_2),
    .EX_BranchTaken(EX_BranchTaken), .PredictJump(IF_predictJump), .JumpAddr(\全相联cache改_1_jumpaddr ));
  // Probe on \总周期数 
  // Probe on \无条件分支数 
  // Probe on \条件分支成功数 
  // Probe on \插入气泡数 
  // Probe on \LoadUse次数 
  Register #(.width(32), .trigger("rising"), .Select("low")) PC (
    .D(multiplexer_2_out), .en(not_3_out), .Q(IF_PC), .clk(CLK), .clr(RST));
  or or_2 (or_2_out, JALR, JAL);
  // Probe on IF_PC[11:0]
  // Probe on WB_PC[19:0]
  // RiscV_Probe riscv_probe_5: pin names not known; wires that end beside it: WB_IR
  Adder #(.width(32)) adder_1 (.a(IF_PC), .b(32'h4), .out(adder_1_out));  // open: cin, cout
  Multiplexer #(.select(1), .width(32), .disabled("Z"), .enable("false")) multiplexer_4 (
    .in0(adder_1_out), .in1(\全相联cache改_1_jumpaddr ), .out(PredictAddr), .sel(IF_predictJump));
  Counter #(.width(16), .max('hffff), .ongoal("wrap"), .trigger("rising"), .behavior("new")) counter_3 (
    .count(or_2_out), .Q(\无条件分支数 ), .clk(CLK), .clr(RST));  // open: load, D, carry, preset, down
  // Probe on EX_PC[11:0]
  // Probe on ID_PC[11:0]
  Multiplexer #(.select(1), .width(1), .disabled("Z"), .enable("false")) multiplexer_5 (
    .in0(IF_predictJump), .in1(1'b0), .out(multiplexer_5_out), .sel(Flush));
  // Probe on M_PC[11:0]
  D_Flip_Flop #(.trigger("high"), .Pre_Clr_Positions("LEGACY"), .NegatePresetClear("false"), .enable("true"), .NewFFLayout("false")) d_ff_1 (.Q(d_ff_1_q));  // open: clk, D, Qn, preset, en, reset
  // Probe on 13'h9e
  IF_ID if_id_1 (
    .IF_PC(IF_PC), .IF_IR(IF_IR), .ID_PC(ID_PC), .ID_IR(ID_IR), .CLK(CLK), .halt(multiplexer_6_out),
    .Flush(Flush));
  ROM #(.addrWidth(10), .dataWidth(32), .Select("high")) rom_1 (.addr(IF_PC[11:2]), .data(IF_IR));
  Register #(.width(1), .trigger("rising"), .Select("low")) register_1 (
    .D(multiplexer_5_out), .en(not_6_out), .Q(register_1_q), .clk(CLK));  // open: clr
  not not_6 (not_6_out, Load_Use);
  // Probe on WB_PC[11:0]
  Comparator #(.width(13), .mode("twosComplement")) comparator_1 (
    .a(CNT_num), .b(13'h9e), .eq(comparator_1_eq), .lt(comparator_1_lt));  // open: gt
  Clock #(.highDuration(1), .lowDuration(1)) clock_1 (.out(clock_1_out));
  Multiplexer #(.select(1), .width(1), .disabled("Z"), .enable("false")) multiplexer_6 (
    .in0(Load_Use), .in1(and_4_out), .out(multiplexer_6_out), .sel(halt));
  and and_4 (and_4_out, not_7_out, halt);
  not not_7 (not_7_out, Go);
  Multiplexer #(.select(1), .width(5), .disabled("Z"), .enable("false")) multiplexer_7 (
    .in0(ID_IR[19:15]), .in1(5'b10001), .out(rrs1), .sel(ID_ecall));
  Multiplexer #(.select(1), .width(5), .disabled("Z"), .enable("false")) multiplexer_8 (
    .in0(ID_IR[24:20]), .in1(5'b01010), .out(rrs2), .sel(ID_ecall));
  or or_3 (or_3_out, JALR, JAL);
  not not_8 (not_8_out, or_3_out);
  nand nand_1 (nand_1_out, d_ff_1_q, comparator_1_eq);
  Counter #(.width(13), .max('h1fff), .ongoal("stay"), .trigger("rising"), .behavior("old")) counter_4 (
    .count(comparator_1_lt), .Q(CNT_num), .clk(clock_1_out));  // open: load, D, carry, clr, preset
  // RiscV_Probe riscv_probe_6: pin names not known; wires that end beside it: ID_IR
  Reg_Din reg_din_1 (
    .DM_Dout(DM_Dout), .PC(WB_PC), .CSR_out(CSR_out), .ALU_Res(WB_ALU_Res), .LH(WB_LH),
    .MemToReg(WB_MemToReg), .CSR(WB_CSR), .JAL(WB_JAL), .JALR(WB_JALR), .RDin(RDin));
  and and_5 (and_5_out, EX_BranchTaken, not_8_out);
  Counter #(.width(16), .max('hffff), .ongoal("wrap"), .trigger("rising"), .behavior("new")) counter_5 (
    .count(and_5_out), .Q(\条件分支成功数 ), .clk(CLK), .clr(RST));  // open: load, D, carry, preset, down
  assign CLK = nand_1_out ? clock_1_out : 1'bz;  // Controlled_Buffer controlled_buffer_1
  Register #(.width(32), .trigger("rising"), .Select("low")) register_2 (
    .D(WB_ALU_Res), .en(WB_CSR), .Q(ID_CSR_out), .clk(CLK), .clr(RST));
  Regifile regifile_1 (
    .Din(RDin), .Clk(CLK), .R1(ID_Reg_R1), .R2(regifile_1_r2), .WE(RegWrite), .W_num(WB_rd), .R1_num(rrs1),
    .R2_num(rrs2));
  Pull_Resistor #(.pull(1)) pull_resistor_1 (.node(CLK));
  newcontrol newcontrol_1 (
    .out_4(newcontrol_1_out_4), .out_6(newcontrol_1_out_6), .out_8(newcontrol_1_out_8),
    .out_10(newcontrol_1_out_10), .out_12(newcontrol_1_out_12), .out_14(newcontrol_1_out_14),
    .in_1(ID_IR[21]), .in_2(ID_IR[6:2]), .in_3({ID_IR[30], ID_IR[25], ID_IR[14:12]}),
    .out_5(newcontrol_1_out_5), .out_7(newcontrol_1_out_7), .out_9(newcontrol_1_out_9),
    .out_11(newcontrol_1_out_11), .out_13(newcontrol_1_out_13), .out_15(newcontrol_1_out_15),
    .out_16(newcontrol_1_out_16), .out_17(newcontrol_1_out_17), .out_18(ID_ecall));
  or or_4 (or_4_out, Flush, Load_Use);
  Counter #(.width(16), .max('hffff), .ongoal("wrap"), .trigger("rising"), .behavior("new")) counter_6 (
    .count(or_4_out), .Q(\插入气泡数 ), .clk(CLK), .clr(RST));  // open: load, D, carry, preset, down
  redirect redirect_1 (
    .ERegwrite(EX_RegWrite), .IDrs1(rrs1), .Erd(EX_rd), .IDrs2(rrs2), .Mrd(MEM_rd), .MRegWrite(MEM_RegWrite),
    .OPcode(ID_IR[6:2]), .Rt_MEM(redirect_1_rt_mem), .Rs_MEM(redirect_1_rs_mem), .Rs_WB(redirect_1_rs_wb),
    .Rt_WB(redirect_1_rt_wb), .ID_ecall(ID_ecall));
  Load_Use load_use_1 (
    .ERegwrite(EX_RegWrite), .IDrs1(rrs1), .Erd(EX_rd), .IDrs2(rrs2), .OPcode1(ID_IR[6:2]),
    .LoadUse(Load_Use), .EX_MemToReg(EX_MemToReg));
  or or_5 (or_5_out, Load_Use, Flush);
  Multiplexer #(.select(1), .width(1), .disabled("Z"), .enable("false")) multiplexer_9 (
    .in0(register_1_q), .in1(1'b0), .out(multiplexer_9_out), .sel(or_6_out));
  or or_6 (or_6_out, Load_Use, Flush);
  ID_EX id_ex_1 (
    .ID_PC(ID_PC), .ID_IR(ID_IR), .ID_rs1(ID_IR[19:15]), .ID_rd(ID_IR[11:7]), .ID_imm12(ID_IR[31:20]),
    .ID_imms({ID_IR[31:25], ID_IR[11:7]}), .ID_immb({ID_IR[31], ID_IR[7], ID_IR[30:25], ID_IR[11:8]}),
    .ID_immuj({ID_IR[31], ID_IR[19:12], ID_IR[20], ID_IR[30:21]}), .ID_Beq(newcontrol_1_out_5),
    .ID_Bne(newcontrol_1_out_7), .ID_MemToReg(newcontrol_1_out_9), .ID_MemWrite(newcontrol_1_out_11),
    .ID_ALUOP(newcontrol_1_out_13), .ID_ALUSrcB(newcontrol_1_out_15), .ID_RegWrite(newcontrol_1_out_16),
    .ID_S_type(newcontrol_1_out_17), .ID_JAL(newcontrol_1_out_4), .ID_JALR(newcontrol_1_out_6),
    .ID_URET(newcontrol_1_out_8), .ID_BLTU(newcontrol_1_out_10), .ID_CSR(newcontrol_1_out_12),
    .ID_LH(newcontrol_1_out_14), .ID_ecall(ID_ecall), .ID_Reg_R2(regifile_1_r2), .ID_CSR_out(ID_CSR_out),
    .EX_PC(EX_PC), .EX_IR(EX_IR), .EX_rs1(EX_rs1), .EX_rd(EX_rd), .EX_imm12(EX_imm12), .EX_imms(EX_imms),
    .EX_immb(immb), .EX_immuj(immuj), .EX_Beq(Beq), .EX_Bne(Bne), .EX_MemToReg(EX_MemToReg),
    .EX_MemWrite(id_ex_1_ex_memwrite), .EX_ALUOP(id_ex_1_ex_aluop), .EX_ALUSrcB(id_ex_1_ex_alusrcb),
    .EX_RegWrite(EX_RegWrite), .EX_S_type(id_ex_1_ex_s_type), .EX_JAL(JAL), .EX_JALR(JALR), .EX_URET(URET),
    .EX_BLTU(BLTU), .EX_CSR(EX_CSR), .EX_LH(id_ex_1_ex_lh), .EX_ecall(EX_ecall), .EX_Reg_R2(EX_Reg_R2),
    .EX_CSR_out(EX_CSR_out), .CLK(CLK), .ID_Reg_R1(ID_Reg_R1), .EX_Reg_R1(EX_Reg_R1), .halt(and_6_out),
    .Flush(or_5_out), .Rt_MEM_2(Rt_MEM), .Rs_MEM_2(Rs_MEM), .Rs_WB_2(Rs_WB), .Rt_WB_2(Rt_WB),
    .Rt_MEM(redirect_1_rt_mem), .Rs_MEM(redirect_1_rs_mem), .Rs_WB(redirect_1_rs_wb), .Rt_WB(redirect_1_rt_wb));
  and and_6 (and_6_out, not_9_out, halt);
  not not_9 (not_9_out, Go);
  Register #(.width(1), .trigger("rising"), .Select("low")) register_3 (
    .D(multiplexer_9_out), .Q(register_3_q), .clk(CLK));  // open: en, clr
  xor xor_1 (PredictErr, EX_BranchTaken, register_3_q);
  Multiplexer #(.select(1), .width(32), .disabled("Z"), .enable("false")) multiplexer_10 (
    .in0(EX_Reg_R1), .in1(RDin), .out(multiplexer_10_out), .sel(Rs_WB));
  Multiplexer #(.select(1), .width(32), .disabled("Z"), .enable("false")) multiplexer_11 (
    .in0(EX_Reg_R2), .in1(RDin), .out(multiplexer_11_out), .sel(Rt_WB));
  Multiplexer #(.select(1), .width(32), .disabled("Z"), .enable("false")) multiplexer_12 (
    .in0(redirect_Reg_R1), .in1(EX_CSR_out), .out(multiplexer_12_out), .sel(EX_CSR));
  ALU_Bin alu_bin_1 (
    .Reg_R2(redirect_Reg_R2), .immb(EX_imm12), .rs1(EX_rs1), .imms(EX_imms), .CSR(EX_CSR),
    .S_type(id_ex_1_ex_s_type), .AluSrcB(id_ex_1_ex_alusrcb), .ALU_Bin(alu_bin_1_alu_bin));
  ALU alu_1 (
    .X(multiplexer_12_out), .Y(alu_bin_1_alu_bin), .AluOP(id_ex_1_ex_aluop), .Equal(Equal),
    .Result(EX_ALU_Res), .out_4(GE));  // open: Result_2, out_6
  Comparator #(.width(32), .mode("twosComplement")) comparator_2 (
    .a(32'h22), .b(redirect_Reg_R1), .eq(comparator_2_eq));  // open: gt, lt
  Multiplexer #(.select(1), .width(32), .disabled("Z"), .enable("false")) multiplexer_13 (
    .in0(multiplexer_10_out), .in1(MEM_ALU_Res), .out(redirect_Reg_R1), .sel(Rs_MEM));
  Multiplexer #(.select(1), .width(32), .disabled("Z"), .enable("false")) multiplexer_14 (
    .in0(multiplexer_11_out), .in1(MEM_ALU_Res), .out(redirect_Reg_R2), .sel(Rt_MEM));
  not not_10 (not_10_out, comparator_2_eq);
  Register #(.width(1), .trigger("rising"), .Select("low")) register_4 (
    .D(not_10_out), .en(EX_ecall), .Q(register_4_q), .clk(CLK), .clr(Go));
  Register #(.width(32), .trigger("rising"), .Select("low")) register_5 (
    .D(redirect_Reg_R2), .en(comparator_2_eq), .Q(LedData), .clk(CLK), .clr(RST));
  EX_MEM ex_mem_1 (
    .EX_PC(EX_PC), .EX_IR(EX_IR), .EX_rd(EX_rd), .ID_MemToReg(EX_MemToReg),
    .ID_MemWrite(id_ex_1_ex_memwrite), .ID_RegWrite(EX_RegWrite), .ID_CSR(EX_CSR), .ID_LH(id_ex_1_ex_lh),
    .EX_Reg_R2(redirect_Reg_R2), .EX_ALU_Res(EX_ALU_Res), .MEM_PC(M_PC), .MEM_IR(MEM_IR), .MEM_rd(MEM_rd),
    .EX_MemToReg(ex_mem_1_ex_memtoreg), .EX_MemWrite(MemWrite), .EX_RegWrite(MEM_RegWrite),
    .EX_CSR(ex_mem_1_ex_csr), .EX_LH(ex_mem_1_ex_lh), .MEM_Reg_R2(MDin), .MEM_ALU_Res(MEM_ALU_Res),
    .CLK(CLK), .halt(and_7_out), .ID_JALR(JALR), .EX_JALR(ex_mem_1_ex_jalr), .ID_JAL(JAL),
    .EX_JAL(ex_mem_1_ex_jal), .EX_CSR_out(EX_CSR_out), .MEM_CSR_out(ex_mem_1_mem_csr_out),
    .EX_halt(register_4_q), .MEM_halt(ex_mem_1_mem_halt));  // open: Flush
  and and_7 (and_7_out, not_11_out, halt);
  not not_11 (not_11_out, Go);
  not not_12 (not_12_out, MemWrite);
  RAM #(.addrWidth(10), .dataWidth(32), .bus("separate"), .Select("high")) ram_1 (
    .addr(MEM_ALU_Res[11:2]), .din(MDin), .data(ram_1_data), .str(MemWrite), .clk(CLK), .ld(not_12_out),
    .clr(RST));  // open: sel
  MEM_WB mem_wb_1 (
    .MEM_PC(M_PC), .MEM_IR(MEM_IR), .MEM_rd(MEM_rd), .ID_MemToReg(ex_mem_1_ex_memtoreg),
    .ID_RegWrite(MEM_RegWrite), .ID_JAL(ex_mem_1_ex_jal), .ID_JALR(ex_mem_1_ex_jalr),
    .ID_CSR(ex_mem_1_ex_csr), .ID_LH(ex_mem_1_ex_lh), .MEM_ALU_Res(MEM_ALU_Res), .WB_PC(WB_PC),
    .WB_IR(WB_IR), .WB_rd(WB_rd), .EX_MemToReg(WB_MemToReg), .EX_RegWrite(RegWrite), .EX_JAL(WB_JAL),
    .EX_JALR(WB_JALR), .EX_CSR(WB_CSR), .EX_LH(WB_LH), .WB_ALU_Res(WB_ALU_Res), .in_15(and_8_out),
    .in_16(CLK), .MEM_DM_Dput(ram_1_data), .WB_DM_Dout(DM_Dout), .MEM_CSR_out(ex_mem_1_mem_csr_out),
    .WB_CSR_out(CSR_out), .MEM_halt(ex_mem_1_mem_halt), .WB_halt(halt));  // open: Flush
  and and_8 (and_8_out, not_13_out, halt);
  not not_13 (not_13_out, Go);

  // Other names for the same wires on the sheet: rd[4:0] = ID_IR[11:7]; ID_rs2[4:0] = ID_IR[24:20];
  //   ID_rs1[4:0] = ID_IR[19:15]; ID_OPcode[4:0] = ID_IR[6:2]; MEM_PC[31:0] = M_PC

  // Notes on the sheet:
  //   中断源
  //   时空图监测，可删除
  //   中断等待指示
  //   数码管输出
  //   指令存储器
  //   控制位
  //   流水调试日志用
  //   暂停节拍，不能为0
  //   指令字
  //   contents of rom_1 (hex, n*v repeats v):
  //   100493 100006f 100493 200913 300993 100006f 100493 200913 300993 100006f 100493 200913 300993
  //   100006f 100493 200913 300993 3d8000ef 100413 100493 1f49493 900533 2200893 73 24d493 48463 fedff06f
  //   900533 2200893 73 100493 249493 900533 2200893 73 48463 fedff06f 100493 1f49493 900533 2200893 73
  //   4034d493 900533 2200893 73 4044d493 900533 2200893 73 4044d493 900533 2200893 73 4044d493 900533
  //   2200893 73 4044d493 900533 2200893 73 4044d493 900533 2200893 73 4044d493 900533 2200893 73 4044d493
  //   900533 2200893 73 100413 1f41993 41f9d993 433 c00913 300b13 140413 f47413 800293 100313 499993
  //   89e9b3 1300533 2200893 73 406282b3 fe0294e3 140413 f00f93 1f47433 1c41413 800293 100313 49d993
  //   89e9b3 1300533 2200893 73 406282b3 fe0294e3 1c45413 406b0b33 b0463 f95ff06f 2b3 fff2c293 829293
  //   ff2e293 500533 2200893 73 fff00413 493 84a023 140413 448493 84a023 140413 448493 84a023 140413
  //   448493 84a023 140413 448493 84a023 140413 448493 84a023 140413 448493 84a023 140413 448493 84a023
  //   140413 448493 84a023 140413 448493 84a023 140413 448493 84a023 140413 448493 84a023 140413 448493
  //   84a023 140413 448493 84a023 140413 448493 84a023 140413 448493 84a023 140413 448493 140413 433
  //   3c00493 42983 4aa03 149a2b3 28663 134a023 1442023 ffc48493 fe9412e3 800533 2200893 73 440413 3c00493
  //   fc9416e3 3200893 73 100293 300313 800493 849493 7648493 900533 2200893 73 800e13 5494b3 6494b3
  //   900533 2200893 73 fffe0e13 fe0e14e3 a00893 73 fff00293 7700493 849493 7748493 900533 2200893 73
  //   1000e13 54c4b3 900533 2200893 73 fffe0e13 fe0e16e3 a00893 73 313 1000e13 8400493 849493 8348493
  //   400913 891913 490913 849493 8248493 849493 8148493 891913 490913 891913 490913 932023 12484b3 430313
  //   fffe0e13 fe0e18e3 2000e13 313 31483 900533 2200893 73 230313 fffe0e13 fe0e14e3 a00893 73 ff100493
  //   900533 2200893 73 148493 fe9068e3 900533 2200893 73 a00893 73 a00893 73 413 140413 800533 2200893 73
  //   240413 800533 2200893 73 340413 800533 2200893 73 440413 800533 2200893 73 540413 800533 2200893 73
  //   640413 800533 2200893 73 740413 800533 2200893 73 840413 800533 2200893 2200893 73 8067
  //   戳工具置1进入计数暂停模式，ctrl+k时钟自动运行到对应节拍暂停
  //   ctrl+k关闭时钟连续运行，将控制位置零，进入单步调试模式调试
  //   指令探针
  //   可计数暂停的时钟源
  //   为方便自动评测，需要输出流水线各段保存的PC值，注意是PC不是PC+4，另外ID段寄存器写入信息，Mem段内存写入信息也要输出
  //   数据存储器
endmodule
